// Logisim project DE0_BASE.circ as structural Verilog: 1 circuit, main circuit main
module main (
  input  [9:0] SW,
  input  [3:0] BUTTON
);

  wire CLK;
  wire [6:0] HEX0, HEX1, HEX2, HEX3;
  wire [9:0] LED;

  Clock u_CLK (.out(CLK));
  LED LED0 (.in(LED[0]));
  LED LED1 (.in(LED[1]));
  LED LED2 (.in(LED[2]));
  LED LED3 (.in(LED[3]));
  LED LED4 (.in(LED[4]));
  LED LED5 (.in(LED[5]));
  LED LED6 (.in(LED[6]));
  LED LED7 (.in(LED[7]));
  LED LED8 (.in(LED[8]));
  LED LED9 (.in(LED[9]));
  _7_Segment_Display u_HEX0 (
    .g(HEX0[3]), .f(HEX0[2]), .a(HEX0[1]), .b(HEX0[0]), .e(HEX0[4]), .d(HEX0[5]), .c(HEX0[6]), .dp(1'b0));
  _7_Segment_Display u_HEX1 (
    .g(HEX1[3]), .f(HEX1[2]), .a(HEX1[1]), .b(HEX1[0]), .e(HEX1[4]), .d(HEX1[5]), .c(HEX1[6]), .dp(1'b0));
  _7_Segment_Display u_HEX2 (
    .g(HEX2[3]), .f(HEX2[2]), .a(HEX2[1]), .b(HEX2[0]), .e(HEX2[4]), .d(HEX2[5]), .c(HEX2[6]), .dp(1'b0));
  _7_Segment_Display u_HEX3 (
    .g(HEX3[3]), .f(HEX3[2]), .a(HEX3[1]), .b(HEX3[0]), .e(HEX3[4]), .d(HEX3[5]), .c(HEX3[6]), .dp(1'b0));
endmodule
