// Logisim project DE0_BASE_FSM.circ as structural Verilog: 1 circuit, main circuit main
module main (
  input  [9:0] SW,
  input  [3:0] BUTTON
);

  wire CLK, priority_encoder_1_gs, TWEQ_p6, TWEQ_p7, TWEQ_p8, TWEQ_p9;
  wire [1:0] priority_encoder_1_out;
  wire [3:0] dfgdfg_p5, TWEQ_p1;
  wire [6:0] HEX0, HEX1, HEX2, HEX3;

  Clock u_CLK (.out(CLK));
  // KeyPad TWEQ: pin names not known; wires that end beside it: TWEQ_p1, TWEQ_p1[3], TWEQ_p1[2], TWEQ_p1[1], TWEQ_p1[0], TWEQ_p6, TWEQ_p7, TWEQ_p8, TWEQ_p9
  // FSM_Entity #(.content("fsm example @[ 50 , 50 , 800 , 500 ] { in A [ 3 ] @[ 50 , 100 , 43 , 15 ] ; out\nX [ 4 ] @[ 808 , 140 , 42 , 15 ] ; codeWidth = 2 ; reset = S0 ; state S0 = \"01\"\n@[ 297 , 181 , 30 , 30 ] { commands @[ 246 , 173 , 50 , 40 ] { X = \"0001\" ; }\ntransitions { S0 -> S1 when default @[ 432 , 151 , 50 , 22 ] ; S0 -> S3 when A\n== \"000\" @[ 346 , 269 , 69 , 22 ] ; } } state S1 = \"10\" @[ 470 , 186 , 30 , 30\n] { commands @[ 522 , 190 , 40 , 40 ] { X = \"0010\" ; } transitions { S1 -> S2\nwhen default @[ 533 , 276 , 50 , 22 ] ; S1 -> S0 when A == \"000\" @[ 399 , 230 ,\n69 , 22 ] ; } } state S2 = \"00\" @[ 471 , 339 , 30 , 30 ] { commands @[ 524 ,\n353 , 60 , 40 ] { X = { \"00\" , A [ 1 ] , \"1\" } ; } transitions { S2 -> S3 when\ndefault @[ 392 , 398 , 50 , 22 ] ; S2 -> S1 when A [ 2 : 1 ] == \"11\" @[ 557 ,\n250 , 89 , 22 ] ; } } state S3 = \"11\" @[ 287 , 325 , 30 , 30 ] { commands @[\n244 , 341 , 60 , 40 ] { X = \"1000\" ; } transitions { S3 -> S0 when default @[\n248 , 278 , 50 , 22 ] ; S3 -> S2 when A == \"000\" @[ 388 , 313 , 69 , 22 ] ; } }\n}")) dfgdfg: pin names not known; wires that end beside it: CLK, BUTTON[0], SW[0], BUTTON[3:1], dfgdfg_p5
  Priority_Encoder #(.select(2)) priority_encoder_1 (
    .in0(TWEQ_p6), .in1(TWEQ_p7), .in2(TWEQ_p8), .in3(TWEQ_p9), .out(priority_encoder_1_out),
    .gs(priority_encoder_1_gs), .en_in(1'b1));  // open: en_out
  // FSM_Entity #(.content("fsm example @[ 50 , 50 , 800 , 500 ] { in L [ 4 ] @[ 50 , 126 , 41 , 15 ] ; in\nRead [ 1 ] @[ 50 , 171 , 36 , 15 ] ; out C [ 4 ] @[ 807 , 140 , 43 , 15 ] ; out\nHit [ 1 ] @[ 825 , 241 , 25 , 15 ] ; codeWidth = 4 ; reset = S0 ; state S0 =\n\"0001\" @[ 497 , 173 , 30 , 30 ] { commands @[ 542 , 188 , 50 , 40 ] { C =\n\"0000\" ; } } state S1 = \"1000\" @[ 267 , 166 , 30 , 30 ] { commands @[ 312 , 181\n, 40 , 40 ] { C = L ; } } state S2 = \"0010\" @[ 491 , 305 , 30 , 30 ] { commands\n@[ 536 , 320 , 60 , 40 ] { } } state S3 = \"0100\" @[ 266 , 305 , 30 , 30 ] {\ncommands @[ 311 , 320 , 60 , 40 ] { } } }")) fsm_entity_1: pin names not known; wires that end beside it: CLK, BUTTON[0], SW[0], priority_encoder_1_out, priority_encoder_1_gs
  LED LED0 (.in(dfgdfg_p5[0]));
  LED LED1 (.in(dfgdfg_p5[1]));
  LED LED2 (.in(dfgdfg_p5[2]));
  LED LED3 (.in(dfgdfg_p5[3]));
  LED LED4 (.in(1'b1));
  LED LED5 (.in(1'b1));
  LED LED6 (.in(1'b1));
  LED LED7 (.in(1'b1));
  LED LED8 (.in(1'b1));
  LED LED9 (.in(1'b1));
  _7_Segment_Display u_HEX0 (
    .g(HEX0[3]), .f(HEX0[2]), .a(HEX0[1]), .b(HEX0[0]), .e(HEX0[4]), .d(HEX0[5]), .c(HEX0[6]), .dp(1'b0));
  _7_Segment_Display u_HEX1 (
    .g(HEX1[3]), .f(HEX1[2]), .a(HEX1[1]), .b(HEX1[0]), .e(HEX1[4]), .d(HEX1[5]), .c(HEX1[6]), .dp(1'b0));
  _7_Segment_Display u_HEX2 (
    .g(HEX2[3]), .f(HEX2[2]), .a(HEX2[1]), .b(HEX2[0]), .e(HEX2[4]), .d(HEX2[5]), .c(HEX2[6]), .dp(1'b0));
  _7_Segment_Display u_HEX3 (
    .g(HEX3[3]), .f(HEX3[2]), .a(HEX3[1]), .b(HEX3[0]), .e(HEX3[4]), .d(HEX3[5]), .c(HEX3[6]), .dp(1'b0));

  // Other names for the same wires on the sheet: CLR = BUTTON[0]; A[2:0] = BUTTON[3:1]; EN = SW[0]
endmodule
