// Logisim project DE0_CV_KEYPAD.circ as structural Verilog: 3 circuits, main circuit main
module main (
);

  wire not_1_out, not_2_out, not_3_out, not_4_out, SW_sw1, SW_sw2, SW_sw3, SW_sw4, TWEQ_p5, TWEQ_p6, TWEQ_p7,
       TWEQ_p8;

  DipSwitch #(.number(4)) SW (.sw1(SW_sw1), .sw2(SW_sw2), .sw3(SW_sw3), .sw4(SW_sw4));
  not not_1 (not_1_out, SW_sw1);
  not not_2 (not_2_out, SW_sw2);
  not not_3 (not_3_out, SW_sw3);
  not not_4 (not_4_out, SW_sw4);
  // KeyPad TWEQ: pin names not known; wires that end beside it: not_4_out, not_3_out, not_2_out, not_1_out, TWEQ_p5, TWEQ_p6, TWEQ_p7, TWEQ_p8
  LED L0 (.in(TWEQ_p5));
  LED L1 (.in(TWEQ_p6));
  LED L2 (.in(TWEQ_p7));
  LED L3 (.in(TWEQ_p8));
  LED C3 (.in(not_1_out));
  LED C2 (.in(not_2_out));
  LED C1 (.in(not_3_out));
  LED C0 (.in(not_4_out));
endmodule

module DECODE (
  input  L1,
  input  L2,
  input  L3,
  input  L4,
  output Hit,
  output [1:0] RowId
);

  wire not_1_out, not_2_out, not_3_out, not_4_out;

  not not_1 (not_1_out, L1);
  not not_2 (not_2_out, L2);
  not not_3 (not_3_out, L3);
  not not_4 (not_4_out, L4);
  or or_1 (Hit, L4, L3, L2, L1);
  or or_2 (RowId[1], L4, L3);
  or or_3 (RowId[0], L4, L2);
endmodule

module sdfg (
  input  in_1,
  output out_2
);

  buf buffer_1 (out_2, in_1);
endmodule
