// Logisim project DE0_CV_REGFILE.circ as structural Verilog: 1 circuit, main circuit main
module main (
  input  RST,
  input  WE,
  input  [4:0] WA,
  input  [4:0] DI
);

  wire regfile_p4;
  wire [31:0] bcd_to_7_segment_decoder_2_p2, bcd_to_7_segment_decoder_3_p2, bit_extender_1_out;

  assign bit_extender_1_out = {{27{DI[4]}}, DI};  // Bit_Extender bit_extender_1
  _7_Segment_Display WA_RA ();  // open: g, f, a, b, e, d, c, dp
  // BCD_to_7_Segment_decoder bcd_to_7_segment_decoder_1: pin names not known
  // Register_File regfile: pin names not known; wires that end beside it: WA[3:0], WA, bit_extender_1_out, regfile_p4, RST
  Clock clock_1 (.out(regfile_p4));
  LED LED_1 (.in(WE));
  _7_Segment_Display DO_MSB ();  // open: g, f, a, b, e, d, c, dp
  // BCD_to_7_Segment_decoder bcd_to_7_segment_decoder_2: pin names not known; wires that end beside it: WE, bcd_to_7_segment_decoder_2_p2, bcd_to_7_segment_decoder_2_p2[7:4]
  // BCD_to_7_Segment_decoder bcd_to_7_segment_decoder_3: pin names not known; wires that end beside it: WA, bcd_to_7_segment_decoder_3_p2, bit_extender_1_out[7:4]
  _7_Segment_Display DI_MSB ();  // open: g, f, a, b, e, d, c, dp
  _7_Segment_Display DO_LSB ();  // open: g, f, a, b, e, d, c, dp
  // BCD_to_7_Segment_decoder bcd_to_7_segment_decoder_4: pin names not known; wires that end beside it: bcd_to_7_segment_decoder_2_p2[3:0]
  Comparator #(.width(32)) comparator_1 (
    .a(bcd_to_7_segment_decoder_2_p2), .b(bcd_to_7_segment_decoder_3_p2));  // open: gt, eq, lt
  // BCD_to_7_Segment_decoder bcd_to_7_segment_decoder_5: pin names not known; wires that end beside it: bit_extender_1_out[3:0]
  _7_Segment_Display DI_LSB ();  // open: g, f, a, b, e, d, c, dp
endmodule
