// Logisim project Montre1.circ as structural Verilog: 7 circuits, main circuit Horloge
module Horloge (
  input  load,
  input  [4:0] in_2,
  input  [5:0] in_3,
  input  [5:0] in_4,
  input  [4:0] in_5,
  input  [3:0] in_6,
  input  [11:0] in_7,
  input  RAZ,
  output [4:0] out_9,
  output [5:0] out_10,
  output [5:0] out_11,
  output [4:0] out_12,
  output [3:0] out_13,
  output [11:0] out_14
);

  wire annee_1_bisex, clk_out, heure_1_clk_heure, jour_1_clk_jour, minute_1_clk_min, mois_1_clk_mois,
       seconde_1_clk_sec;

  Clock clk (.out(clk_out));
  Seconde seconde_1 (
    .clk(clk_out), .RAZ(RAZ), .load(load), .Input_sec(in_4), .clk_sec(seconde_1_clk_sec), .secondes(out_11));
  Minute minute_1 (
    .clk(seconde_1_clk_sec), .RAZ(RAZ), .load(load), .Input_heure(in_3), .clk_min(minute_1_clk_min),
    .minutes(out_10));
  Heure heure_1 (
    .clk(minute_1_clk_min), .RAZ(RAZ), .load(load), .Input_heure(in_2), .clk_heure(heure_1_clk_heure),
    .heures(out_9));
  Jour jour_1 (
    .clk(heure_1_clk_heure), .RAZ(RAZ), .load(load), .Input_jour(in_5), .mois(out_13), .bisex(annee_1_bisex),
    .clk_jour(jour_1_clk_jour), .jours(out_12));
  Mois mois_1 (
    .clk(jour_1_clk_jour), .RAZ(RAZ), .load(load), .Input_mois(in_6), .clk_mois(mois_1_clk_mois),
    .mois(out_13));
  Annee annee_1 (
    .clk(mois_1_clk_mois), .RAZ(RAZ), .load(load), .Input_Annee(in_7), .bisex(annee_1_bisex), .Annee(out_14));

  // Other names for the same wires on the sheet: a[11:0] = out_14; h[4:0] = out_9; i_a[11:0] = in_7; i_h[4:0] = in_2;
  //   i_j[4:0] = in_5; i_m[3:0] = in_6; i_min[5:0] = in_3; i_s[5:0] = in_4; j[4:0] = out_12; m[3:0] = out_13;
  //   min[5:0] = out_10; s[5:0] = out_11
endmodule

module Seconde (
  input  clk,
  input  RAZ,
  input  load,
  input  [5:0] Input_sec,
  output clk_sec,
  output [5:0] secondes
);

  wire comparator_1_gt, or_1_out, or_2_out;

  or or_1 (or_1_out, RAZ, or_2_out);
  Counter #(.width(6), .max('h3f)) counter_1 (
    .clr(or_1_out), .load(load), .up(1'b1), .count(1'b1), .clk(clk), .D(Input_sec), .Q(secondes));  // open: carry
  or or_2 (or_2_out, comparator_1_gt, clk_sec);
  Comparator #(.width(6), .mode("unsigned")) comparator_1 (
    .a(secondes), .b(6'b111100), .gt(comparator_1_gt), .eq(clk_sec));  // open: lt
endmodule

module Minute (
  input  clk,
  input  RAZ,
  input  load,
  input  [5:0] Input_heure,
  output clk_min,
  output [5:0] minutes
);

  wire comparator_1_gt, or_1_out, or_2_out;

  or or_1 (or_1_out, RAZ, or_2_out);
  Counter #(.width(6), .max('h3f)) counter_1 (
    .clr(or_1_out), .load(load), .up(1'b1), .count(1'b1), .clk(clk), .D(Input_heure), .Q(minutes));  // open: carry
  or or_2 (or_2_out, comparator_1_gt, clk_min);
  Comparator #(.width(6), .mode("unsigned")) comparator_1 (
    .a(minutes), .b(6'b111100), .gt(comparator_1_gt), .eq(clk_min));  // open: lt
endmodule

module Heure (
  input  clk,
  input  RAZ,
  input  load,
  input  [4:0] Input_heure,
  output clk_heure,
  output [4:0] heures
);

  wire comparator_1_gt, or_1_out, or_2_out;

  or or_1 (or_1_out, RAZ, or_2_out);
  Counter #(.width(5), .max('h1f)) counter_1 (
    .clr(or_1_out), .load(load), .up(1'b1), .count(1'b1), .clk(clk), .D(Input_heure), .Q(heures));  // open: carry
  or or_2 (or_2_out, comparator_1_gt, clk_heure);
  Comparator #(.width(5), .mode("unsigned")) comparator_1 (
    .a(heures), .b(5'b11000), .gt(comparator_1_gt), .eq(clk_heure));  // open: lt
endmodule

module Jour (
  input  clk,
  input  RAZ,
  input  load,
  input  [4:0] Input_jour,
  input  [3:0] mois,
  input  bisex,
  output clk_jour,
  output [4:0] jours
);

  wire and_1_out, and_2_out, and_3_out, and_4_out, bit0, bit1, bit2, bit3, bit4, clear, comparator_1_eq,
       comparator_2_eq, comparator_3_eq, comparator_4_eq, comparator_5_eq, comparator_6_eq, comparator_7_eq,
       comparator_8_eq, comparator_9_eq, comparator_10_eq, comparator_11_eq, comparator_12_eq,
       comparator_13_gt, comparator_14_gt, comparator_15_gt, comparator_16_gt, multiplexer_1_out,
       multiplexer_2_out, multiplexer_4_out, not_1_out, not_2_out, not_3_out, not_4_out, or_1_out, or_2_out;
  wire [1:0] or_4_out;
  wire [4:0] subtractor_1_out;

  Subtractor #(.width(5)) subtractor_1 (.a(Input_jour), .b(5'b00001), .out(subtractor_1_out));  // open: bin, bout
  and and_1 (and_1_out, bit0, bit1, bit2, bit3, bit4);
  Comparator #(.width(4), .mode("unsigned")) comparator_1 (
    .a(mois), .b(4'b0001), .eq(comparator_1_eq));  // open: gt, lt
  Comparator #(.width(4), .mode("unsigned")) comparator_2 (
    .a(mois), .b(4'b0010), .eq(comparator_2_eq));  // open: gt, lt
  Comparator #(.width(4), .mode("unsigned")) comparator_3 (
    .a(mois), .b(4'b0011), .eq(comparator_3_eq));  // open: gt, lt
  Comparator #(.width(4), .mode("unsigned")) comparator_4 (
    .a(mois), .b(4'b0100), .eq(comparator_4_eq));  // open: gt, lt
  Comparator #(.width(4), .mode("unsigned")) comparator_5 (
    .a(mois), .b(4'b0101), .eq(comparator_5_eq));  // open: gt, lt
  Comparator #(.width(4), .mode("unsigned")) comparator_6 (
    .a(mois), .b(4'b0110), .eq(comparator_6_eq));  // open: gt, lt
  Comparator #(.width(4), .mode("unsigned")) comparator_7 (
    .a(mois), .b(4'b0111), .eq(comparator_7_eq));  // open: gt, lt
  Comparator #(.width(4), .mode("unsigned")) comparator_8 (
    .a(mois), .b(4'b1000), .eq(comparator_8_eq));  // open: gt, lt
  Comparator #(.width(4), .mode("unsigned")) comparator_9 (
    .a(mois), .b(4'b1001), .eq(comparator_9_eq));  // open: gt, lt
  Comparator #(.width(4), .mode("unsigned")) comparator_10 (
    .a(mois), .b(4'b1010), .eq(comparator_10_eq));  // open: gt, lt
  Comparator #(.width(4), .mode("unsigned")) comparator_11 (
    .a(mois), .b(4'b1011), .eq(comparator_11_eq));  // open: gt, lt
  Comparator #(.width(4), .mode("unsigned")) comparator_12 (
    .a(mois), .b(4'b1100), .eq(comparator_12_eq));  // open: gt, lt
  Counter #(.width(5), .max('h1f)) counter_1 (
    .clr(clear), .load(load), .up(1'b1), .count(1'b1), .clk(clk), .D(subtractor_1_out),
    .Q({bit4, bit3, bit2, bit1, bit0}));  // open: carry
  not not_1 (not_1_out, bit0);
  and and_2 (and_2_out, not_1_out, bit1, bit2, bit3, bit4);
  or or_1 (or_1_out, comparator_1_eq, comparator_3_eq, comparator_5_eq, comparator_7_eq, comparator_8_eq, comparator_10_eq, comparator_12_eq);
  or or_2 (or_2_out, comparator_4_eq, comparator_6_eq, comparator_9_eq, comparator_11_eq);
  not not_2 (not_2_out, bit1);
  not not_3 (not_3_out, bit0);
  not not_4 (not_4_out, bit1);
  or or_3 (or_4_out[1], or_1_out, or_2_out);
  Adder #(.width(5)) adder_1 (.a({bit4, bit3, bit2, bit1, bit0}), .b(5'b00001), .out(jours));  // open: cin, cout
  Comparator #(.width(5), .mode("unsigned")) comparator_13 (
    .a({bit4, bit3, bit2, bit1, bit0}), .b({5{1'b1}}), .gt(comparator_13_gt));  // open: eq, lt
  Comparator #(.width(5), .mode("unsigned")) comparator_14 (
    .a({bit4, bit3, bit2, bit1, bit0}), .b(5'b11110), .gt(comparator_14_gt));  // open: eq, lt
  Comparator #(.width(5), .mode("unsigned")) comparator_15 (
    .a({bit4, bit3, bit2, bit1, bit0}), .b(5'b11100), .gt(comparator_15_gt));  // open: eq, lt
  Comparator #(.width(5), .mode("unsigned")) comparator_16 (
    .a({bit4, bit3, bit2, bit1, bit0}), .b(5'b11101), .gt(comparator_16_gt));  // open: eq, lt
  and and_3 (and_3_out, bit0, not_2_out, bit2, bit3, bit4);
  and and_4 (and_4_out, not_3_out, not_4_out, bit2, bit3, bit4);
  Multiplexer #(.enable("false")) multiplexer_1 (
    .in0(comparator_15_gt), .in1(comparator_16_gt), .out(multiplexer_1_out), .sel(bisex));
  Multiplexer #(.enable("false")) multiplexer_2 (
    .in0(and_4_out), .in1(and_3_out), .out(multiplexer_2_out), .sel(bisex));
  or or_4 (or_4_out[0], or_1_out, comparator_2_eq);
  Multiplexer #(.select(2), .enable("false")) multiplexer_3 (
    .in0(and_1_out), .in1(multiplexer_2_out), .in2(and_2_out), .in3(and_1_out), .out(clk_jour), .sel(or_4_out));
  Multiplexer #(.select(2), .enable("false")) multiplexer_4 (
    .in0(comparator_13_gt), .in1(multiplexer_1_out), .in2(comparator_14_gt), .in3(comparator_13_gt),
    .out(multiplexer_4_out), .sel(or_4_out));
  or or_5 (clear, RAZ, multiplexer_4_out, clk_jour);
endmodule

module Mois (
  input  clk,
  input  RAZ,
  input  load,
  input  [3:0] Input_mois,
  output clk_mois,
  output [3:0] mois
);

  wire comparator_1_gt, or_1_out, or_2_out;
  wire [3:0] counter_1_q, subtractor_1_out;

  or or_1 (or_1_out, RAZ, or_2_out);
  Subtractor #(.width(4)) subtractor_1 (.a(Input_mois), .b(4'b0001), .out(subtractor_1_out));  // open: bin, bout
  Counter #(.width(4), .max('hf)) counter_1 (
    .clr(or_1_out), .load(load), .up(1'b1), .count(1'b1), .clk(clk), .D(subtractor_1_out), .Q(counter_1_q));  // open: carry
  or or_2 (or_2_out, comparator_1_gt, clk_mois);
  Comparator #(.width(4), .mode("unsigned")) comparator_1 (
    .a(counter_1_q), .b(4'b1100), .gt(comparator_1_gt), .eq(clk_mois));  // open: lt
  Adder #(.width(4)) adder_1 (.a(counter_1_q), .b(4'b0001), .out(mois));  // open: cin, cout
endmodule

module Annee (
  input  clk,
  input  RAZ,
  input  load,
  input  [11:0] Input_Annee,
  output bisex,
  output [11:0] Annee
);

  wire and_1_out, comparator_1_eq, comparator_2_gt, comparator_3_eq;
  wire [11:0] divider_1_rem, divider_2_rem, divider_3_rem;

  Counter #(.width(12), .max('hfff)) counter_1 (
    .clr(RAZ), .load(load), .up(1'b1), .count(1'b1), .clk(clk), .D(Input_Annee), .Q(Annee));  // open: carry
  Divider #(.width(12)) divider_1 (.a(Annee), .b(12'h4), .rem(divider_1_rem));  // open: out, upper
  Comparator #(.width(12), .mode("unsigned")) comparator_1 (
    .a(divider_1_rem), .b({12{1'b0}}), .eq(comparator_1_eq));  // open: gt, lt
  Divider #(.width(12)) divider_2 (.a(Annee), .b(12'h64), .rem(divider_2_rem));  // open: out, upper
  Comparator #(.width(12), .mode("unsigned")) comparator_2 (
    .a(divider_2_rem), .b({12{1'b0}}), .gt(comparator_2_gt));  // open: eq, lt
  Divider #(.width(12)) divider_3 (.a(Annee), .b(12'h190), .rem(divider_3_rem));  // open: out, upper
  Comparator #(.width(12), .mode("unsigned")) comparator_3 (
    .a(divider_3_rem), .b({12{1'b0}}), .eq(comparator_3_eq));  // open: gt, lt
  and and_1 (and_1_out, comparator_1_eq, comparator_2_gt);
  or or_1 (bisex, and_1_out, comparator_3_eq);
endmodule
