// Logisim project Montre2.circ as structural Verilog: 9 circuits, main circuit Horloge
module Horloge (
  input  affichage,
  input  RAZ,
  input  load,
  input  switch_stop,
  input  bouton_unit,
  input  bouton_diz
);

  wire binairy_to_bcd_converter_1_p8, clk, heures_clk_heure, jours_clk_jour, minutes_clk_min, moiss_clk_mois,
       not_1_out, or1_out, secondes_clk_sec;
  wire [1:0] mach1_p5;
  wire [3:0] bcd_to_7_segment_decoder_1_p1, bcd_to_7_segment_decoder_2_p1, bcd_to_7_segment_decoder_3_p1,
       bcd_to_7_segment_decoder_4_p1, bcd_to_7_segment_decoder_5_p1, bcd_to_7_segment_decoder_6_p1,
       binairy_to_bcd_converter_1_p2, binairy_to_bcd_converter_1_p9, binairy_to_bcd_converter_2_p2,
       binairy_to_bcd_converter_2_p3, binairy_to_bcd_converter_3_p2, binairy_to_bcd_converter_3_p3,
       binairy_to_bcd_converter_4_p2, binairy_to_bcd_converter_4_p3, binairy_to_bcd_converter_4_p5,
       binairy_to_bcd_converter_4_p6, i_m, m;
  wire [4:0] h, h_j, i_h, i_j, j;
  wire [5:0] i_min, i_s, min, min_m, multiplexer_6_out, s, s_m;
  wire [11:0] a, i_a;

  Clock u_clk (.out(clk));
  not not_1 (not_1_out, switch_stop);
  // FSM_Entity #(.content("fsm bouton @[ 50 , 50 , 800 , 500 ] { in A [ 1 ] @[ 50 , 165 , 14 , 15 ] ; out\naffich [ 2 ] @[ 780 , 121 , 70 , 15 ] ; codeWidth = 4 ; reset = S0 ; state S0 =\n\"0000\" @[ 142 , 184 , 30 , 30 ] { commands @[ 113 , 168 , 78 , 21 ] { affich =\n\"00\" ; } transitions { S0 -> S1 when A == \"1\" @[ 233 , 136 , 62 , 21 ] ; } }\nstate S1 = \"0001\" @[ 299 , 97 , 30 , 30 ] { commands @[ 302 , 89 , 78 , 21 ] {\naffich = \"01\" ; } transitions { S1 -> S2 when A == \"0\" @[ 444 , 112 , 62 , 21 ]\n; } } state S2 = \"0010\" @[ 520 , 106 , 30 , 30 ] { commands @[ 565 , 121 , 78 ,\n21 ] { affich = \"01\" ; } transitions { S2 -> S3 when A == \"1\" @[ 659 , 185 , 62\n, 21 ] ; } } state S3 = \"0011\" @[ 704 , 234 , 30 , 30 ] { commands @[ 749 , 249\n, 78 , 21 ] { affich = \"10\" ; } transitions { S3 -> S4 when A == \"0\" @[ 712 ,\n340 , 62 , 21 ] ; } } state S4 = \"0100\" @[ 631 , 398 , 30 , 30 ] { commands @[\n676 , 413 , 78 , 21 ] { affich = \"10\" ; } transitions { S4 -> S5 when A == \"1\"\n@[ 393 , 451 , 62 , 21 ] ; } } state S5 = \"0111\" @[ 185 , 382 , 30 , 30 ] {\ncommands @[ 153 , 423 , 78 , 21 ] { affich = \"00\" ; } transitions { S5 -> S0\nwhen A == \"0\" @[ 116 , 287 , 62 , 21 ] ; } } }")) mach1: pin names not known; wires that end beside it: clk, 1'b0, 1'b1, affichage, mach1_p5
  Seconde secondes (
    .clk(clk), .RAZ(RAZ), .load(load), .Input_sec(i_s), .switch_stop(not_1_out), .clk_sec(secondes_clk_sec),
    .secondes(s));
  Minute minutes (
    .clk(clk), .clk_sec(secondes_clk_sec), .RAZ(RAZ), .load(load), .Input_heure(i_min),
    .switch_stop(not_1_out), .clk_min(minutes_clk_min), .minutes(min));
  Conf conf_sec (
    .RAZ(RAZ), .clk(clk), .switch_stop(switch_stop), .bouton_unit(bouton_unit), .bouton_diz(bouton_diz),
    .input_conf(i_s));
  Multiplexer #(.width(5), .enable("false")) multiplexer_1 (.in0(h), .in1({5{1'b0}}), .out(h_j), .sel(mach1_p5[0]));
  Multiplexer #(.width(6), .enable("false")) multiplexer_2 (.in0(min), .in1({1'b0, j}), .out(min_m), .sel(mach1_p5[0]));
  Multiplexer #(.width(6), .enable("false")) multiplexer_3 (.in0(s), .in1({2'b00, m}), .out(s_m), .sel(mach1_p5[0]));
  Heure heures (
    .clk(clk), .clk_min(minutes_clk_min), .clk_sec(secondes_clk_sec), .RAZ(RAZ), .load(load),
    .Input_heure(i_h), .switch_stop(not_1_out), .clk_heure(heures_clk_heure), .heures(h));
  or or1 (or1_out, mach1_p5[0], mach1_p5[1]);
  _7_Segment_Display Hex6 (.dp(1'b0));  // open: g, f, a, b, e, d, c
  // BCD_to_7_Segment_decoder bcd_to_7_segment_decoder_1: pin names not known; wires that end beside it: bcd_to_7_segment_decoder_1_p1
  // BCD_to_7_Segment_decoder bcd_to_7_segment_decoder_2: pin names not known; wires that end beside it: bcd_to_7_segment_decoder_2_p1
  _7_Segment_Display Hex5 (.dp(1'b1));  // open: g, f, a, b, e, d, c
  Multiplexer #(.width(4), .enable("false")) multiplexer_4 (
    .in0(binairy_to_bcd_converter_1_p9), .in1(4'b0000), .out(bcd_to_7_segment_decoder_2_p1), .sel(or1_out));
  Multiplexer #(.width(4), .enable("false")) multiplexer_5 (
    .in0(binairy_to_bcd_converter_1_p2), .in1(4'b0000), .out(bcd_to_7_segment_decoder_1_p1), .sel(or1_out));
  // Binairy_to_BCD_converter #(.binvalue(5)) binairy_to_bcd_converter_1: pin names not known; wires that end beside it: h_j, binairy_to_bcd_converter_1_p2, clk, secondes_clk_sec, minutes_clk_min, heures_clk_heure, RAZ, binairy_to_bcd_converter_1_p8, binairy_to_bcd_converter_1_p9
  // BCD_to_7_Segment_decoder bcd_to_7_segment_decoder_3: pin names not known; wires that end beside it: bcd_to_7_segment_decoder_3_p1
  _7_Segment_Display Hex4 ();  // open: g, f, a, b, e, d, c, dp
  Jour jours (
    .clk(clk), .clk_sec(secondes_clk_sec), .clk_min(minutes_clk_min), .clk_h(heures_clk_heure), .RAZ(RAZ),
    .load(load), .Input_jour(i_j), .mois(m), .bisex(1'b0), .switch_stop(not_1_out),
    .clk_jour(jours_clk_jour), .jours(j));
  _7_Segment_Display Hex3 (.dp(1'b1));  // open: g, f, a, b, e, d, c
  // BCD_to_7_Segment_decoder bcd_to_7_segment_decoder_4: pin names not known; wires that end beside it: bcd_to_7_segment_decoder_4_p1
  // Binairy_to_BCD_converter #(.binvalue(6)) binairy_to_bcd_converter_2: pin names not known; wires that end beside it: min_m, binairy_to_bcd_converter_2_p2, binairy_to_bcd_converter_2_p3
  Multiplexer #(.width(6), .enable("false")) multiplexer_6 (
    .in0(s_m), .in1(i_s), .out(multiplexer_6_out), .sel(switch_stop));
  // BCD_to_7_Segment_decoder bcd_to_7_segment_decoder_5: pin names not known; wires that end beside it: bcd_to_7_segment_decoder_5_p1
  _7_Segment_Display Hex2 (.dp(1'b0));  // open: g, f, a, b, e, d, c
  // Binairy_to_BCD_converter #(.binvalue(6)) binairy_to_bcd_converter_3: pin names not known; wires that end beside it: multiplexer_6_out, binairy_to_bcd_converter_3_p2, binairy_to_bcd_converter_3_p3
  _7_Segment_Display Hex1 (.dp(1'b0));  // open: g, f, a, b, e, d, c
  // BCD_to_7_Segment_decoder bcd_to_7_segment_decoder_6: pin names not known; wires that end beside it: bcd_to_7_segment_decoder_6_p1
  Mois moiss (
    .clk(clk), .clk_sec(secondes_clk_sec), .clk_min(minutes_clk_min), .clk_h(heures_clk_heure),
    .clk_j(jours_clk_jour), .RAZ(RAZ), .load(load), .Input_mois(i_m), .switch_stop(not_1_out),
    .clk_mois(moiss_clk_mois), .mois(m));
  Multiplexer #(.width(4), .enable("false")) multiplexer_7 (
    .in0(binairy_to_bcd_converter_2_p2), .in1(binairy_to_bcd_converter_4_p2),
    .out(bcd_to_7_segment_decoder_3_p1), .sel(mach1_p5[1]));
  Multiplexer #(.width(4), .enable("false")) multiplexer_8 (
    .in0(binairy_to_bcd_converter_2_p3), .in1(binairy_to_bcd_converter_4_p3),
    .out(bcd_to_7_segment_decoder_4_p1), .sel(mach1_p5[1]));
  // Binairy_to_BCD_converter #(.binvalue(12)) binairy_to_bcd_converter_4: pin names not known; wires that end beside it: a, binairy_to_bcd_converter_4_p2, binairy_to_bcd_converter_4_p3, clk, binairy_to_bcd_converter_4_p5, binairy_to_bcd_converter_4_p6
  Multiplexer #(.width(4), .enable("false")) multiplexer_9 (
    .in0(binairy_to_bcd_converter_3_p2), .in1(binairy_to_bcd_converter_4_p5),
    .out(bcd_to_7_segment_decoder_5_p1), .sel(mach1_p5[1]));
  Multiplexer #(.width(4), .enable("false")) multiplexer_10 (
    .in0(binairy_to_bcd_converter_3_p3), .in1(binairy_to_bcd_converter_4_p6),
    .out(bcd_to_7_segment_decoder_6_p1), .sel(mach1_p5[1]));
  Annee annees (
    .clk(clk), .clk_sec(secondes_clk_sec), .clk_min(minutes_clk_min), .clk_h(heures_clk_heure),
    .clk_j(jours_clk_jour), .clk_m(moiss_clk_mois), .RAZ(RAZ), .load(load), .Input_Annee(i_a),
    .switch_stop(not_1_out), .Annee(a));

  // Other names for the same wires on the sheet: sw = switch_stop
endmodule

module Seconde (
  input  clk,
  input  RAZ,
  input  load,
  input  [5:0] Input_sec,
  input  switch_stop,
  output clk_sec,
  output [5:0] secondes
);

  wire comparator_1_eq, comparator_1_gt, or2_out, or3_out;

  or or2 (or2_out, RAZ, or3_out);
  Counter #(.width(6), .max('h3f)) csec (
    .clr(or2_out), .load(load), .up(1'b1), .count(switch_stop), .clk(clk), .D(Input_sec), .Q(secondes));  // open: carry
  or or3 (or3_out, comparator_1_gt, comparator_1_eq);
  Comparator #(.width(6), .mode("unsigned")) comparator_1 (
    .a(secondes), .b(6'b111100), .gt(comparator_1_gt), .eq(comparator_1_eq));  // open: lt
  Comparator #(.width(6), .mode("unsigned")) comparator_2 (.a(secondes), .b(6'b111011), .eq(clk_sec));  // open: gt, lt
endmodule

module Minute (
  input  clk,
  input  clk_sec,
  input  RAZ,
  input  load,
  input  [5:0] Input_heure,
  input  switch_stop,
  output clk_min,
  output [5:0] minutes
);

  wire and2_out, comparator_1_eq, comparator_1_gt, or4_out, or5_out;

  and and2 (and2_out, clk_sec, switch_stop);
  or or4 (or4_out, RAZ, or5_out);
  Counter #(.width(6), .max('h3f)) cmin (
    .clr(or4_out), .load(load), .up(1'b1), .count(and2_out), .clk(clk), .D(Input_heure), .Q(minutes));  // open: carry
  or or5 (or5_out, comparator_1_gt, comparator_1_eq);
  Comparator #(.width(6), .mode("unsigned")) comparator_1 (
    .a(minutes), .b(6'b111100), .gt(comparator_1_gt), .eq(comparator_1_eq));  // open: lt
  Comparator #(.width(6), .mode("unsigned")) comparator_2 (.a(minutes), .b(6'b111011), .eq(clk_min));  // open: gt, lt
endmodule

module Heure (
  input  clk,
  input  clk_min,
  input  clk_sec,
  input  RAZ,
  input  load,
  input  [4:0] Input_heure,
  input  switch_stop,
  output clk_heure,
  output [4:0] heures
);

  wire and3_out, and4_out, comparator_1_eq, comparator_1_gt, or6_out, or7_out;

  and and3 (and3_out, clk_min, clk_sec);
  or or6 (or6_out, RAZ, or7_out);
  and and4 (and4_out, and3_out, switch_stop);
  Counter #(.width(5), .max('h1f)) cheure (
    .clr(or6_out), .load(load), .up(1'b1), .count(and4_out), .clk(clk), .D(Input_heure), .Q(heures));  // open: carry
  or or7 (or7_out, comparator_1_gt, comparator_1_eq);
  Comparator #(.width(5), .mode("unsigned")) comparator_1 (
    .a(heures), .b(5'b11000), .gt(comparator_1_gt), .eq(comparator_1_eq));  // open: lt
  Comparator #(.width(5), .mode("unsigned")) comparator_2 (.a(heures), .b(5'b10111), .eq(clk_heure));  // open: gt, lt
endmodule

module Jour (
  input  clk,
  input  clk_sec,
  input  clk_min,
  input  clk_h,
  input  RAZ,
  input  load,
  input  [4:0] Input_jour,
  input  [3:0] mois,
  input  bisex,
  input  switch_stop,
  output clk_jour,
  output [4:0] jours
);

  wire and_1_out, and_2_out, and_3_out, and_4_out, and_5_out, and_6_out, bit0, bit1, bit2, bit3, bit4, clear,
       comparator_1_eq, comparator_2_eq, comparator_3_eq, comparator_4_eq, comparator_5_eq, comparator_6_eq,
       comparator_7_eq, comparator_8_eq, comparator_9_eq, comparator_10_eq, comparator_11_eq,
       comparator_12_eq, comparator_13_gt, comparator_14_gt, comparator_15_gt, comparator_16_gt,
       comparator_17_eq, comparator_18_eq, comparator_19_eq, comparator_20_eq, multiplexer_1_out,
       multiplexer_2_out, multiplexer_3_out, multiplexer_4_out, multiplexer_5_out, not_1_out, not_2_out,
       not_3_out, not_4_out, or_1_out, or_2_out;
  wire [1:0] or_4_out;
  wire [4:0] subtractor_1_out;

  and and_1 (and_1_out, clk_sec, clk_min, clk_h);
  Subtractor #(.width(5)) subtractor_1 (
    .a(Input_jour), .b(5'b00001), .out(subtractor_1_out), .bin(1'b0));  // open: bout
  and and_2 (and_2_out, bit0, bit1, bit2, bit3, bit4);
  Comparator #(.width(4), .mode("unsigned")) comparator_1 (
    .a(mois), .b(4'b0001), .eq(comparator_1_eq));  // open: gt, lt
  Comparator #(.width(4), .mode("unsigned")) comparator_2 (
    .a(mois), .b(4'b0010), .eq(comparator_2_eq));  // open: gt, lt
  Comparator #(.width(4), .mode("unsigned")) comparator_3 (
    .a(mois), .b(4'b0011), .eq(comparator_3_eq));  // open: gt, lt
  Comparator #(.width(4), .mode("unsigned")) comparator_4 (
    .a(mois), .b(4'b0100), .eq(comparator_4_eq));  // open: gt, lt
  Comparator #(.width(4), .mode("unsigned")) comparator_5 (
    .a(mois), .b(4'b0101), .eq(comparator_5_eq));  // open: gt, lt
  Comparator #(.width(4), .mode("unsigned")) comparator_6 (
    .a(mois), .b(4'b0110), .eq(comparator_6_eq));  // open: gt, lt
  Comparator #(.width(4), .mode("unsigned")) comparator_7 (
    .a(mois), .b(4'b0111), .eq(comparator_7_eq));  // open: gt, lt
  Comparator #(.width(4), .mode("unsigned")) comparator_8 (
    .a(mois), .b(4'b1000), .eq(comparator_8_eq));  // open: gt, lt
  Comparator #(.width(4), .mode("unsigned")) comparator_9 (
    .a(mois), .b(4'b1001), .eq(comparator_9_eq));  // open: gt, lt
  Comparator #(.width(4), .mode("unsigned")) comparator_10 (
    .a(mois), .b(4'b1010), .eq(comparator_10_eq));  // open: gt, lt
  Comparator #(.width(4), .mode("unsigned")) comparator_11 (
    .a(mois), .b(4'b1011), .eq(comparator_11_eq));  // open: gt, lt
  Comparator #(.width(4), .mode("unsigned")) comparator_12 (
    .a(mois), .b(4'b1100), .eq(comparator_12_eq));  // open: gt, lt
  and and_3 (and_3_out, and_1_out, switch_stop);
  Counter #(.width(5), .max('h1f)) counter_1 (
    .clr(clear), .load(load), .up(1'b1), .count(and_3_out), .clk(clk), .D(subtractor_1_out),
    .Q({bit4, bit3, bit2, bit1, bit0}));  // open: carry
  not not_1 (not_1_out, bit0);
  and and_4 (and_4_out, not_1_out, bit1, bit2, bit3, bit4);
  or or_1 (or_1_out, comparator_1_eq, comparator_3_eq, comparator_5_eq, comparator_7_eq, comparator_8_eq, comparator_10_eq, comparator_12_eq);
  or or_2 (or_2_out, comparator_4_eq, comparator_6_eq, comparator_9_eq, comparator_11_eq);
  not not_2 (not_2_out, bit1);
  not not_3 (not_3_out, bit0);
  not not_4 (not_4_out, bit1);
  or or_3 (or_4_out[1], or_1_out, or_2_out);
  Adder #(.width(5)) adder_1 (.a({bit4, bit3, bit2, bit1, bit0}), .b(5'b00001), .out(jours), .cin(1'b0));  // open: cout
  Comparator #(.width(5), .mode("unsigned")) comparator_13 (
    .a({bit4, bit3, bit2, bit1, bit0}), .b({5{1'b1}}), .gt(comparator_13_gt));  // open: eq, lt
  Comparator #(.width(5), .mode("unsigned")) comparator_14 (
    .a({bit4, bit3, bit2, bit1, bit0}), .b(5'b11110), .gt(comparator_14_gt));  // open: eq, lt
  Comparator #(.width(5), .mode("unsigned")) comparator_15 (
    .a({bit4, bit3, bit2, bit1, bit0}), .b(5'b11100), .gt(comparator_15_gt));  // open: eq, lt
  Comparator #(.width(5), .mode("unsigned")) comparator_16 (
    .a({bit4, bit3, bit2, bit1, bit0}), .b(5'b11101), .gt(comparator_16_gt));  // open: eq, lt
  and and_5 (and_5_out, bit0, not_2_out, bit2, bit3, bit4);
  and and_6 (and_6_out, not_3_out, not_4_out, bit2, bit3, bit4);
  Multiplexer #(.enable("false")) multiplexer_1 (
    .in0(comparator_15_gt), .in1(comparator_16_gt), .out(multiplexer_1_out), .sel(bisex));
  Multiplexer #(.enable("false")) multiplexer_2 (
    .in0(and_6_out), .in1(and_5_out), .out(multiplexer_2_out), .sel(bisex));
  or or_4 (or_4_out[0], or_1_out, comparator_2_eq);
  Multiplexer #(.select(2), .enable("false")) multiplexer_3 (
    .in0(and_2_out), .in1(multiplexer_2_out), .in2(and_4_out), .in3(and_2_out), .out(multiplexer_3_out),
    .sel(or_4_out));
  Comparator #(.width(5), .mode("unsigned")) comparator_17 (
    .a(jours), .b({5{1'b1}}), .eq(comparator_17_eq));  // open: gt, lt
  Comparator #(.width(5), .mode("unsigned")) comparator_18 (
    .a(jours), .b(5'b11110), .eq(comparator_18_eq));  // open: gt, lt
  Comparator #(.width(5), .mode("unsigned")) comparator_19 (
    .a(jours), .b(5'b11100), .eq(comparator_19_eq));  // open: gt, lt
  Comparator #(.width(5), .mode("unsigned")) comparator_20 (
    .a(jours), .b(5'b11101), .eq(comparator_20_eq));  // open: gt, lt
  Multiplexer #(.select(2), .enable("false")) multiplexer_4 (
    .in0(comparator_13_gt), .in1(multiplexer_1_out), .in2(comparator_14_gt), .in3(comparator_13_gt),
    .out(multiplexer_4_out), .sel(or_4_out));
  Multiplexer #(.enable("false")) multiplexer_5 (
    .in0(comparator_19_eq), .in1(comparator_20_eq), .out(multiplexer_5_out), .sel(bisex));
  or or_5 (clear, RAZ, multiplexer_4_out, multiplexer_3_out);
  Multiplexer #(.select(2), .enable("false")) multiplexer_6 (
    .in0(comparator_17_eq), .in1(multiplexer_5_out), .in2(comparator_18_eq), .in3(comparator_17_eq),
    .out(clk_jour), .sel(or_4_out));
endmodule

module Mois (
  input  clk,
  input  clk_sec,
  input  clk_min,
  input  clk_h,
  input  clk_j,
  input  RAZ,
  input  load,
  input  [3:0] Input_mois,
  input  switch_stop,
  output clk_mois,
  output [3:0] mois
);

  wire and_1_out, and_2_out, comparator_1_eq, comparator_1_gt, or_1_out, or_2_out;
  wire [3:0] counter_1_q, subtractor_1_out;

  and and_1 (and_1_out, clk_sec, clk_min, clk_h, clk_j);
  or or_1 (or_1_out, RAZ, or_2_out);
  Subtractor #(.width(4)) subtractor_1 (.a(Input_mois), .b(4'b0001), .out(subtractor_1_out), .bin(1'b0));  // open: bout
  and and_2 (and_2_out, and_1_out, switch_stop);
  Counter #(.width(4), .max('hf)) counter_1 (
    .clr(or_1_out), .load(load), .up(1'b1), .count(and_2_out), .clk(clk), .D(subtractor_1_out),
    .Q(counter_1_q));  // open: carry
  or or_2 (or_2_out, comparator_1_gt, comparator_1_eq);
  Comparator #(.width(4), .mode("unsigned")) comparator_1 (
    .a(counter_1_q), .b(4'b1100), .gt(comparator_1_gt), .eq(comparator_1_eq));  // open: lt
  Adder #(.width(4)) adder_1 (.a(counter_1_q), .b(4'b0001), .out(mois), .cin(1'b0));  // open: cout
  Comparator #(.width(4), .mode("unsigned")) comparator_2 (.a(mois), .b(4'b1100), .eq(clk_mois));  // open: gt, lt
endmodule

module Annee (
  input  clk,
  input  clk_sec,
  input  clk_min,
  input  clk_h,
  input  clk_j,
  input  clk_m,
  input  RAZ,
  input  load,
  input  [11:0] Input_Annee,
  input  switch_stop,
  output [11:0] Annee
);

  wire and_1_out, and_2_out;

  and and_1 (and_1_out, clk_sec, clk_min, clk_h, clk_j, clk_m);
  Counter #(.width(12), .max('hfff)) counter_1 (
    .clr(RAZ), .load(load), .up(1'b1), .count(and_2_out), .clk(clk), .D(Input_Annee), .Q(Annee));  // open: carry
  and and_2 (and_2_out, and_1_out, switch_stop);
endmodule

module Conf (
  input  RAZ,
  input  clk,
  input  switch_stop,
  input  bouton_unit,
  input  bouton_diz,
  output [5:0] input_conf
);

  wire bouton_di_p5, bouton_un_p5, comparator_1_eq, comparator_2_eq, or1_out, or2_out;
  wire [3:0] diza_q, unit_q;
  wire [5:0] multiplier_1_out;

  // FSM_Entity #(.content("fsm bouton1 @[ 50 , 50 , 800 , 500 ] { in B [ 1 ] @[ 50 , 100 , 14 , 15 ] ; out\ncount [ 1 ] @[ 808 , 140 , 42 , 15 ] ; codeWidth = 2 ; reset = S0 ; state S0 =\n\"01\" @[ 225 , 235 , 30 , 30 ] { commands @[ 270 , 250 , 72 , 21 ] { count = \"0\"\n; } transitions { S0 -> S1 when B == \"1\" @[ 312 , 178 , 62 , 21 ] ; } } state\nS1 = \"10\" @[ 470 , 186 , 30 , 30 ] { commands @[ 541 , 190 , 72 , 21 ] { count\n= \"1\" ; } transitions { S1 -> S0 when default @[ 355 , 292 , 50 , 21 ] ; } } }")) bouton_un: pin names not known; wires that end beside it: clk, 1'b0, switch_stop, bouton_unit, bouton_un_p5
  // FSM_Entity #(.content("fsm example @[ 50 , 50 , 800 , 500 ] { in B [ 1 ] @[ 50 , 100 , 14 , 15 ] ; out\ncount [ 1 ] @[ 808 , 140 , 42 , 15 ] ; codeWidth = 2 ; reset = S0 ; state S0 =\n\"01\" @[ 287 , 215 , 30 , 30 ] { commands @[ 259 , 196 , 72 , 21 ] { count = \"0\"\n; } transitions { S0 -> S1 when B == \"1\" @[ 432 , 151 , 62 , 21 ] ; } } state\nS1 = \"10\" @[ 522 , 214 , 30 , 30 ] { commands @[ 567 , 229 , 72 , 21 ] { count\n= \"1\" ; } transitions { S1 -> S0 when default @[ 440 , 313 , 50 , 21 ] ; } } }")) bouton_di: pin names not known; wires that end beside it: clk, 1'b0, switch_stop, bouton_diz, bouton_di_p5
  or or1 (or1_out, comparator_1_eq, RAZ);
  or or2 (or2_out, comparator_2_eq, RAZ);
  Counter #(.width(4), .max('hf)) unit (
    .clr(or1_out), .load(1'b0), .up(1'b1), .count(bouton_un_p5), .clk(clk), .D(4'b0000), .Q(unit_q));  // open: carry
  Counter #(.width(4), .max('hf)) diza (
    .clr(or2_out), .load(1'b0), .up(1'b1), .count(bouton_di_p5), .clk(clk), .D(4'b0000), .Q(diza_q));  // open: carry
  Comparator #(.width(4), .mode("unsigned")) comparator_1 (
    .a(unit_q), .b(4'b1010), .eq(comparator_1_eq));  // open: gt, lt
  Comparator #(.width(4), .mode("unsigned")) comparator_2 (
    .a(diza_q), .b(4'b0110), .eq(comparator_2_eq));  // open: gt, lt
  Multiplier #(.width(6)) multiplier_1 (
    .a({2'b00, diza_q}), .b(6'b001010), .out(multiplier_1_out), .cin({6{1'b0}}));  // open: cout
  Adder #(.width(6)) adder_1 (.a({2'b00, unit_q}), .b(multiplier_1_out), .out(input_conf), .cin(1'b0));  // open: cout

  // Other names for the same wires on the sheet: sw = switch_stop
endmodule

module testConf (
  input  RAZ,
  input  SW,
  input  B1,
  input  B2,
  output SWX,
  output B1X,
  output B2X,
  output RAZX
);

  wire bcd_to_7_segment_decoder_1_p1, binairy_to_bcd_converter_1_p3, clk_out;
  wire [5:0] conff_input_conf;

  Clock clk (.out(clk_out));
  Conf conff (
    .RAZ(RAZ), .clk(clk_out), .switch_stop(SW), .bouton_unit(B1), .bouton_diz(B2),
    .input_conf(conff_input_conf));
  // BCD_to_7_Segment_decoder bcd_to_7_segment_decoder_1: pin names not known; wires that end beside it: bcd_to_7_segment_decoder_1_p1
  _7_Segment_Display Hex2 ();  // open: g, f, a, b, e, d, c, dp
  // Binairy_to_BCD_converter #(.binvalue(6)) binairy_to_bcd_converter_1: pin names not known; wires that end beside it: conff_input_conf, bcd_to_7_segment_decoder_1_p1, binairy_to_bcd_converter_1_p3
  _7_Segment_Display Hex1 ();  // open: g, f, a, b, e, d, c, dp
  // BCD_to_7_Segment_decoder bcd_to_7_segment_decoder_2: pin names not known; wires that end beside it: binairy_to_bcd_converter_1_p3

  assign B1X = B1;
  assign B2X = B2;
  assign RAZX = RAZ;
  assign SWX = SW;
endmodule
