// Logisim project Montre3.circ as structural Verilog: 12 circuits, main circuit Horloge
module Horloge (
  input  affichage,
  input  RAZ,
  input  load,
  input  switch_stop,
  input  bouton_unit,
  input  bouton_diz,
  input  conf,
  output [1:0] confi
);

  wire and_1_out, and_2_out, annees_bisex, binairy_to_bcd_converter_1_p8, clk, comparator_1_gt,
       comparator_2_eq, comparator_3_gt, demultiplexer_1_out0, demultiplexer_1_out1, demultiplexer_1_out2,
       demultiplexer_2_out0, demultiplexer_2_out1, demultiplexer_2_out2, demultiplexer_3_out0,
       demultiplexer_3_out1, demultiplexer_3_out2, demultiplexer_4_out0, demultiplexer_4_out1,
       demultiplexer_4_out2, demultiplexer_5_out0, demultiplexer_5_out1, demultiplexer_6_out1,
       demultiplexer_7_out0, demultiplexer_7_out1, demultiplexer_8_out0, demultiplexer_8_out1,
       heures_clk_heure, jours_clk_jour, mach2_p2, minutes_clk_min, moiss_clk_mois, not_1_out, not_2_out,
       or1_out, or_2_out, secondes_clk_sec;
  wire [1:0] Affich;
  wire [3:0] bcd_to_7_segment_decoder_1_p1, bcd_to_7_segment_decoder_2_p1, bcd_to_7_segment_decoder_3_p1,
       bcd_to_7_segment_decoder_4_p1, bcd_to_7_segment_decoder_5_p1, bcd_to_7_segment_decoder_6_p1,
       binairy_to_bcd_converter_1_p2, binairy_to_bcd_converter_1_p9, binairy_to_bcd_converter_2_p2,
       binairy_to_bcd_converter_3_p1, binairy_to_bcd_converter_3_p3, binairy_to_bcd_converter_3_p4,
       binairy_to_bcd_converter_4_p2, binairy_to_bcd_converter_4_p3, binairy_to_bcd_converter_4_p5,
       binairy_to_bcd_converter_4_p6, i_m, m;
  wire [4:0] h, h_j, i_h, i_hex3, i_j, j, multiplexer_4_out;
  wire [5:0] i_min, i_s, min, min_m, s, s_m;
  wire [6:0] i_a1, i_a2, i_hex1, i_hex2, multiplexer_7_out, multiplexer_8_out;
  wire [11:0] a, i_a, multiplier_1_out;

  // FSM_Entity #(.content("fsm bouton2 @[ 50 , 50 , 800 , 500 ] { in B [ 1 ] @[ 50 , 100 , 15 , 15 ] ; out\naffich [ 2 ] @[ 781 , 140 , 69 , 15 ] ; codeWidth = 4 ; reset = S0 ; state S0 =\n\"0000\" @[ 127 , 192 , 30 , 30 ] { commands @[ 172 , 207 , 79 , 21 ] { affich =\n\"00\" ; } transitions { S0 -> S1 when B == \"1\" @[ 241 , 131 , 63 , 21 ] ; } }\nstate S1 = \"0001\" @[ 397 , 143 , 30 , 30 ] { commands @[ 388 , 123 , 79 , 21 ]\n{ affich = \"01\" ; } transitions { S1 -> S2 when B == \"0\" @[ 554 , 145 , 63 , 21\n] ; } } state S2 = \"0010\" @[ 632 , 180 , 30 , 30 ] { commands @[ 677 , 195 , 79\n, 21 ] { affich = \"01\" ; } transitions { S2 -> S3 when B == \"1\" @[ 743 , 229 ,\n63 , 21 ] ; } } state S3 = \"0011\" @[ 700 , 307 , 30 , 30 ] { commands @[ 752 ,\n329 , 79 , 21 ] { affich = \"10\" ; } transitions { S3 -> S4 when B == \"0\" @[ 708\n, 439 , 63 , 21 ] ; } } state S4 = \"0100\" @[ 550 , 441 , 30 , 30 ] { commands\n@[ 595 , 456 , 79 , 21 ] { affich = \"10\" ; } transitions { S4 -> S5 when B ==\n\"1\" @[ 442 , 503 , 63 , 21 ] ; } } state S5 = \"0101\" @[ 222 , 396 , 30 , 30 ] {\ncommands @[ 267 , 411 , 79 , 21 ] { affich = \"00\" ; } transitions { S5 -> S0\nwhen B == \"0\" @[ 93 , 317 , 63 , 21 ] ; } } }")) mach2: pin names not known; wires that end beside it: clk, mach2_p2, 1'b1, conf, confi
  or or_1 (mach2_p2, and_1_out, affichage);
  Clock u_clk (.out(clk));
  not not_1 (not_1_out, switch_stop);
  // FSM_Entity #(.content("fsm bouton @[ 50 , 50 , 800 , 500 ] { in A [ 1 ] @[ 50 , 165 , 14 , 15 ] ; out\naffich [ 2 ] @[ 780 , 121 , 70 , 15 ] ; codeWidth = 4 ; reset = S0 ; state S0 =\n\"0000\" @[ 142 , 184 , 30 , 30 ] { commands @[ 113 , 168 , 78 , 21 ] { affich =\n\"00\" ; } transitions { S0 -> S1 when A == \"1\" @[ 233 , 136 , 62 , 21 ] ; } }\nstate S1 = \"0001\" @[ 299 , 97 , 30 , 30 ] { commands @[ 302 , 89 , 78 , 21 ] {\naffich = \"01\" ; } transitions { S1 -> S2 when A == \"0\" @[ 444 , 112 , 62 , 21 ]\n; } } state S2 = \"0010\" @[ 520 , 106 , 30 , 30 ] { commands @[ 565 , 121 , 78 ,\n21 ] { affich = \"01\" ; } transitions { S2 -> S3 when A == \"1\" @[ 659 , 185 , 62\n, 21 ] ; } } state S3 = \"0011\" @[ 704 , 234 , 30 , 30 ] { commands @[ 749 , 249\n, 78 , 21 ] { affich = \"10\" ; } transitions { S3 -> S4 when A == \"0\" @[ 712 ,\n340 , 62 , 21 ] ; } } state S4 = \"0100\" @[ 631 , 398 , 30 , 30 ] { commands @[\n676 , 413 , 78 , 21 ] { affich = \"10\" ; } transitions { S4 -> S5 when A == \"1\"\n@[ 393 , 451 , 62 , 21 ] ; } } state S5 = \"0111\" @[ 185 , 382 , 30 , 30 ] {\ncommands @[ 153 , 423 , 78 , 21 ] { affich = \"00\" ; } transitions { S5 -> S0\nwhen A == \"0\" @[ 116 , 287 , 62 , 21 ] ; } } }")) mach1: pin names not known; wires that end beside it: clk, 1'b0, 1'b1, affichage, Affich
  Comparator #(.width(2), .mode("unsigned")) comparator_1 (
    .a(Affich), .b(2'b00), .gt(comparator_1_gt));  // open: eq, lt
  and and_1 (and_1_out, comparator_1_gt, comparator_2_eq);
  Demultiplexer #(.select(2), .enable("false")) demultiplexer_1 (
    .out0(demultiplexer_1_out0), .out1(demultiplexer_1_out1), .out2(demultiplexer_1_out2), .in(bouton_unit),
    .sel(Affich));  // open: out3
  Demultiplexer #(.select(2), .enable("false")) demultiplexer_2 (
    .out0(demultiplexer_2_out0), .out1(demultiplexer_2_out1), .out2(demultiplexer_2_out2), .in(bouton_diz),
    .sel(Affich));  // open: out3
  Comparator #(.width(2), .mode("unsigned")) comparator_2 (.a(confi), .b(2'b10), .eq(comparator_2_eq));  // open: gt, lt
  Seconde secondes (
    .clk(clk), .RAZ(RAZ), .load(load), .Input_sec(i_s), .switch_stop(not_1_out), .clk_sec(secondes_clk_sec),
    .secondes(s));
  Demultiplexer #(.select(2), .enable("false")) demultiplexer_3 (
    .out0(demultiplexer_3_out0), .out1(demultiplexer_3_out1), .out2(demultiplexer_3_out2),
    .in(demultiplexer_1_out0), .sel(confi));  // open: out3
  Demultiplexer #(.select(2), .enable("false")) demultiplexer_4 (
    .out0(demultiplexer_4_out0), .out1(demultiplexer_4_out1), .out2(demultiplexer_4_out2),
    .in(demultiplexer_2_out0), .sel(confi));  // open: out3
  Demultiplexer #(.select(2), .enable("false")) demultiplexer_5 (
    .out0(demultiplexer_5_out0), .out1(demultiplexer_5_out1), .in(demultiplexer_1_out1), .sel(confi));  // open: out2, out3
  Demultiplexer #(.select(2), .enable("false")) demultiplexer_6 (
    .out1(demultiplexer_6_out1), .in(demultiplexer_2_out1), .sel(confi));  // open: out0, out2, out3
  Demultiplexer #(.select(2), .enable("false")) demultiplexer_7 (
    .out0(demultiplexer_7_out0), .out1(demultiplexer_7_out1), .in(demultiplexer_1_out2), .sel(confi));  // open: out2, out3
  Demultiplexer #(.select(2), .enable("false")) demultiplexer_8 (
    .out0(demultiplexer_8_out0), .out1(demultiplexer_8_out1), .in(demultiplexer_2_out2), .sel(confi));  // open: out2, out3
  Minute minutes (
    .clk(clk), .clk_sec(secondes_clk_sec), .RAZ(RAZ), .load(load), .Input_heure(i_min),
    .switch_stop(not_1_out), .clk_min(minutes_clk_min), .minutes(min));
  Multiplexer #(.width(5), .enable("false")) multiplexer_1 (.in0(h), .in1({5{1'b0}}), .out(h_j), .sel(Affich[0]));
  Multiplexer #(.width(6), .enable("false")) multiplexer_2 (.in0(min), .in1({1'b0, j}), .out(min_m), .sel(Affich[0]));
  Multiplexer #(.width(6), .enable("false")) multiplexer_3 (.in0(s), .in1({2'b00, m}), .out(s_m), .sel(Affich[0]));
  Heure heures (
    .clk(clk), .clk_min(minutes_clk_min), .clk_sec(secondes_clk_sec), .RAZ(RAZ), .load(load),
    .Input_heure(i_h), .switch_stop(not_1_out), .clk_heure(heures_clk_heure), .heures(h));
  Comparator #(.width(12), .mode("unsigned")) comparator_3 (
    .a(i_a), .b({12{1'b1}}), .gt(comparator_3_gt));  // open: eq, lt
  or or1 (or1_out, Affich[0], Affich[1]);
  or or_2 (or_2_out, RAZ, comparator_3_gt);
  Multiplexer #(.width(5), .enable("false")) multiplexer_4 (
    .in0(h_j), .in1(i_hex3), .out(multiplexer_4_out), .sel(switch_stop));
  _7_Segment_Display Hex5 (.dp(1'b1));  // open: g, f, a, b, e, d, c
  _7_Segment_Display Hex6 (.dp(1'b0));  // open: g, f, a, b, e, d, c
  // BCD_to_7_Segment_decoder bcd_to_7_segment_decoder_1: pin names not known; wires that end beside it: bcd_to_7_segment_decoder_1_p1
  // BCD_to_7_Segment_decoder bcd_to_7_segment_decoder_2: pin names not known; wires that end beside it: bcd_to_7_segment_decoder_2_p1
  Multiplexer #(.width(4), .enable("false")) multiplexer_5 (
    .in0(binairy_to_bcd_converter_1_p2), .in1(4'b0000), .out(bcd_to_7_segment_decoder_1_p1), .sel(or1_out));
  Multiplexer #(.width(4), .enable("false")) multiplexer_6 (
    .in0(binairy_to_bcd_converter_1_p9), .in1(4'b0000), .out(bcd_to_7_segment_decoder_2_p1), .sel(or1_out));
  // Binairy_to_BCD_converter #(.binvalue(5)) binairy_to_bcd_converter_1: pin names not known; wires that end beside it: multiplexer_4_out, binairy_to_bcd_converter_1_p2, clk, secondes_clk_sec, minutes_clk_min, heures_clk_heure, RAZ, binairy_to_bcd_converter_1_p8, binairy_to_bcd_converter_1_p9
  Multiplexer #(.width(7), .enable("false")) multiplexer_7 (
    .in0({1'b0, min_m}), .in1(i_hex2), .out(multiplexer_7_out), .sel(switch_stop));
  // BCD_to_7_Segment_decoder bcd_to_7_segment_decoder_3: pin names not known; wires that end beside it: bcd_to_7_segment_decoder_3_p1
  _7_Segment_Display Hex4 ();  // open: g, f, a, b, e, d, c, dp
  // Binairy_to_BCD_converter #(.binvalue(7)) binairy_to_bcd_converter_2: pin names not known; wires that end beside it: multiplexer_7_out, binairy_to_bcd_converter_2_p2
  Jour jours (
    .clk(clk), .clk_sec(secondes_clk_sec), .clk_min(minutes_clk_min), .clk_h(heures_clk_heure), .RAZ(RAZ),
    .load(load), .Input_jour(i_j), .mois(m), .bisex(annees_bisex), .switch_stop(not_1_out),
    .clk_jour(jours_clk_jour), .jours(j));
  // BCD_to_7_Segment_decoder bcd_to_7_segment_decoder_4: pin names not known; wires that end beside it: bcd_to_7_segment_decoder_4_p1
  _7_Segment_Display Hex3 (.dp(1'b1));  // open: g, f, a, b, e, d, c
  Multiplexer #(.width(7), .enable("false")) multiplexer_8 (
    .in0({1'b0, s_m}), .in1(i_hex1), .out(multiplexer_8_out), .sel(switch_stop));
  Conf_sec_min conf_sec (
    .RAZ(RAZ), .clk(clk), .switch_stop(switch_stop), .bouton_unit(demultiplexer_3_out0),
    .bouton_diz(demultiplexer_4_out0), .input_conf(i_s));
  Conf_sec_min conf_min (
    .RAZ(RAZ), .clk(clk), .switch_stop(switch_stop), .bouton_unit(demultiplexer_3_out1),
    .bouton_diz(demultiplexer_4_out1), .input_conf(i_min));
  Conf_h conf_heure (
    .RAZ(RAZ), .clk(clk), .switch_stop(switch_stop), .bouton_unit(demultiplexer_3_out2),
    .bouton_diz(demultiplexer_4_out2), .input_conf(i_h));
  Conf_j Conf_jour (
    .RAZ(RAZ), .clk(clk), .switch_stop(switch_stop), .bouton_unit(demultiplexer_5_out1),
    .bouton_diz(demultiplexer_6_out1), .input_conf(i_j));
  Conj_m Conf_m (.RAZ(RAZ), .clk(clk), .switch_stop(switch_stop), .bouton(demultiplexer_5_out0), .input_conf(i_m));
  Conf_a Conf_a1 (
    .RAZ(or_2_out), .clk(clk), .switch_stop(switch_stop), .bouton_unit(demultiplexer_7_out0),
    .bouton_diz(demultiplexer_8_out0), .input_conf(i_a1));
  Conf_a Conf_a2 (
    .RAZ(or_2_out), .clk(clk), .switch_stop(switch_stop), .bouton_unit(demultiplexer_7_out1),
    .bouton_diz(demultiplexer_8_out1), .input_conf(i_a2));
  _7_Segment_Display Hex2 (.dp(1'b0));  // open: g, f, a, b, e, d, c
  // BCD_to_7_Segment_decoder bcd_to_7_segment_decoder_5: pin names not known; wires that end beside it: bcd_to_7_segment_decoder_5_p1
  not not_2 (not_2_out, switch_stop);
  // Binairy_to_BCD_converter #(.binvalue(7)) binairy_to_bcd_converter_3: pin names not known; wires that end beside it: binairy_to_bcd_converter_3_p1, multiplexer_8_out, binairy_to_bcd_converter_3_p3, binairy_to_bcd_converter_3_p4
  // BCD_to_7_Segment_decoder bcd_to_7_segment_decoder_6: pin names not known; wires that end beside it: bcd_to_7_segment_decoder_6_p1
  _7_Segment_Display Hex1 (.dp(1'b0));  // open: g, f, a, b, e, d, c
  and and_2 (and_2_out, not_2_out, Affich[1]);
  Multiplier #(.width(12)) multiplier_1 (
    .a({{5{1'b0}}, i_a2}), .b(12'h64), .out(multiplier_1_out), .cin({12{1'b0}}));  // open: cout
  Mois moiss (
    .clk(clk), .clk_sec(secondes_clk_sec), .clk_min(minutes_clk_min), .clk_h(heures_clk_heure),
    .clk_j(jours_clk_jour), .RAZ(RAZ), .load(load), .Input_mois(i_m), .switch_stop(not_1_out),
    .clk_mois(moiss_clk_mois), .mois(m));
  Adder #(.width(12)) adder_1 (.a({{5{1'b0}}, i_a1}), .b(multiplier_1_out), .out(i_a), .cin(1'b0));  // open: cout
  Multiplexer #(.width(4), .enable("false")) multiplexer_9 (
    .in0(binairy_to_bcd_converter_2_p2), .in1(binairy_to_bcd_converter_4_p2),
    .out(bcd_to_7_segment_decoder_3_p1), .sel(and_2_out));
  Multiplexer #(.width(4), .enable("false")) multiplexer_10 (
    .in0(binairy_to_bcd_converter_3_p1), .in1(binairy_to_bcd_converter_4_p3),
    .out(bcd_to_7_segment_decoder_4_p1), .sel(and_2_out));
  // Binairy_to_BCD_converter #(.binvalue(12)) binairy_to_bcd_converter_4: pin names not known; wires that end beside it: a, binairy_to_bcd_converter_4_p2, binairy_to_bcd_converter_4_p3, clk, binairy_to_bcd_converter_4_p5, binairy_to_bcd_converter_4_p6
  Multiplexer #(.width(4), .enable("false")) multiplexer_11 (
    .in0(binairy_to_bcd_converter_3_p3), .in1(binairy_to_bcd_converter_4_p5),
    .out(bcd_to_7_segment_decoder_5_p1), .sel(and_2_out));
  Multiplexer #(.select(2), .width(7), .enable("false")) multiplexer_12 (
    .in0({1'b0, i_s}), .in1({3'b000, i_m}), .in2(i_a1), .in3({7{1'b0}}), .out(i_hex1), .sel(Affich));
  Multiplexer #(.select(2), .width(7), .enable("false")) multiplexer_13 (
    .in0({1'b0, i_min}), .in1({2'b00, i_j}), .in2(i_a2), .in3({7{1'b0}}), .out(i_hex2), .sel(Affich));
  Multiplexer #(.select(2), .width(5), .enable("false")) multiplexer_14 (
    .in0(i_h), .in1({5{1'b0}}), .in2({5{1'b0}}), .in3({5{1'b0}}), .out(i_hex3), .sel(Affich));
  Multiplexer #(.width(4), .enable("false")) multiplexer_15 (
    .in0(binairy_to_bcd_converter_3_p4), .in1(binairy_to_bcd_converter_4_p6),
    .out(bcd_to_7_segment_decoder_6_p1), .sel(and_2_out));
  Annee annees (
    .clk(clk), .clk_sec(secondes_clk_sec), .clk_min(minutes_clk_min), .clk_h(heures_clk_heure),
    .clk_j(jours_clk_jour), .clk_m(moiss_clk_mois), .RAZ(RAZ), .load(load), .Input_Annee(i_a),
    .switch_stop(not_1_out), .Annee(a), .bisex(annees_bisex));

  // Other names for the same wires on the sheet: af = affichage; sw = switch_stop
endmodule

module Seconde (
  input  clk,
  input  RAZ,
  input  load,
  input  [5:0] Input_sec,
  input  switch_stop,
  output clk_sec,
  output [5:0] secondes
);

  wire comparator_1_eq, comparator_1_gt, or2_out, or3_out;

  or or2 (or2_out, RAZ, or3_out);
  Counter #(.width(6), .max('h3f)) csec (
    .clr(or2_out), .load(load), .up(1'b1), .count(switch_stop), .clk(clk), .D(Input_sec), .Q(secondes));  // open: carry
  or or3 (or3_out, comparator_1_gt, comparator_1_eq);
  Comparator #(.width(6), .mode("unsigned")) comparator_1 (
    .a(secondes), .b(6'b111100), .gt(comparator_1_gt), .eq(comparator_1_eq));  // open: lt
  Comparator #(.width(6), .mode("unsigned")) comparator_2 (.a(secondes), .b(6'b111011), .eq(clk_sec));  // open: gt, lt
endmodule

module Minute (
  input  clk,
  input  clk_sec,
  input  RAZ,
  input  load,
  input  [5:0] Input_heure,
  input  switch_stop,
  output clk_min,
  output [5:0] minutes
);

  wire and2_out, comparator_1_eq, comparator_1_gt, or4_out, or5_out;

  and and2 (and2_out, clk_sec, switch_stop);
  or or4 (or4_out, RAZ, or5_out);
  Counter #(.width(6), .max('h3f)) cmin (
    .clr(or4_out), .load(load), .up(1'b1), .count(and2_out), .clk(clk), .D(Input_heure), .Q(minutes));  // open: carry
  or or5 (or5_out, comparator_1_gt, comparator_1_eq);
  Comparator #(.width(6), .mode("unsigned")) comparator_1 (
    .a(minutes), .b(6'b111100), .gt(comparator_1_gt), .eq(comparator_1_eq));  // open: lt
  Comparator #(.width(6), .mode("unsigned")) comparator_2 (.a(minutes), .b(6'b111011), .eq(clk_min));  // open: gt, lt
endmodule

module Heure (
  input  clk,
  input  clk_min,
  input  clk_sec,
  input  RAZ,
  input  load,
  input  [4:0] Input_heure,
  input  switch_stop,
  output clk_heure,
  output [4:0] heures
);

  wire and3_out, and4_out, comparator_1_eq, comparator_1_gt, or6_out, or7_out;

  and and3 (and3_out, clk_min, clk_sec);
  or or6 (or6_out, RAZ, or7_out);
  and and4 (and4_out, and3_out, switch_stop);
  Counter #(.width(5), .max('h1f)) cheure (
    .clr(or6_out), .load(load), .up(1'b1), .count(and4_out), .clk(clk), .D(Input_heure), .Q(heures));  // open: carry
  or or7 (or7_out, comparator_1_gt, comparator_1_eq);
  Comparator #(.width(5), .mode("unsigned")) comparator_1 (
    .a(heures), .b(5'b11000), .gt(comparator_1_gt), .eq(comparator_1_eq));  // open: lt
  Comparator #(.width(5), .mode("unsigned")) comparator_2 (.a(heures), .b(5'b10111), .eq(clk_heure));  // open: gt, lt
endmodule

module Jour (
  input  clk,
  input  clk_sec,
  input  clk_min,
  input  clk_h,
  input  RAZ,
  input  load,
  input  [4:0] Input_jour,
  input  [3:0] mois,
  input  bisex,
  input  switch_stop,
  output clk_jour,
  output [4:0] jours
);

  wire and_1_out, and_2_out, and_3_out, and_4_out, and_5_out, and_6_out, bit0, bit1, bit2, bit3, bit4, clear,
       comparator_1_eq, comparator_2_eq, comparator_3_eq, comparator_4_eq, comparator_5_eq, comparator_6_eq,
       comparator_7_eq, comparator_8_eq, comparator_9_eq, comparator_10_eq, comparator_11_eq,
       comparator_12_eq, comparator_13_gt, comparator_14_gt, comparator_15_gt, comparator_16_gt,
       comparator_17_eq, comparator_18_eq, comparator_19_eq, comparator_20_eq, multiplexer_1_out,
       multiplexer_2_out, multiplexer_3_out, multiplexer_4_out, multiplexer_5_out, not_1_out, not_2_out,
       not_3_out, not_4_out, or_1_out, or_2_out;
  wire [1:0] or_4_out;
  wire [4:0] subtractor_1_out;

  and and_1 (and_1_out, clk_sec, clk_min, clk_h);
  Subtractor #(.width(5)) subtractor_1 (
    .a(Input_jour), .b(5'b00001), .out(subtractor_1_out), .bin(1'b0));  // open: bout
  and and_2 (and_2_out, bit0, bit1, bit2, bit3, bit4);
  Comparator #(.width(4), .mode("unsigned")) comparator_1 (
    .a(mois), .b(4'b0001), .eq(comparator_1_eq));  // open: gt, lt
  Comparator #(.width(4), .mode("unsigned")) comparator_2 (
    .a(mois), .b(4'b0010), .eq(comparator_2_eq));  // open: gt, lt
  Comparator #(.width(4), .mode("unsigned")) comparator_3 (
    .a(mois), .b(4'b0011), .eq(comparator_3_eq));  // open: gt, lt
  Comparator #(.width(4), .mode("unsigned")) comparator_4 (
    .a(mois), .b(4'b0100), .eq(comparator_4_eq));  // open: gt, lt
  Comparator #(.width(4), .mode("unsigned")) comparator_5 (
    .a(mois), .b(4'b0101), .eq(comparator_5_eq));  // open: gt, lt
  Comparator #(.width(4), .mode("unsigned")) comparator_6 (
    .a(mois), .b(4'b0110), .eq(comparator_6_eq));  // open: gt, lt
  Comparator #(.width(4), .mode("unsigned")) comparator_7 (
    .a(mois), .b(4'b0111), .eq(comparator_7_eq));  // open: gt, lt
  Comparator #(.width(4), .mode("unsigned")) comparator_8 (
    .a(mois), .b(4'b1000), .eq(comparator_8_eq));  // open: gt, lt
  Comparator #(.width(4), .mode("unsigned")) comparator_9 (
    .a(mois), .b(4'b1001), .eq(comparator_9_eq));  // open: gt, lt
  Comparator #(.width(4), .mode("unsigned")) comparator_10 (
    .a(mois), .b(4'b1010), .eq(comparator_10_eq));  // open: gt, lt
  Comparator #(.width(4), .mode("unsigned")) comparator_11 (
    .a(mois), .b(4'b1011), .eq(comparator_11_eq));  // open: gt, lt
  Comparator #(.width(4), .mode("unsigned")) comparator_12 (
    .a(mois), .b(4'b1100), .eq(comparator_12_eq));  // open: gt, lt
  and and_3 (and_3_out, and_1_out, switch_stop);
  Counter #(.width(5), .max('h1f)) counter_1 (
    .clr(clear), .load(load), .up(1'b1), .count(and_3_out), .clk(clk), .D(subtractor_1_out),
    .Q({bit4, bit3, bit2, bit1, bit0}));  // open: carry
  not not_1 (not_1_out, bit0);
  and and_4 (and_4_out, not_1_out, bit1, bit2, bit3, bit4);
  or or_1 (or_1_out, comparator_1_eq, comparator_3_eq, comparator_5_eq, comparator_7_eq, comparator_8_eq, comparator_10_eq, comparator_12_eq);
  or or_2 (or_2_out, comparator_4_eq, comparator_6_eq, comparator_9_eq, comparator_11_eq);
  not not_2 (not_2_out, bit1);
  not not_3 (not_3_out, bit0);
  not not_4 (not_4_out, bit1);
  or or_3 (or_4_out[1], or_1_out, or_2_out);
  Adder #(.width(5)) adder_1 (.a({bit4, bit3, bit2, bit1, bit0}), .b(5'b00001), .out(jours), .cin(1'b0));  // open: cout
  Comparator #(.width(5), .mode("unsigned")) comparator_13 (
    .a({bit4, bit3, bit2, bit1, bit0}), .b({5{1'b1}}), .gt(comparator_13_gt));  // open: eq, lt
  Comparator #(.width(5), .mode("unsigned")) comparator_14 (
    .a({bit4, bit3, bit2, bit1, bit0}), .b(5'b11110), .gt(comparator_14_gt));  // open: eq, lt
  Comparator #(.width(5), .mode("unsigned")) comparator_15 (
    .a({bit4, bit3, bit2, bit1, bit0}), .b(5'b11100), .gt(comparator_15_gt));  // open: eq, lt
  Comparator #(.width(5), .mode("unsigned")) comparator_16 (
    .a({bit4, bit3, bit2, bit1, bit0}), .b(5'b11101), .gt(comparator_16_gt));  // open: eq, lt
  and and_5 (and_5_out, bit0, not_2_out, bit2, bit3, bit4);
  and and_6 (and_6_out, not_3_out, not_4_out, bit2, bit3, bit4);
  Multiplexer #(.enable("false")) multiplexer_1 (
    .in0(comparator_15_gt), .in1(comparator_16_gt), .out(multiplexer_1_out), .sel(bisex));
  Multiplexer #(.enable("false")) multiplexer_2 (
    .in0(and_6_out), .in1(and_5_out), .out(multiplexer_2_out), .sel(bisex));
  or or_4 (or_4_out[0], or_1_out, comparator_2_eq);
  Multiplexer #(.select(2), .enable("false")) multiplexer_3 (
    .in0(and_2_out), .in1(multiplexer_2_out), .in2(and_4_out), .in3(and_2_out), .out(multiplexer_3_out),
    .sel(or_4_out));
  Comparator #(.width(5), .mode("unsigned")) comparator_17 (
    .a(jours), .b({5{1'b1}}), .eq(comparator_17_eq));  // open: gt, lt
  Comparator #(.width(5), .mode("unsigned")) comparator_18 (
    .a(jours), .b(5'b11110), .eq(comparator_18_eq));  // open: gt, lt
  Comparator #(.width(5), .mode("unsigned")) comparator_19 (
    .a(jours), .b(5'b11100), .eq(comparator_19_eq));  // open: gt, lt
  Comparator #(.width(5), .mode("unsigned")) comparator_20 (
    .a(jours), .b(5'b11101), .eq(comparator_20_eq));  // open: gt, lt
  Multiplexer #(.select(2), .enable("false")) multiplexer_4 (
    .in0(comparator_13_gt), .in1(multiplexer_1_out), .in2(comparator_14_gt), .in3(comparator_13_gt),
    .out(multiplexer_4_out), .sel(or_4_out));
  Multiplexer #(.enable("false")) multiplexer_5 (
    .in0(comparator_19_eq), .in1(comparator_20_eq), .out(multiplexer_5_out), .sel(bisex));
  or or_5 (clear, RAZ, multiplexer_4_out, multiplexer_3_out);
  Multiplexer #(.select(2), .enable("false")) multiplexer_6 (
    .in0(comparator_17_eq), .in1(multiplexer_5_out), .in2(comparator_18_eq), .in3(comparator_17_eq),
    .out(clk_jour), .sel(or_4_out));
endmodule

module Mois (
  input  clk,
  input  clk_sec,
  input  clk_min,
  input  clk_h,
  input  clk_j,
  input  RAZ,
  input  load,
  input  [3:0] Input_mois,
  input  switch_stop,
  output clk_mois,
  output [3:0] mois
);

  wire and_1_out, and_2_out, comparator_1_eq, comparator_1_gt, or_1_out, or_2_out;
  wire [3:0] counter_1_q, subtractor_1_out;

  and and_1 (and_1_out, clk_sec, clk_min, clk_h, clk_j);
  or or_1 (or_1_out, RAZ, or_2_out);
  Subtractor #(.width(4)) subtractor_1 (.a(Input_mois), .b(4'b0001), .out(subtractor_1_out), .bin(1'b0));  // open: bout
  and and_2 (and_2_out, and_1_out, switch_stop);
  Counter #(.width(4), .max('hf)) counter_1 (
    .clr(or_1_out), .load(load), .up(1'b1), .count(and_2_out), .clk(clk), .D(subtractor_1_out),
    .Q(counter_1_q));  // open: carry
  or or_2 (or_2_out, comparator_1_gt, comparator_1_eq);
  Comparator #(.width(4), .mode("unsigned")) comparator_1 (
    .a(counter_1_q), .b(4'b1100), .gt(comparator_1_gt), .eq(comparator_1_eq));  // open: lt
  Adder #(.width(4)) adder_1 (.a(counter_1_q), .b(4'b0001), .out(mois), .cin(1'b0));  // open: cout
  Comparator #(.width(4), .mode("unsigned")) comparator_2 (.a(mois), .b(4'b1100), .eq(clk_mois));  // open: gt, lt
endmodule

module Annee (
  input  clk,
  input  clk_sec,
  input  clk_min,
  input  clk_h,
  input  clk_j,
  input  clk_m,
  input  RAZ,
  input  load,
  input  [11:0] Input_Annee,
  input  switch_stop,
  output [11:0] Annee,
  output bisex
);

  wire and_1_out, and_2_out, comparator_1_eq, or_1_out;
  wire [2:0] adder_1_out, counter_2_q;

  or or_1 (or_1_out, RAZ, comparator_1_eq);
  and and_1 (and_1_out, clk_sec, clk_min, clk_h, clk_j, clk_m);
  Counter #(.width(12), .max('hfff)) counter_1 (
    .clr(RAZ), .load(load), .up(1'b1), .count(and_2_out), .clk(clk), .D(Input_Annee), .Q(Annee));  // open: carry
  Counter #(.width(3), .max('h7)) counter_2 (
    .clr(or_1_out), .load(1'b0), .up(1'b1), .count(switch_stop), .clk(clk), .D(3'b000), .Q(counter_2_q));  // open: carry
  and and_2 (and_2_out, and_1_out, switch_stop);
  Adder #(.width(3)) adder_1 (.a(counter_2_q), .b(3'b001), .out(adder_1_out));  // open: cin, cout
  Comparator #(.width(3), .mode("unsigned")) comparator_1 (
    .a(adder_1_out), .b(3'b101), .eq(comparator_1_eq));  // open: gt, lt
  Comparator #(.width(3), .mode("unsigned")) comparator_2 (.a(adder_1_out), .b(3'b100), .eq(bisex));  // open: gt, lt
endmodule

module Conf_sec_min (
  input  RAZ,
  input  clk,
  input  switch_stop,
  input  bouton_unit,
  input  bouton_diz,
  output [5:0] input_conf
);

  wire and_1_out, and_2_out, comparator_1_eq, comparator_2_eq, or1_out, or2_out;
  wire [3:0] diza_q, unit_q;
  wire [5:0] multiplier_1_out;

  and and_1 (and_1_out, switch_stop, bouton_unit);
  or or1 (or1_out, comparator_1_eq, RAZ);
  or or2 (or2_out, comparator_2_eq, RAZ);
  and and_2 (and_2_out, switch_stop, bouton_diz);
  Counter #(.width(4), .max('hf)) unit (
    .clr(or1_out), .load(1'b0), .up(1'b1), .count(and_1_out), .clk(clk), .D(4'b0000), .Q(unit_q));  // open: carry
  Counter #(.width(4), .max('hf)) diza (
    .clr(or2_out), .load(1'b0), .up(1'b1), .count(and_2_out), .clk(clk), .D(4'b0000), .Q(diza_q));  // open: carry
  Comparator #(.width(4), .mode("unsigned")) comparator_1 (
    .a(unit_q), .b(4'b1010), .eq(comparator_1_eq));  // open: gt, lt
  Comparator #(.width(4), .mode("unsigned")) comparator_2 (
    .a(diza_q), .b(4'b0110), .eq(comparator_2_eq));  // open: gt, lt
  Multiplier #(.width(6)) multiplier_1 (
    .a({2'b00, diza_q}), .b(6'b001010), .out(multiplier_1_out), .cin({6{1'b0}}));  // open: cout
  Adder #(.width(6)) adder_1 (.a({2'b00, unit_q}), .b(multiplier_1_out), .out(input_conf), .cin(1'b0));  // open: cout

  // Other names for the same wires on the sheet: sw = switch_stop
endmodule

module Conf_h (
  input  RAZ,
  input  clk,
  input  switch_stop,
  input  bouton_unit,
  input  bouton_diz,
  output [4:0] input_conf
);

  wire and6_out, and7_out, comparator_1_eq, comparator_2_eq, comparator_3_lt, not_1_out, or5_out, or6_out,
       or_1_out, or_2_out;
  wire [3:0] diza_q, unit_q;
  wire [4:0] multiplier_1_out;

  and and6 (and6_out, switch_stop, bouton_unit);
  or or5 (or5_out, or_2_out, RAZ);
  or or6 (or6_out, or_1_out, RAZ);
  and and7 (and7_out, switch_stop, bouton_diz);
  Counter #(.width(4), .max('hf)) unit (
    .clr(or5_out), .load(1'b0), .up(1'b1), .count(and6_out), .clk(clk), .D(4'b0000), .Q(unit_q));  // open: carry
  Counter #(.width(4), .max('hf)) diza (
    .clr(or6_out), .load(1'b0), .up(1'b1), .count(and7_out), .clk(clk), .D(4'b0000), .Q(diza_q));  // open: carry
  or or_1 (or_1_out, or_2_out, comparator_2_eq);
  Comparator #(.width(4), .mode("unsigned")) comparator_1 (
    .a(unit_q), .b(4'b1010), .eq(comparator_1_eq));  // open: gt, lt
  Comparator #(.width(4), .mode("unsigned")) comparator_2 (
    .a(diza_q), .b(4'b0011), .eq(comparator_2_eq));  // open: gt, lt
  or or_2 (or_2_out, comparator_1_eq, not_1_out);
  Multiplier #(.width(5)) multiplier_1 (
    .a({1'b0, diza_q}), .b(5'b01010), .out(multiplier_1_out), .cin({5{1'b0}}));  // open: cout
  Adder #(.width(5)) adder_1 (.a({1'b0, unit_q}), .b(multiplier_1_out), .out(input_conf), .cin(1'b0));  // open: cout
  Comparator #(.width(5), .mode("unsigned")) comparator_3 (
    .a(input_conf), .b(5'b11001), .lt(comparator_3_lt));  // open: gt, eq
  not not_1 (not_1_out, comparator_3_lt);

  // Other names for the same wires on the sheet: sw = switch_stop
endmodule

module Conf_j (
  input  RAZ,
  input  clk,
  input  switch_stop,
  input  bouton_unit,
  input  bouton_diz,
  output [4:0] input_conf
);

  wire and8_out, and9_out, comparator_1_eq, comparator_2_eq, or7_out, or8_out;
  wire [3:0] counter_1_q, unit_q;
  wire [4:0] multiplier_1_out;

  or or7 (or7_out, comparator_1_eq, RAZ);
  and and8 (and8_out, switch_stop, bouton_unit);
  or or8 (or8_out, comparator_2_eq, RAZ);
  and and9 (and9_out, switch_stop, bouton_diz);
  Counter #(.width(4), .max('hf)) unit (
    .clr(or7_out), .load(1'b0), .up(1'b1), .count(and8_out), .clk(clk), .D(4'b0000), .Q(unit_q));  // open: carry
  Counter #(.width(4), .max('hf)) counter_1 (
    .clr(or8_out), .load(1'b0), .up(1'b1), .count(and9_out), .clk(clk), .D(4'b0000), .Q(counter_1_q));  // open: carry
  Comparator #(.width(4), .mode("unsigned")) comparator_1 (
    .a(unit_q), .b(4'b1010), .eq(comparator_1_eq));  // open: gt, lt
  Comparator #(.width(4), .mode("unsigned")) comparator_2 (
    .a(counter_1_q), .b(4'b0100), .eq(comparator_2_eq));  // open: gt, lt
  Multiplier #(.width(5)) multiplier_1 (
    .a({1'b0, counter_1_q}), .b(5'b01010), .out(multiplier_1_out), .cin({5{1'b0}}));  // open: cout
  Adder #(.width(5)) adder_1 (.a({1'b0, unit_q}), .b(multiplier_1_out), .out(input_conf), .cin(1'b0));  // open: cout

  // Other names for the same wires on the sheet: sw = switch_stop
endmodule

module Conj_m (
  input  RAZ,
  input  clk,
  input  switch_stop,
  input  bouton,
  output [3:0] input_conf
);

  wire and_1_out, comparator_1_eq, or_1_out;

  or or_1 (or_1_out, comparator_1_eq, RAZ);
  and and_1 (and_1_out, switch_stop, bouton);
  Counter #(.width(4), .max('hf)) counter_1 (
    .clr(or_1_out), .load(1'b0), .up(1'b1), .count(and_1_out), .clk(clk), .D(4'b0000), .Q(input_conf));  // open: carry
  Comparator #(.width(4), .mode("unsigned")) comparator_1 (
    .a(input_conf), .b(4'b1101), .eq(comparator_1_eq));  // open: gt, lt

  // Other names for the same wires on the sheet: sw = switch_stop
endmodule

module Conf_a (
  input  RAZ,
  input  clk,
  input  switch_stop,
  input  bouton_unit,
  input  bouton_diz,
  output [6:0] input_conf
);

  wire and_1_out, and_2_out, comparator_1_eq, comparator_2_eq, or_1_out, or_2_out;
  wire [3:0] counter_1_q, counter_2_q;
  wire [6:0] multiplier_1_out;

  and and_1 (and_1_out, switch_stop, bouton_unit);
  or or_1 (or_1_out, comparator_1_eq, RAZ);
  or or_2 (or_2_out, comparator_2_eq, RAZ);
  and and_2 (and_2_out, switch_stop, bouton_diz);
  Counter #(.width(4), .max('hf)) counter_1 (
    .clr(or_1_out), .load(1'b0), .up(1'b1), .count(and_1_out), .clk(clk), .D(4'b0000), .Q(counter_1_q));  // open: carry
  Counter #(.width(4), .max('hf)) counter_2 (
    .clr(or_2_out), .load(1'b0), .up(1'b1), .count(and_2_out), .clk(clk), .D(4'b0000), .Q(counter_2_q));  // open: carry
  Comparator #(.width(4), .mode("unsigned")) comparator_1 (
    .a(counter_1_q), .b(4'b1010), .eq(comparator_1_eq));  // open: gt, lt
  Comparator #(.width(4), .mode("unsigned")) comparator_2 (
    .a(counter_2_q), .b(4'b1010), .eq(comparator_2_eq));  // open: gt, lt
  Multiplier #(.width(7)) multiplier_1 (
    .a({3'b000, counter_2_q}), .b(7'b0001010), .out(multiplier_1_out), .cin({7{1'b0}}));  // open: cout
  Adder #(.width(7)) adder_1 (
    .a({3'b000, counter_1_q}), .b(multiplier_1_out), .out(input_conf), .cin(1'b0));  // open: cout

  // Other names for the same wires on the sheet: sw = switch_stop
endmodule
