// Logisim project Montre4.circ as structural Verilog: 13 circuits, main circuit Montre
module Montre (
  input  affichage,
  input  RAZ,
  input  load,
  input  switch_stop,
  input  bouton_unit,
  input  conf,
  output [1:0] affich,
  output [1:0] confi
);

  wire and_1_out, annees_bisex, clk, clk_2Hz_out, clk_2kHz, clk_enable, comparator_1_gt,
       demultiplexer_1_out0, demultiplexer_1_out1, demultiplexer_1_out2, demultiplexer_2_out0,
       demultiplexer_2_out1, demultiplexer_2_out2, demultiplexer_3_out0, demultiplexer_3_out1,
       demultiplexer_4_out0, demultiplexer_4_out1, heures_clk_heure, jours_clk_jour, minutes_clk_min,
       moiss_clk_mois, not_1_out, or1_out, or_1_out, secondes_clk_sec;
  wire [3:0] bcd_to_7_segment_decoder_1_p1, bcd_to_7_segment_decoder_2_p1, bcd_to_7_segment_decoder_3_p1,
       bcd_to_7_segment_decoder_4_p1, bcd_to_7_segment_decoder_5_p1, bcd_to_7_segment_decoder_6_p1,
       binairy_to_bcd_converter_1_p2, binairy_to_bcd_converter_1_p3, binairy_to_bcd_converter_2_p2,
       binairy_to_bcd_converter_3_p1, binairy_to_bcd_converter_3_p3, binairy_to_bcd_converter_3_p4,
       binairy_to_bcd_converter_4_p2, binairy_to_bcd_converter_4_p3, binairy_to_bcd_converter_4_p5,
       binairy_to_bcd_converter_4_p6, i_m, m, undriven_3;
  wire [4:0] h, h_j, i_h, i_hex3, i_j, j, multiplexer_4_out;
  wire [5:0] i_min, i_s, min, min_m, s, s_m;
  wire [5:5] Conf_jour_input_conf, undriven;
  wire [6:0] i_a1, i_a2, i_hex1, i_hex2, in_adiz, in_aunit, multiplexer_7_out, multiplexer_8_out,
       multiplier_2_out, multiplier_3_out;
  wire [6:4] undriven_2, undriven_4, undriven_5, undriven_6;
  wire [11:0] a, i_a, multiplier_1_out;

  Clock u_clk_2kHz (.out(clk_2kHz));
  Clock #(.highDuration(125), .lowDuration(125)) clk_16Hz (.out(clk));
  // FSM_Entity #(.content("fsm bouton2 @[ 50 , 50 , 800 , 500 ] { in B [ 1 ] @[ 50 , 100 , 14 , 15 ] ; in\naffich [ 2 ] @[ 50 , 139 , 70 , 15 ] ; out confi [ 2 ] @[ 784 , 140 , 66 , 15 ]\n; codeWidth = 4 ; reset = S0 ; state S0 = \"0000\" @[ 127 , 192 , 30 , 30 ] {\ncommands @[ 172 , 207 , 74 , 21 ] { confi = \"00\" ; } transitions { S0 -> S1\nwhen B == \"1\" @[ 226 , 122 , 62 , 21 ] ; } } state S1 = \"0001\" @[ 378 , 127 ,\n30 , 30 ] { commands @[ 370 , 118 , 74 , 21 ] { confi = \"01\" ; } transitions {\nS1 -> S2 when B == \"0\" @[ 484 , 117 , 62 , 21 ] ; } } state S2 = \"0010\" @[ 540\n, 165 , 30 , 30 ] { commands @[ 585 , 180 , 74 , 21 ] { confi = \"01\" ; }\ntransitions { S2 -> S3 when B == \"1\" . affich == \"00\" @[ 617 , 225 , 166 , 21 ]\n; S2 -> S5 when B == \"1\" . ( affich == \"01\" + affich == \"10\" ) @[ 399 , 293 ,\n276 , 21 ] ; } } state S3 = \"0011\" @[ 619 , 323 , 30 , 30 ] { commands @[ 664 ,\n338 , 74 , 21 ] { confi = \"10\" ; } transitions { S3 -> S4 when B == \"0\" @[ 644\n, 425 , 62 , 21 ] ; } } state S4 = \"0100\" @[ 514 , 432 , 30 , 30 ] { commands\n@[ 547 , 473 , 74 , 21 ] { confi = \"10\" ; } transitions { S4 -> S5 when B ==\n\"1\" @[ 442 , 503 , 62 , 21 ] ; } } state S5 = \"0101\" @[ 222 , 396 , 30 , 30 ] {\ncommands @[ 267 , 411 , 74 , 21 ] { confi = \"00\" ; } transitions { S5 -> S0\nwhen B == \"0\" @[ 93 , 317 , 62 , 21 ] ; } } }")) mach2: pin names not known; wires that end beside it: clk_2kHz, affichage, 1'b1, conf, affich, confi
  Clock #(.highDuration(1000), .lowDuration(1000)) clk_2Hz (.out(clk_2Hz_out));
  // FSM_Entity #(.content("fsm bouton @[ 50 , 50 , 800 , 500 ] { in A [ 1 ] @[ 50 , 165 , 14 , 15 ] ; out\naffich [ 2 ] @[ 780 , 121 , 70 , 15 ] ; codeWidth = 4 ; reset = S0 ; state S0 =\n\"0000\" @[ 142 , 184 , 30 , 30 ] { commands @[ 113 , 168 , 78 , 21 ] { affich =\n\"00\" ; } transitions { S0 -> S1 when A == \"1\" @[ 233 , 136 , 62 , 21 ] ; } }\nstate S1 = \"0001\" @[ 299 , 97 , 30 , 30 ] { commands @[ 302 , 89 , 78 , 21 ] {\naffich = \"01\" ; } transitions { S1 -> S2 when A == \"0\" @[ 444 , 112 , 62 , 21 ]\n; } } state S2 = \"0010\" @[ 520 , 106 , 30 , 30 ] { commands @[ 565 , 121 , 78 ,\n21 ] { affich = \"01\" ; } transitions { S2 -> S3 when A == \"1\" @[ 659 , 185 , 62\n, 21 ] ; } } state S3 = \"0011\" @[ 704 , 234 , 30 , 30 ] { commands @[ 749 , 249\n, 78 , 21 ] { affich = \"10\" ; } transitions { S3 -> S4 when A == \"0\" @[ 712 ,\n340 , 62 , 21 ] ; } } state S4 = \"0100\" @[ 631 , 398 , 30 , 30 ] { commands @[\n676 , 413 , 78 , 21 ] { affich = \"10\" ; } transitions { S4 -> S5 when A == \"1\"\n@[ 393 , 451 , 62 , 21 ] ; } } state S5 = \"0111\" @[ 185 , 382 , 30 , 30 ] {\ncommands @[ 153 , 423 , 78 , 21 ] { affich = \"00\" ; } transitions { S5 -> S0\nwhen A == \"0\" @[ 116 , 287 , 62 , 21 ] ; } } }")) mach1: pin names not known; wires that end beside it: clk_2kHz, 1'b0, 1'b1, affichage, affich
  Demultiplexer #(.select(2), .enable("false")) demultiplexer_1 (
    .out0(demultiplexer_1_out0), .out1(demultiplexer_1_out1), .out2(demultiplexer_1_out2), .in(bouton_unit),
    .sel(affich));  // open: out3
  Seconde secondes (
    .clk(clk_2Hz_out), .RAZ(RAZ), .load(load), .Input_sec(i_s), .clk_enable(clk_enable),
    .clk_sec(secondes_clk_sec), .secondes(s));
  Demultiplexer #(.select(2), .enable("false")) demultiplexer_2 (
    .out0(demultiplexer_2_out0), .out1(demultiplexer_2_out1), .out2(demultiplexer_2_out2),
    .in(demultiplexer_1_out0), .sel(confi));  // open: out3
  Demultiplexer #(.select(2), .enable("false")) demultiplexer_3 (
    .out0(demultiplexer_3_out0), .out1(demultiplexer_3_out1), .in(demultiplexer_1_out1), .sel(confi));  // open: out2, out3
  Demultiplexer #(.select(2), .enable("false")) demultiplexer_4 (
    .out0(demultiplexer_4_out0), .out1(demultiplexer_4_out1), .in(demultiplexer_1_out2), .sel(confi));  // open: out2, out3
  Minute minutes (
    .clk(clk_2Hz_out), .clk_sec(secondes_clk_sec), .RAZ(RAZ), .load(load), .Input_heure(i_min),
    .clk_enable(clk_enable), .clk_min(minutes_clk_min), .minutes(min));
  Multiplexer #(.width(5), .enable("false")) multiplexer_1 (.in0(h), .in1({5{1'b0}}), .out(h_j), .sel(affich[0]));
  Multiplexer #(.width(6), .enable("false")) multiplexer_2 (.in0(min), .in1({1'b0, j}), .out(min_m), .sel(affich[0]));
  Multiplexer #(.width(6), .enable("false")) multiplexer_3 (.in0(s), .in1({2'b00, m}), .out(s_m), .sel(affich[0]));
  Heure heures (
    .clk(clk_2Hz_out), .clk_min(minutes_clk_min), .clk_sec(secondes_clk_sec), .RAZ(RAZ), .load(load),
    .Input_heure(i_h), .clk_heure(heures_clk_heure), .heures(h));
  Comparator #(.width(12), .mode("unsigned")) comparator_1 (
    .a(i_a), .b({12{1'b1}}), .gt(comparator_1_gt));  // open: eq, lt
  or or1 (or1_out, affich[0], affich[1]);
  or or_1 (or_1_out, RAZ, comparator_1_gt);
  Multiplexer #(.width(5), .enable("false")) multiplexer_4 (
    .in0(h_j), .in1(i_hex3), .out(multiplexer_4_out), .sel(switch_stop));
  _7_Segment_Display Hex5 (.dp(1'b1));  // open: g, f, a, b, e, d, c
  _7_Segment_Display Hex6 (.dp(1'b0));  // open: g, f, a, b, e, d, c
  // BCD_to_7_Segment_decoder bcd_to_7_segment_decoder_1: pin names not known; wires that end beside it: bcd_to_7_segment_decoder_1_p1
  // BCD_to_7_Segment_decoder bcd_to_7_segment_decoder_2: pin names not known; wires that end beside it: bcd_to_7_segment_decoder_2_p1
  Multiplexer #(.width(4), .enable("false")) multiplexer_5 (
    .in0(binairy_to_bcd_converter_1_p2), .in1(4'b0000), .out(bcd_to_7_segment_decoder_1_p1), .sel(or1_out));
  Multiplexer #(.width(4), .enable("false")) multiplexer_6 (
    .in0(binairy_to_bcd_converter_1_p3), .in1(4'b0000), .out(bcd_to_7_segment_decoder_2_p1), .sel(or1_out));
  // Binairy_to_BCD_converter #(.binvalue(5)) binairy_to_bcd_converter_1: pin names not known; wires that end beside it: multiplexer_4_out, binairy_to_bcd_converter_1_p2, binairy_to_bcd_converter_1_p3
  Multiplexer #(.width(7), .enable("false")) multiplexer_7 (
    .in0({1'b0, min_m}), .in1(i_hex2), .out(multiplexer_7_out), .sel(switch_stop));
  _7_Segment_Display Hex4 ();  // open: g, f, a, b, e, d, c, dp
  // BCD_to_7_Segment_decoder bcd_to_7_segment_decoder_3: pin names not known; wires that end beside it: bcd_to_7_segment_decoder_3_p1
  // Binairy_to_BCD_converter #(.binvalue(7)) binairy_to_bcd_converter_2: pin names not known; wires that end beside it: multiplexer_7_out, binairy_to_bcd_converter_2_p2
  Jour jours (
    .clk(clk_2Hz_out), .clk_sec(secondes_clk_sec), .clk_min(minutes_clk_min), .clk_h(heures_clk_heure),
    .RAZ(RAZ), .load(load), .Input_jour(i_j), .mois(m), .bisex(annees_bisex), .clk_jour(jours_clk_jour),
    .jours(j));
  // BCD_to_7_Segment_decoder bcd_to_7_segment_decoder_4: pin names not known; wires that end beside it: bcd_to_7_segment_decoder_4_p1
  _7_Segment_Display Hex3 (.dp(1'b1));  // open: g, f, a, b, e, d, c
  Multiplexer #(.width(7), .enable("false")) multiplexer_8 (
    .in0({1'b0, s_m}), .in1(i_hex1), .out(multiplexer_8_out), .sel(switch_stop));
  Conf_sec_min conf_sec (
    .RAZ(RAZ), .clk(clk), .switch_stop(switch_stop), .bouton_unit(demultiplexer_2_out0), .input_sec_min(s),
    .input_conf(i_s));
  Conf_sec_min conf_min (
    .RAZ(RAZ), .clk(clk), .switch_stop(switch_stop), .bouton_unit(demultiplexer_2_out1), .input_sec_min(min),
    .input_conf(i_min));
  Conf_h conf_heure (
    .RAZ(RAZ), .clk(clk), .switch_stop(switch_stop), .bouton_unit(demultiplexer_2_out2), .input_h(h),
    .input_conf(i_h));
  Conf_j Conf_jour (
    .RAZ(RAZ), .clk(clk), .switch_stop(switch_stop), .bouton_unit(demultiplexer_3_out1),
    .input_j({undriven[5], j}), .input_conf({Conf_jour_input_conf[5], i_j}));
  Conj_m Conf_m (
    .RAZ(RAZ), .clk(clk), .switch_stop(switch_stop), .bouton(demultiplexer_3_out0), .input_m(m),
    .input_conf(i_m));
  Conf_a Conf_a1 (
    .RAZ(or_1_out), .clk(clk), .switch_stop(switch_stop), .bouton_unit(demultiplexer_4_out0),
    .input_a(in_aunit), .input_conf(i_a1));
  Conf_a Conf_a2 (
    .RAZ(or_1_out), .clk(clk), .switch_stop(switch_stop), .bouton_unit(demultiplexer_4_out1),
    .input_a(in_adiz), .input_conf(i_a2));
  // BCD_to_7_Segment_decoder bcd_to_7_segment_decoder_5: pin names not known; wires that end beside it: bcd_to_7_segment_decoder_5_p1
  _7_Segment_Display Hex2 (.dp(1'b0));  // open: g, f, a, b, e, d, c
  not not_1 (not_1_out, switch_stop);
  // Binairy_to_BCD_converter #(.binvalue(7)) binairy_to_bcd_converter_3: pin names not known; wires that end beside it: binairy_to_bcd_converter_3_p1, multiplexer_8_out, binairy_to_bcd_converter_3_p3, binairy_to_bcd_converter_3_p4
  // BCD_to_7_Segment_decoder bcd_to_7_segment_decoder_6: pin names not known; wires that end beside it: bcd_to_7_segment_decoder_6_p1
  _7_Segment_Display Hex1 (.dp(1'b0));  // open: g, f, a, b, e, d, c
  and and_1 (and_1_out, not_1_out, affich[1]);
  Multiplier #(.width(12)) multiplier_1 (
    .a({{5{1'b0}}, i_a2}), .b(12'h64), .out(multiplier_1_out), .cin({12{1'b0}}));  // open: cout
  Mois moiss (
    .clk(clk_2Hz_out), .clk_sec(secondes_clk_sec), .clk_min(minutes_clk_min), .clk_h(heures_clk_heure),
    .clk_j(jours_clk_jour), .RAZ(RAZ), .load(load), .Input_mois(i_m), .clk_mois(moiss_clk_mois), .mois(m));
  Adder #(.width(12)) adder_1 (.a({{5{1'b0}}, i_a1}), .b(multiplier_1_out), .out(i_a), .cin(1'b0));  // open: cout
  Multiplexer #(.width(4), .enable("false")) multiplexer_9 (
    .in0(binairy_to_bcd_converter_2_p2), .in1(binairy_to_bcd_converter_4_p2),
    .out(bcd_to_7_segment_decoder_3_p1), .sel(and_1_out));
  Multiplexer #(.width(4), .enable("false")) multiplexer_10 (
    .in0(binairy_to_bcd_converter_3_p1), .in1(binairy_to_bcd_converter_4_p3),
    .out(bcd_to_7_segment_decoder_4_p1), .sel(and_1_out));
  // Binairy_to_BCD_converter #(.binvalue(12)) binairy_to_bcd_converter_4: pin names not known; wires that end beside it: a, binairy_to_bcd_converter_4_p2, binairy_to_bcd_converter_4_p3, clk_2Hz_out, binairy_to_bcd_converter_4_p5, binairy_to_bcd_converter_4_p6
  Multiplexer #(.width(4), .enable("false")) multiplexer_11 (
    .in0(binairy_to_bcd_converter_3_p3), .in1(binairy_to_bcd_converter_4_p5),
    .out(bcd_to_7_segment_decoder_5_p1), .sel(and_1_out));
  Multiplexer #(.select(2), .width(7), .enable("false")) multiplexer_12 (
    .in0({1'b0, i_s}), .in1({3'b000, i_m}), .in2(i_a1), .in3({7{1'b0}}), .out(i_hex1), .sel(affich));
  Multiplexer #(.select(2), .width(7), .enable("false")) multiplexer_13 (
    .in0({1'b0, i_min}), .in1({2'b00, i_j}), .in2(i_a2), .in3({7{1'b0}}), .out(i_hex2), .sel(affich));
  Multiplexer #(.select(2), .width(5), .enable("false")) multiplexer_14 (
    .in0(i_h), .in1({5{1'b0}}), .in2({5{1'b0}}), .in3({5{1'b0}}), .out(i_hex3), .sel(affich));
  Multiplexer #(.width(4), .enable("false")) multiplexer_15 (
    .in0(binairy_to_bcd_converter_3_p4), .in1(binairy_to_bcd_converter_4_p6),
    .out(bcd_to_7_segment_decoder_6_p1), .sel(and_1_out));
  Annee annees (
    .clk(clk_2Hz_out), .clk_sec(secondes_clk_sec), .clk_min(minutes_clk_min), .clk_h(heures_clk_heure),
    .clk_j(jours_clk_jour), .clk_m(moiss_clk_mois), .RAZ(RAZ), .load(load), .Input_Annee(i_a), .Annee(a),
    .bisex(annees_bisex));
  Multiplier #(.width(7)) multiplier_2 (
    .a({undriven_4, undriven_3}), .b(7'b0001010), .out(multiplier_2_out), .cin({7{1'b0}}));  // open: cout
  Multiplier #(.width(7)) multiplier_3 (
    .a({undriven_6, binairy_to_bcd_converter_4_p6}), .b(7'b0001010), .out(multiplier_3_out), .cin({7{1'b0}}));  // open: cout
  Adder #(.width(7)) adder_2 (
    .a({undriven_2, binairy_to_bcd_converter_4_p3}), .b(multiplier_2_out), .out(in_adiz), .cin(1'b0));  // open: cout
  Adder #(.width(7)) adder_3 (
    .a({undriven_5, binairy_to_bcd_converter_4_p5}), .b(multiplier_3_out), .out(in_aunit), .cin(1'b0));  // open: cout

  // Other names for the same wires on the sheet: af = affichage; sw = switch_stop

  // Notes on the sheet:
  //   Mettre frequence d'horloge FPGA à 2 kHz
endmodule

module Seconde (
  input  clk,
  input  RAZ,
  input  load,
  input  [5:0] Input_sec,
  input  clk_enable,
  output clk_sec,
  output [5:0] secondes
);

  wire comparator_1_eq, comparator_1_gt, or2_out, or3_out;

  or or2 (or2_out, RAZ, or3_out);
  Counter #(.width(6), .max('h3b)) csec (
    .clr(or2_out), .load(load), .up(1'b1), .count(1'b1), .clk(clk), .D(Input_sec), .Q(secondes));  // open: carry
  or or3 (or3_out, comparator_1_gt, comparator_1_eq);
  Comparator #(.width(6), .mode("unsigned")) comparator_1 (
    .a(secondes), .b(6'b111100), .gt(comparator_1_gt), .eq(comparator_1_eq));  // open: lt
  Comparator #(.width(6), .mode("unsigned")) comparator_2 (.a(secondes), .b(6'b111011), .eq(clk_sec));  // open: gt, lt
endmodule

module Minute (
  input  clk,
  input  clk_sec,
  input  RAZ,
  input  load,
  input  [5:0] Input_heure,
  input  clk_enable,
  output clk_min,
  output [5:0] minutes
);

  wire comparator_1_eq, comparator_1_gt, or4_out, or5_out;

  or or4 (or4_out, RAZ, or5_out);
  Counter #(.width(6), .max('h3b)) cmin (
    .clr(or4_out), .load(load), .up(1'b1), .count(clk_sec), .clk(clk), .D(Input_heure), .Q(minutes));  // open: carry
  or or5 (or5_out, comparator_1_gt, comparator_1_eq);
  Comparator #(.width(6), .mode("unsigned")) comparator_1 (
    .a(minutes), .b(6'b111100), .gt(comparator_1_gt), .eq(comparator_1_eq));  // open: lt
  Comparator #(.width(6), .mode("unsigned")) comparator_2 (.a(minutes), .b(6'b111011), .eq(clk_min));  // open: gt, lt
endmodule

module Heure (
  input  clk,
  input  clk_min,
  input  clk_sec,
  input  RAZ,
  input  load,
  input  [4:0] Input_heure,
  output clk_heure,
  output [4:0] heures
);

  wire and3_out, comparator_1_eq, comparator_1_gt, or6_out, or7_out;

  and and3 (and3_out, clk_min, clk_sec);
  or or6 (or6_out, RAZ, or7_out);
  Counter #(.width(5), .max('h17)) cheure (
    .clr(or6_out), .load(load), .up(1'b1), .count(and3_out), .clk(clk), .D(Input_heure), .Q(heures));  // open: carry
  or or7 (or7_out, comparator_1_gt, comparator_1_eq);
  Comparator #(.width(5), .mode("unsigned")) comparator_1 (
    .a(heures), .b(5'b11000), .gt(comparator_1_gt), .eq(comparator_1_eq));  // open: lt
  Comparator #(.width(5), .mode("unsigned")) comparator_2 (.a(heures), .b(5'b10111), .eq(clk_heure));  // open: gt, lt
endmodule

module Jour (
  input  clk,
  input  clk_sec,
  input  clk_min,
  input  clk_h,
  input  RAZ,
  input  load,
  input  [4:0] Input_jour,
  input  [3:0] mois,
  input  bisex,
  output clk_jour,
  output [4:0] jours
);

  wire and_1_out, and_2_out, and_3_out, and_4_out, and_5_out, bit0, bit1, bit2, bit3, bit4, clear,
       comparator_1_eq, comparator_2_eq, comparator_3_eq, comparator_4_eq, comparator_5_eq, comparator_6_eq,
       comparator_7_eq, comparator_8_eq, comparator_9_eq, comparator_10_eq, comparator_11_eq,
       comparator_12_eq, comparator_13_gt, comparator_14_gt, comparator_15_gt, comparator_16_gt,
       comparator_17_eq, comparator_18_eq, comparator_19_eq, comparator_20_eq, multiplexer_1_out,
       multiplexer_2_out, multiplexer_3_out, multiplexer_4_out, multiplexer_5_out, not_1_out, not_2_out,
       not_3_out, not_4_out, or_1_out, or_2_out;
  wire [1:0] or_4_out;
  wire [4:0] subtractor_1_out;

  and and_1 (and_1_out, clk_sec, clk_min, clk_h);
  Subtractor #(.width(5)) subtractor_1 (
    .a(Input_jour), .b(5'b00001), .out(subtractor_1_out), .bin(1'b0));  // open: bout
  and and_2 (and_2_out, bit0, bit1, bit2, bit3, bit4);
  Comparator #(.width(4), .mode("unsigned")) comparator_1 (
    .a(mois), .b(4'b0001), .eq(comparator_1_eq));  // open: gt, lt
  Comparator #(.width(4), .mode("unsigned")) comparator_2 (
    .a(mois), .b(4'b0010), .eq(comparator_2_eq));  // open: gt, lt
  Comparator #(.width(4), .mode("unsigned")) comparator_3 (
    .a(mois), .b(4'b0011), .eq(comparator_3_eq));  // open: gt, lt
  Comparator #(.width(4), .mode("unsigned")) comparator_4 (
    .a(mois), .b(4'b0100), .eq(comparator_4_eq));  // open: gt, lt
  Comparator #(.width(4), .mode("unsigned")) comparator_5 (
    .a(mois), .b(4'b0101), .eq(comparator_5_eq));  // open: gt, lt
  Comparator #(.width(4), .mode("unsigned")) comparator_6 (
    .a(mois), .b(4'b0110), .eq(comparator_6_eq));  // open: gt, lt
  Comparator #(.width(4), .mode("unsigned")) comparator_7 (
    .a(mois), .b(4'b0111), .eq(comparator_7_eq));  // open: gt, lt
  Comparator #(.width(4), .mode("unsigned")) comparator_8 (
    .a(mois), .b(4'b1000), .eq(comparator_8_eq));  // open: gt, lt
  Comparator #(.width(4), .mode("unsigned")) comparator_9 (
    .a(mois), .b(4'b1001), .eq(comparator_9_eq));  // open: gt, lt
  Comparator #(.width(4), .mode("unsigned")) comparator_10 (
    .a(mois), .b(4'b1010), .eq(comparator_10_eq));  // open: gt, lt
  Comparator #(.width(4), .mode("unsigned")) comparator_11 (
    .a(mois), .b(4'b1011), .eq(comparator_11_eq));  // open: gt, lt
  Comparator #(.width(4), .mode("unsigned")) comparator_12 (
    .a(mois), .b(4'b1100), .eq(comparator_12_eq));  // open: gt, lt
  Counter #(.width(5), .max('h1f)) counter_1 (
    .clr(clear), .load(load), .up(1'b1), .count(and_1_out), .clk(clk), .D(subtractor_1_out),
    .Q({bit4, bit3, bit2, bit1, bit0}));  // open: carry
  not not_1 (not_1_out, bit0);
  and and_3 (and_3_out, not_1_out, bit1, bit2, bit3, bit4);
  or or_1 (or_1_out, comparator_1_eq, comparator_3_eq, comparator_5_eq, comparator_7_eq, comparator_8_eq, comparator_10_eq, comparator_12_eq);
  or or_2 (or_2_out, comparator_4_eq, comparator_6_eq, comparator_9_eq, comparator_11_eq);
  not not_2 (not_2_out, bit1);
  not not_3 (not_3_out, bit0);
  not not_4 (not_4_out, bit1);
  or or_3 (or_4_out[1], or_1_out, or_2_out);
  Adder #(.width(5)) adder_1 (.a({bit4, bit3, bit2, bit1, bit0}), .b(5'b00001), .out(jours), .cin(1'b0));  // open: cout
  Comparator #(.width(5), .mode("unsigned")) comparator_13 (
    .a({bit4, bit3, bit2, bit1, bit0}), .b({5{1'b1}}), .gt(comparator_13_gt));  // open: eq, lt
  Comparator #(.width(5), .mode("unsigned")) comparator_14 (
    .a({bit4, bit3, bit2, bit1, bit0}), .b(5'b11110), .gt(comparator_14_gt));  // open: eq, lt
  Comparator #(.width(5), .mode("unsigned")) comparator_15 (
    .a({bit4, bit3, bit2, bit1, bit0}), .b(5'b11100), .gt(comparator_15_gt));  // open: eq, lt
  Comparator #(.width(5), .mode("unsigned")) comparator_16 (
    .a({bit4, bit3, bit2, bit1, bit0}), .b(5'b11101), .gt(comparator_16_gt));  // open: eq, lt
  and and_4 (and_4_out, bit0, not_2_out, bit2, bit3, bit4);
  and and_5 (and_5_out, not_3_out, not_4_out, bit2, bit3, bit4);
  Multiplexer #(.enable("false")) multiplexer_1 (
    .in0(comparator_15_gt), .in1(comparator_16_gt), .out(multiplexer_1_out), .sel(bisex));
  Multiplexer #(.enable("false")) multiplexer_2 (
    .in0(and_5_out), .in1(and_4_out), .out(multiplexer_2_out), .sel(bisex));
  or or_4 (or_4_out[0], or_1_out, comparator_2_eq);
  Multiplexer #(.select(2), .enable("false")) multiplexer_3 (
    .in0(and_2_out), .in1(multiplexer_2_out), .in2(and_3_out), .in3(and_2_out), .out(multiplexer_3_out),
    .sel(or_4_out));
  Comparator #(.width(5), .mode("unsigned")) comparator_17 (
    .a(jours), .b({5{1'b1}}), .eq(comparator_17_eq));  // open: gt, lt
  Comparator #(.width(5), .mode("unsigned")) comparator_18 (
    .a(jours), .b(5'b11110), .eq(comparator_18_eq));  // open: gt, lt
  Comparator #(.width(5), .mode("unsigned")) comparator_19 (
    .a(jours), .b(5'b11100), .eq(comparator_19_eq));  // open: gt, lt
  Comparator #(.width(5), .mode("unsigned")) comparator_20 (
    .a(jours), .b(5'b11101), .eq(comparator_20_eq));  // open: gt, lt
  Multiplexer #(.select(2), .enable("false")) multiplexer_4 (
    .in0(comparator_13_gt), .in1(multiplexer_1_out), .in2(comparator_14_gt), .in3(comparator_13_gt),
    .out(multiplexer_4_out), .sel(or_4_out));
  Multiplexer #(.enable("false")) multiplexer_5 (
    .in0(comparator_19_eq), .in1(comparator_20_eq), .out(multiplexer_5_out), .sel(bisex));
  or or_5 (clear, RAZ, multiplexer_4_out, multiplexer_3_out);
  Multiplexer #(.select(2), .enable("false")) multiplexer_6 (
    .in0(comparator_17_eq), .in1(multiplexer_5_out), .in2(comparator_18_eq), .in3(comparator_17_eq),
    .out(clk_jour), .sel(or_4_out));
endmodule

module Mois (
  input  clk,
  input  clk_sec,
  input  clk_min,
  input  clk_h,
  input  clk_j,
  input  RAZ,
  input  load,
  input  [3:0] Input_mois,
  output clk_mois,
  output [3:0] mois
);

  wire and_1_out, comparator_1_eq, comparator_1_gt, or_1_out, or_2_out;
  wire [3:0] counter_1_q, subtractor_1_out;

  and and_1 (and_1_out, clk_sec, clk_min, clk_h, clk_j);
  or or_1 (or_1_out, RAZ, or_2_out);
  Subtractor #(.width(4)) subtractor_1 (.a(Input_mois), .b(4'b0001), .out(subtractor_1_out), .bin(1'b0));  // open: bout
  Counter #(.width(4), .max('hc)) counter_1 (
    .clr(or_1_out), .load(load), .up(1'b1), .count(and_1_out), .clk(clk), .D(subtractor_1_out),
    .Q(counter_1_q));  // open: carry
  or or_2 (or_2_out, comparator_1_gt, comparator_1_eq);
  Comparator #(.width(4), .mode("unsigned")) comparator_1 (
    .a(counter_1_q), .b(4'b1100), .gt(comparator_1_gt), .eq(comparator_1_eq));  // open: lt
  Adder #(.width(4)) adder_1 (.a(counter_1_q), .b(4'b0001), .out(mois), .cin(1'b0));  // open: cout
  Comparator #(.width(4), .mode("unsigned")) comparator_2 (.a(mois), .b(4'b1100), .eq(clk_mois));  // open: gt, lt
endmodule

module Annee (
  input  clk,
  input  clk_sec,
  input  clk_min,
  input  clk_h,
  input  clk_j,
  input  clk_m,
  input  RAZ,
  input  load,
  input  [11:0] Input_Annee,
  output [11:0] Annee,
  output bisex
);

  wire and_1_out, comparator_1_eq, or_1_out;
  wire [2:0] adder_1_out, counter_2_q;

  or or_1 (or_1_out, RAZ, comparator_1_eq);
  and and_1 (and_1_out, clk_sec, clk_min, clk_h, clk_j, clk_m);
  Counter #(.width(12), .max('hfff)) counter_1 (
    .clr(RAZ), .load(load), .up(1'b1), .count(and_1_out), .clk(clk), .D(Input_Annee), .Q(Annee));  // open: carry
  Counter #(.width(3), .max('h7)) counter_2 (
    .clr(or_1_out), .load(1'b0), .up(1'b1), .count(1'b1), .clk(clk), .D(3'b000), .Q(counter_2_q));  // open: carry
  Adder #(.width(3)) adder_1 (.a(counter_2_q), .b(3'b001), .out(adder_1_out));  // open: cin, cout
  Comparator #(.width(3), .mode("unsigned")) comparator_1 (
    .a(adder_1_out), .b(3'b101), .eq(comparator_1_eq));  // open: gt, lt
  Comparator #(.width(3), .mode("unsigned")) comparator_2 (.a(adder_1_out), .b(3'b100), .eq(bisex));  // open: gt, lt
endmodule

module Conf_sec_min (
  input  RAZ,
  input  clk,
  input  switch_stop,
  input  bouton_unit,
  input  [5:0] input_sec_min,
  output [5:0] input_conf
);

  wire and_1_out, comparator_1_eq, or1_out, switch_p5;

  // FSM_Entity #(.content("fsm example @[ 50 , 50 , 800 , 500 ] { in sw [ 1 ] @[ 50 , 120 , 22 , 15 ] ; out\nX [ 1 ] @[ 837 , 140 , 13 , 15 ] ; codeWidth = 2 ; reset = S0 ; state S0 = \"01\"\n@[ 297 , 181 , 30 , 30 ] { commands @[ 265 , 173 , 43 , 21 ] { X = \"1\" ; }\ntransitions { S0 -> S1 when sw == \"1\" @[ 412 , 152 , 70 , 21 ] ; } } state S1 =\n\"10\" @[ 470 , 186 , 30 , 30 ] { commands @[ 541 , 190 , 43 , 21 ] { X = \"0\" ; }\ntransitions { S1 -> S2 when default @[ 499 , 292 , 50 , 21 ] ; } } state S2 =\n\"00\" @[ 370 , 292 , 30 , 30 ] { commands @[ 415 , 307 , 43 , 21 ] { X = \"0\" ; }\ntransitions { S2 -> S0 when sw == \"0\" @[ 304 , 266 , 70 , 21 ] ; } } }")) switch: pin names not known; wires that end beside it: clk, 1'b0, 1'b1, switch_stop, switch_p5
  and and_1 (and_1_out, switch_stop, bouton_unit);
  or or1 (or1_out, comparator_1_eq, RAZ);
  Counter #(.width(6), .max('h3b)) unit (
    .clr(or1_out), .load(switch_p5), .up(1'b1), .count(and_1_out), .clk(clk), .D(input_sec_min),
    .Q(input_conf));  // open: carry
  Comparator #(.width(6), .mode("unsigned")) comparator_1 (
    .a(input_conf), .b(6'b111100), .eq(comparator_1_eq));  // open: gt, lt

  // Other names for the same wires on the sheet: sw = switch_stop
endmodule

module Conf_h (
  input  RAZ,
  input  clk,
  input  switch_stop,
  input  bouton_unit,
  input  [4:0] input_h,
  output [4:0] input_conf
);

  wire and6_out, comparator_1_eq, or5_out, switch_p5;

  // FSM_Entity #(.content("fsm example @[ 50 , 50 , 800 , 500 ] { in sw [ 1 ] @[ 50 , 100 , 22 , 15 ] ; out\nX [ 1 ] @[ 837 , 140 , 13 , 15 ] ; codeWidth = 2 ; reset = S0 ; state S0 = \"01\"\n@[ 297 , 181 , 30 , 30 ] { commands @[ 265 , 173 , 43 , 21 ] { X = \"1\" ; }\ntransitions { S0 -> S1 when sw == \"1\" @[ 432 , 151 , 70 , 21 ] ; } } state S1 =\n\"10\" @[ 470 , 186 , 30 , 30 ] { commands @[ 541 , 190 , 43 , 21 ] { X = \"0\" ; }\ntransitions { S1 -> S2 when default @[ 556 , 286 , 50 , 21 ] ; } } state S2 =\n\"00\" @[ 395 , 296 , 30 , 30 ] { commands @[ 439 , 311 , 43 , 21 ] { X = \"0\" ; }\ntransitions { S2 -> S0 when sw == \"0\" @[ 328 , 277 , 70 , 21 ] ; } } }")) switch: pin names not known; wires that end beside it: clk, 1'b0, 1'b1, switch_stop, switch_p5
  and and6 (and6_out, switch_stop, bouton_unit);
  or or5 (or5_out, comparator_1_eq, RAZ);
  Counter #(.width(5), .max('h17)) unit (
    .clr(or5_out), .load(switch_p5), .up(1'b1), .count(and6_out), .clk(clk), .D(input_h), .Q(input_conf));  // open: carry
  Comparator #(.width(5), .mode("unsigned")) comparator_1 (
    .a(input_conf), .b(5'b11000), .eq(comparator_1_eq));  // open: gt, lt

  // Other names for the same wires on the sheet: sw = switch_stop
endmodule

module Conf_j (
  input  RAZ,
  input  clk,
  input  switch_stop,
  input  bouton_unit,
  input  [5:0] input_j,
  output [5:0] input_conf
);

  wire and8_out, comparator_1_eq, or7_out, switch_p5;
  wire [5:0] subtractor_1_out, unit_q;

  // FSM_Entity #(.content("fsm example @[ 50 , 50 , 800 , 500 ] { in sw [ 1 ] @[ 50 , 100 , 22 , 15 ] ; out\nX [ 1 ] @[ 837 , 140 , 13 , 15 ] ; codeWidth = 2 ; reset = S0 ; state S0 = \"01\"\n@[ 297 , 181 , 30 , 30 ] { commands @[ 265 , 173 , 43 , 21 ] { X = \"1\" ; }\ntransitions { S0 -> S1 when sw == \"1\" @[ 432 , 151 , 70 , 21 ] ; } } state S1 =\n\"10\" @[ 515 , 216 , 30 , 30 ] { commands @[ 560 , 231 , 43 , 21 ] { X = \"0\" ; }\ntransitions { S1 -> S2 when default @[ 506 , 324 , 50 , 21 ] ; } } state S2 =\n\"00\" @[ 402 , 314 , 30 , 30 ] { commands @[ 426 , 363 , 43 , 21 ] { X = \"0\" ; }\ntransitions { S2 -> S0 when sw == \"0\" @[ 305 , 280 , 70 , 21 ] ; } } }")) switch: pin names not known; wires that end beside it: clk, 1'b0, 1'b1, switch_stop, switch_p5
  Subtractor #(.width(6)) subtractor_1 (.a(input_j), .b(6'b000001), .out(subtractor_1_out), .bin(1'b0));  // open: bout
  or or7 (or7_out, comparator_1_eq, RAZ);
  and and8 (and8_out, switch_stop, bouton_unit);
  Counter #(.width(6), .max('h1f)) unit (
    .clr(or7_out), .load(switch_p5), .up(1'b1), .count(and8_out), .clk(clk), .D(subtractor_1_out), .Q(unit_q));  // open: carry
  Adder #(.width(6)) adder_1 (.a(unit_q), .b(6'b000001), .out(input_conf), .cin(1'b0));  // open: cout
  Comparator #(.width(6), .mode("unsigned")) comparator_1 (
    .a(unit_q), .b(6'b011111), .eq(comparator_1_eq));  // open: gt, lt

  // Other names for the same wires on the sheet: sw = switch_stop
endmodule

module Conj_m (
  input  RAZ,
  input  clk,
  input  switch_stop,
  input  bouton,
  input  [3:0] input_m,
  output [3:0] input_conf
);

  wire and_1_out, comparator_1_eq, or_1_out, switch_p5;
  wire [3:0] counter_1_q, subtractor_1_out;

  Subtractor #(.width(4)) subtractor_1 (.a(input_m), .b(4'b0001), .out(subtractor_1_out), .bin(1'b0));  // open: bout
  // FSM_Entity #(.content("fsm example @[ 50 , 50 , 800 , 500 ] { in sw [ 1 ] @[ 50 , 102 , 22 , 15 ] ; out\nX [ 1 ] @[ 837 , 140 , 13 , 15 ] ; codeWidth = 2 ; reset = S0 ; state S0 = \"01\"\n@[ 297 , 181 , 30 , 30 ] { commands @[ 272 , 175 , 43 , 21 ] { X = \"1\" ; }\ntransitions { S0 -> S1 when sw == \"1\" @[ 432 , 151 , 70 , 21 ] ; } } state S1 =\n\"10\" @[ 470 , 186 , 30 , 30 ] { commands @[ 541 , 190 , 43 , 21 ] { X = \"0\" ; }\ntransitions { S1 -> S2 when default @[ 489 , 292 , 50 , 21 ] ; } } state S2 =\n\"00\" @[ 355 , 298 , 30 , 30 ] { commands @[ 399 , 313 , 43 , 21 ] { X = \"0\" ; }\ntransitions { S2 -> S0 when sw == \"0\" @[ 263 , 281 , 70 , 21 ] ; } } }")) switch: pin names not known; wires that end beside it: clk, 1'b0, 1'b1, switch_stop, switch_p5
  or or_1 (or_1_out, comparator_1_eq, RAZ);
  and and_1 (and_1_out, switch_stop, bouton);
  Counter #(.width(4), .max('hc)) counter_1 (
    .clr(or_1_out), .load(switch_p5), .up(1'b1), .count(and_1_out), .clk(clk), .D(subtractor_1_out),
    .Q(counter_1_q));  // open: carry
  Adder #(.width(4)) adder_1 (.a(counter_1_q), .b(4'b0001), .out(input_conf), .cin(1'b0));  // open: cout
  Comparator #(.width(4), .mode("unsigned")) comparator_1 (
    .a(counter_1_q), .b(4'b1100), .eq(comparator_1_eq));  // open: gt, lt

  // Other names for the same wires on the sheet: sw = switch_stop
endmodule

module Conf_a (
  input  RAZ,
  input  clk,
  input  switch_stop,
  input  bouton_unit,
  input  [6:0] input_a,
  output [6:0] input_conf
);

  wire and_1_out, comparator_1_eq, or_1_out, switch_p5;

  // FSM_Entity #(.content("fsm example @[ 50 , 50 , 800 , 500 ] { in sw [ 1 ] @[ 50 , 100 , 22 , 15 ] ; out\nX [ 1 ] @[ 837 , 140 , 13 , 15 ] ; codeWidth = 2 ; reset = S0 ; state S0 = \"01\"\n@[ 297 , 181 , 30 , 30 ] { commands @[ 265 , 173 , 43 , 21 ] { X = \"1\" ; }\ntransitions { S0 -> S1 when sw == \"1\" @[ 432 , 151 , 70 , 21 ] ; } } state S1 =\n\"10\" @[ 470 , 186 , 30 , 30 ] { commands @[ 541 , 190 , 43 , 21 ] { X = \"0\" ; }\ntransitions { S1 -> S2 when default @[ 493 , 275 , 50 , 21 ] ; } } state S2 =\n\"00\" @[ 392 , 288 , 30 , 30 ] { commands @[ 441 , 324 , 43 , 21 ] { X = \"0\" ; }\ntransitions { S2 -> S0 when sw == \"0\" @[ 304 , 298 , 70 , 21 ] ; } } }")) switch: pin names not known; wires that end beside it: clk, 1'b0, 1'b1, switch_stop, switch_p5
  and and_1 (and_1_out, switch_stop, bouton_unit);
  or or_1 (or_1_out, comparator_1_eq, RAZ);
  Counter #(.width(7), .max('h63)) counter_1 (
    .clr(or_1_out), .load(switch_p5), .up(1'b1), .count(and_1_out), .clk(clk), .D(input_a), .Q(input_conf));  // open: carry
  Comparator #(.width(7), .mode("unsigned")) comparator_1 (
    .a(input_conf), .b(7'b1100100), .eq(comparator_1_eq));  // open: gt, lt

  // Other names for the same wires on the sheet: sw = switch_stop
endmodule

module Clk_Hz (
  input  clk,
  output clk_2Hz,
  output clk_16Hz
);

  wire comparator_1_eq, comparator_2_eq;
  wire [4:0] counter_2_q;
  wire [9:0] counter_1_q;

  Counter #(.width(10), .max('h3e8)) counter_1 (
    .load(1'b0), .up(1'b1), .count(1'b1), .clk(clk), .D({10{1'b0}}), .Q(counter_1_q));  // open: clr, carry
  Counter #(.width(5), .max('h10)) counter_2 (
    .load(1'b0), .up(1'b1), .count(1'b1), .clk(clk), .D({5{1'b0}}), .Q(counter_2_q));  // open: clr, carry
  Comparator #(.width(10), .mode("unsigned")) comparator_1 (
    .a(counter_1_q), .b(10'h3e8), .eq(comparator_1_eq));  // open: gt, lt
  Comparator #(.width(5), .mode("unsigned")) comparator_2 (
    .a(counter_2_q), .b(5'b10000), .eq(comparator_2_eq));  // open: gt, lt
  // FSM_Entity #(.content("fsm example @[ 50 , 50 , 800 , 500 ] { in x [ 1 ] @[ 50 , 100 , 12 , 15 ] ; out\nclk [ 1 ] @[ 827 , 140 , 23 , 15 ] ; codeWidth = 2 ; reset = S0 ; state S0 =\n\"01\" @[ 297 , 181 , 30 , 30 ] { commands @[ 265 , 173 , 53 , 21 ] { clk = \"0\" ;\n} transitions { S0 -> S1 when x == \"1\" @[ 432 , 151 , 60 , 21 ] ; } } state S1\n= \"10\" @[ 522 , 185 , 30 , 30 ] { commands @[ 567 , 200 , 53 , 21 ] { clk = \"1\"\n; } transitions { S1 -> S0 when default @[ 423 , 273 , 50 , 21 ] ; } } }")) Clk2Hz: pin names not known; wires that end beside it: clk, 1'b0, 1'b1, comparator_1_eq, clk_2Hz
  // FSM_Entity #(.content("fsm example @[ 50 , 50 , 800 , 500 ] { in x [ 1 ] @[ 50 , 100 , 12 , 15 ] ; out\nclk [ 1 ] @[ 827 , 140 , 23 , 15 ] ; codeWidth = 2 ; reset = S0 ; state S0 =\n\"01\" @[ 297 , 181 , 30 , 30 ] { commands @[ 265 , 173 , 53 , 21 ] { clk = \"0\" ;\n} transitions { S0 -> S1 when x == \"1\" @[ 432 , 151 , 60 , 21 ] ; } } state S1\n= \"10\" @[ 558 , 193 , 30 , 30 ] { commands @[ 604 , 208 , 30 , 20 ] { }\ntransitions { S1 -> S0 when default @[ 415 , 277 , 50 , 21 ] ; } } }")) Clk16Hz: pin names not known; wires that end beside it: clk, 1'b0, 1'b1, comparator_2_eq, clk_16Hz
endmodule
