// Logisim project TP1.circ as structural Verilog: 1 circuit, main circuit main
module main (
  input  in_1,
  input  in_2,
  input  in_3,
  input  [3:0] in_4,
  input  [3:0] in_5,
  input  [3:0] Y,
  input  [3:0] X,
  input  in_8,
  input  in_9,
  input  [3:0] Y_2,
  input  in_11,
  input  [3:0] X_2,
  output out_13,
  output [3:0] out_14,
  output out_15,
  output [3:0] out_16,
  output [3:0] out_17,
  output [3:0] out_18,
  output out_19
);

  wire nor_1_out, nor_2_out;

  nor nor_1 (nor_1_out, in_1, in_1);
  nor nor_2 (nor_2_out, in_2, in_2);
  Multiplexer #(.width(4), .enable("false")) multiplexer_1 (.in0(Y), .in1(X), .out(out_16), .sel(in_8));
  Adder #(.width(4)) adder_1 (.a(in_4), .b(in_5), .out(out_14), .cin(in_3), .cout(out_15));
  Adder #(.width(4)) adder_2 (.a(Y_2), .b(X_2), .out(out_17), .cin(in_9), .cout(out_19));
  nor nor_3 (out_13, nor_1_out, nor_2_out);
  Multiplexer #(.width(4), .enable("false")) multiplexer_2 (.in0(out_17), .in1(X_2), .out(out_18), .sel(in_11));

  // Notes on the sheet:
  //   Exercice 2 : Additionneur
  //   Exercice 1 : PORTE ET : / (a/ + b/) = a . b
  //   Exercice 3 : 3.1 Multiplexeurs
  //   Exercice 3 : 3.2 Multiplexeurs avec Additionneur
endmodule
