// Logisim project TP2.circ as structural Verilog: 1 circuit, main circuit main
module main (
  input  [3:0] in_1,
  input  [3:0] in_2,
  input  [3:0] in_3,
  input  in_4,
  input  [3:0] in_5,
  input  [3:0] in_6,
  output out_7,
  output out_8,
  output out_9,
  output [3:0] out_10,
  output out_11
);

  wire adder_1_cout, and_1_out, and_2_out, and_3_out, and_4_out, and_6_out, and_7_out, and_8_out, and_9_out,
       and_10_out, nor_1_out, not_1_out, not_2_out, or_1_out;
  wire [2:2] and_11_out;
  wire [3:0] adder_1_out;

  Adder #(.width(4)) adder_1 (.a(in_5), .b(in_6), .out(adder_1_out), .cin(in_4), .cout(adder_1_cout));
  and and_1 (and_1_out, in_1[1], in_1[3]);
  not not_1 (not_1_out, in_1[2]);
  and and_2 (and_2_out, in_2[0], in_2[1]);
  nor nor_1 (nor_1_out, in_3[2], in_3[3]);
  not not_2 (not_2_out, in_3[2]);
  and and_3 (and_3_out, in_3[0], in_3[1]);
  and and_4 (and_4_out, not_2_out, in_3[3]);
  and and_5 (out_7, and_1_out, not_1_out);
  and and_6 (and_6_out, and_2_out, in_2[2]);
  and and_7 (and_7_out, and_3_out, nor_1_out);
  and and_8 (and_8_out, and_3_out, and_4_out);
  or or_1 (or_1_out, adder_1_out[1], adder_1_out[2]);
  and and_9 (and_9_out, adder_1_out[3], 1'b1);
  or or_2 (out_8, and_6_out, in_2[3]);
  nor nor_2 (out_9, and_7_out, and_8_out);
  and and_10 (and_10_out, or_1_out, and_9_out);
  or or_3 (out_11, adder_1_cout, and_10_out);
  and and_11 (and_11_out[2], 1'b1, out_11);
  Adder #(.width(4)) adder_2 (.a(adder_1_out), .b({1'b0, {2{and_11_out[2]}}, 1'b0}), .out(out_10));  // open: cin, cout

  // Notes on the sheet:
  //   Exercice 1 :
  //   f1(x)
  //   f2(x)
  //   f3(x)
  //   Exercice 2 :
endmodule
