// Logisim project TP3.circ as structural Verilog: 3 circuits, main circuit main
module main (
  input  [3:0] X,
  input  [3:0] Y,
  input  [3:0] Z,
  input  X_2,
  input  Y_2,
  input  in_6,
  input  in_7,
  input  [3:0] X_3,
  input  [3:0] Y_3,
  output [5:0] out_10,
  output [2:0] out_11,
  output Sup,
  output Inf
);

  wire adder_1_cout, adder_2_cout, and_1_out, and_2_out, and_4_out, and_5_out, and_6_out, comp1_1_inf,
       comp1_1_sup, comp1_2_inf, comp1_2_sup, comp1_3_inf, comp1_3_sup, comp1_4_inf, comp1_4_sup, exp2_1_inf,
       exp2_1_sup, exp2_2_inf, exp2_2_sup, xor_1_out, xor_2_out, xor_5_out;
  wire [3:0] adder_1_out;

  Adder #(.width(4)) adder_1 (.a(X), .b(Y), .out(adder_1_out), .cout(adder_1_cout));  // open: cin
  xor xor_1 (xor_1_out, X_2, Y_2);
  and and_1 (and_1_out, X_2, Y_2);
  xor xor_2 (xor_2_out, in_6, in_7);
  and and_2 (and_2_out, in_6, in_7);
  COMP1 comp1_1 (.X(X_3[3]), .Y(Y_3[3]), .Sup(comp1_1_sup), .Inf(comp1_1_inf));
  COMP1 comp1_2 (.X(X_3[2]), .Y(Y_3[2]), .Sup(comp1_2_sup), .Inf(comp1_2_inf));
  COMP1 comp1_3 (.X(X_3[1]), .Y(Y_3[1]), .Sup(comp1_3_sup), .Inf(comp1_3_inf));
  COMP1 comp1_4 (.X(X_3[0]), .Y(Y_3[0]), .Sup(comp1_4_sup), .Inf(comp1_4_inf));
  Adder #(.width(4)) adder_2 (.a(adder_1_out), .b(Z), .out(out_10[3:0]), .cout(adder_2_cout));  // open: cin
  xor xor_3 (out_10[4], adder_2_cout, adder_1_cout);
  and and_3 (out_10[5], adder_2_cout, adder_1_cout);
  EXP2 exp2_1 (
    .Sup_MSB(comp1_1_sup), .Inf_MSB(comp1_1_inf), .Sup_LSB(comp1_2_sup), .Inf_LSB(comp1_2_inf),
    .Sup(exp2_1_sup), .Inf(exp2_1_inf));
  EXP2 exp2_2 (
    .Sup_MSB(comp1_3_sup), .Inf_MSB(comp1_3_inf), .Sup_LSB(comp1_4_sup), .Inf_LSB(comp1_4_inf),
    .Sup(exp2_2_sup), .Inf(exp2_2_inf));
  xor xor_4 (out_11[0], xor_1_out, xor_2_out);
  and and_4 (and_4_out, xor_1_out, xor_2_out);
  xor xor_5 (xor_5_out, and_1_out, and_2_out);
  xor xor_6 (out_11[1], xor_5_out, and_4_out);
  and and_5 (and_5_out, and_4_out, xor_5_out);
  and and_6 (and_6_out, and_1_out, and_2_out);
  EXP2 exp2_3 (
    .Sup_MSB(exp2_1_sup), .Inf_MSB(exp2_1_inf), .Sup_LSB(exp2_2_sup), .Inf_LSB(exp2_2_inf), .Sup(Sup),
    .Inf(Inf));
  or or_1 (out_11[2], and_5_out, and_6_out);

  // Notes on the sheet:
  //   Exercice 1 :
  //   Exercice 2 :
  //   Exercice 3 :
endmodule

module COMP1 (
  input  X,
  input  Y,
  output Sup,
  output Inf
);

  wire not_1_out, not_2_out;

  not not_1 (not_1_out, Y);
  not not_2 (not_2_out, X);
  and and_1 (Sup, X, not_1_out);
  and and_2 (Inf, Y, not_2_out);
endmodule

module EXP2 (
  input  Sup_MSB,
  input  Inf_MSB,
  input  Sup_LSB,
  input  Inf_LSB,
  output Sup,
  output Inf
);

  wire and_1_out, and_2_out, nor_1_out;

  nor nor_1 (nor_1_out, Inf_MSB, Sup_MSB);
  and and_1 (and_1_out, nor_1_out, Sup_LSB);
  and and_2 (and_2_out, nor_1_out, Inf_LSB);
  xor xor_1 (Sup, Sup_MSB, and_1_out);
  xor xor_2 (Inf, Inf_MSB, and_2_out);
endmodule
