// Logisim project TP4.circ as structural Verilog: 6 circuits, main circuit main
module main (
  input  [3:0] X,
  input  [3:0] Y,
  input  [2:0] I,
  output [3:0] R,
  output CY,
  output O
);

  wire and_2_out, not_1_out, or_1_out;
  wire [1:1] and_1_out;
  wire [3:0] ad_sous_1_s, oplog_1_r;

  and and_1 (and_1_out[1], I[1], I[2]);
  or or_1 (or_1_out, I[1], I[2]);
  not not_1 (not_1_out, or_1_out);
  and and_2 (and_2_out, I[0], not_1_out);
  AD_SOUS ad_sous_1 (.X(X), .Y(Y), .AS(and_2_out), .S(ad_sous_1_s), .CY(CY), .O(O));
  OPLOG oplog_1 (.X(X), .Y(Y), .L1L0({and_1_out[1], I[0]}), .R(oplog_1_r));
  Multiplexer #(.width(4), .enable("false")) multiplexer_1 (
    .in0(ad_sous_1_s), .in1(oplog_1_r), .out(R), .sel(or_1_out));
endmodule

module ET_ID (
  input  [3:0] A,
  input  [3:0] B,
  input  et,
  output [3:0] S
);

  wire [3:0] and_1_out;

  and and_1 (and_1_out[0], A[0], B[0]);
  and and_2 (and_1_out[1], A[1], B[1]);
  and and_3 (and_1_out[2], A[2], B[2]);
  and and_4 (and_1_out[3], A[3], B[3]);
  Multiplexer #(.width(4), .enable("false")) multiplexer_1 (.in0(B), .in1(and_1_out), .out(S), .sel(et));
endmodule

module INVCOND (
  input  [3:0] A,
  input  Inv,
  output [3:0] B
);

  xor xor_1 (B[0], A[0], Inv);
  xor xor_2 (B[1], A[1], Inv);
  xor xor_3 (B[2], A[2], Inv);
  xor xor_4 (B[3], A[3], Inv);
endmodule

module OPLOG (
  input  [3:0] X,
  input  [3:0] Y,
  input  [1:0] L1L0,
  output [3:0] R
);

  wire [3:0] invcond_1_b;

  INVCOND invcond_1 (.A(Y), .Inv(L1L0[0]), .B(invcond_1_b));
  ET_ID et_id_1 (.A(X), .B(invcond_1_b), .et(L1L0[1]), .S(R));
endmodule

module AD_SOUS (
  input  [3:0] X,
  input  [3:0] Y,
  input  AS,
  output [3:0] S,
  output CY,
  output O
);

  wire [3:0] add4group_1_s, invcond_1_b;

  INVCOND invcond_1 (.A(Y), .Inv(AS), .B(invcond_1_b));
  ADD4GROUP add4group_1 (.Cin(1'b0), .A(invcond_1_b), .B({3'b000, AS}), .S(add4group_1_s), .Cout(O));
  ADD4GROUP add4group_2 (.Cin(1'b0), .A(X), .B(add4group_1_s), .S(S), .Cout(CY));
endmodule

module ADD4GROUP (
  input  Cin,
  input  [3:0] A,
  input  [3:0] B,
  output [3:0] S,
  output Cout
);

  Adder #(.width(4)) adder_1 (.a(A), .b(B), .out(S), .cin(Cin), .cout(Cout));
endmodule
