// Logisim project TP5.circ as structural Verilog: 3 circuits, main circuit main
module main (
  input  in_1,
  input  [3:0] in_2,
  input  [3:0] in_3,
  input  [3:0] in_4,
  input  [3:0] in_5,
  input  [3:0] E,
  input  RAZ,
  output [1:0] Re,
  output out_9,
  output [3:0] out_10,
  output [3:0] out_11,
  output out_12,
  output [3:0] out_13,
  output [3:0] out_14,
  output [3:0] out_15
);

  wire and_1_out, and_2_out, and_3_out, clk_out, clock_1_out, clock_2_out, d_ff_1_qn, not_1_out, not_2_out,
       not_3_out, not_4_out, xor_1_out;
  wire [3:0] register_1_q, register_2_q, register_3_q, register_4_q;

  Clock clock_1 (.out(clock_1_out));
  Clock clk (.out(clk_out));
  not not_1 (not_1_out, clk_out);
  Clock clock_2 (.out(clock_2_out));
  D_Flip_Flop d_ff_1 (.D(d_ff_1_qn), .clk(clock_1_out), .Q(Re[0]), .Qn(d_ff_1_qn));  // open: preset, reset
  Register #(.width(4)) register_1 (.D(E), .en(1'b1), .clk(not_1_out), .Q(register_1_q));  // open: clr
  Counter #(.width(4), .max('hf)) counter_1 (
    .clr(RAZ), .load(1'b0), .up(1'b1), .count(not_4_out), .clk(clock_2_out), .Q(out_15));  // open: D, carry
  Register #(.width(4)) register_2 (.D(register_1_q), .en(1'b1), .clk(not_1_out), .Q(register_2_q));  // open: clr
  xor xor_1 (xor_1_out, Re[0], Re[1]);
  ADDEC2 addec2_1 (
    .Re(in_1), .X_MSB(in_2), .X_LSB(in_3), .Y_MSB(in_4), .Y_LSB(in_5), .Rs(out_9), .S_MSB(out_10),
    .S_LSB(out_11));
  D_Flip_Flop d_ff_2 (.D(xor_1_out), .clk(clock_1_out), .Q(Re[1]));  // open: Qn, preset, reset
  Register #(.width(4)) register_3 (.D(register_2_q), .en(1'b1), .clk(not_1_out), .Q(register_3_q));  // open: clr
  Register #(.width(4)) register_4 (.D(register_3_q), .en(1'b1), .clk(not_1_out), .Q(register_4_q));  // open: clr
  not not_2 (not_2_out, out_15[1]);
  not not_3 (not_3_out, out_15[3]);
  and and_1 (and_1_out, out_15[0], out_15[2]);
  and and_2 (and_2_out, not_2_out, not_3_out);
  ADDEC2 addec2_2 (
    .Re(1'b0), .X_MSB(register_3_q), .X_LSB(register_4_q), .Y_MSB(register_1_q), .Y_LSB(register_2_q),
    .Rs(out_12), .S_MSB(out_13), .S_LSB(out_14));
  and and_3 (and_3_out, and_1_out, and_2_out);
  not not_4 (not_4_out, and_3_out);

  // Notes on the sheet:
  //   Exercice 2 :
  //   Exercice 1 :
  //   Exercice 3 :
endmodule

module ADDEC1 (
  input  in_1,
  input  [3:0] in_2,
  input  [3:0] in_3,
  output [3:0] out_4,
  output out_5
);

  wire adder_1_cout, and_1_out, and_2_out, or_1_out;
  wire [2:2] and_3_out;
  wire [3:0] adder_1_out;

  Adder #(.width(4)) adder_1 (.a(in_2), .b(in_3), .out(adder_1_out), .cin(in_1), .cout(adder_1_cout));
  or or_1 (or_1_out, adder_1_out[1], adder_1_out[2]);
  and and_1 (and_1_out, adder_1_out[3], 1'b1);
  and and_2 (and_2_out, or_1_out, and_1_out);
  or or_2 (out_5, adder_1_cout, and_2_out);
  and and_3 (and_3_out[2], 1'b1, out_5);
  Adder #(.width(4)) adder_2 (.a(adder_1_out), .b({1'b0, {2{and_3_out[2]}}, 1'b0}), .out(out_4));  // open: cin, cout
endmodule

module ADDEC2 (
  input  Re,
  input  [3:0] X_MSB,
  input  [3:0] X_LSB,
  input  [3:0] Y_MSB,
  input  [3:0] Y_LSB,
  output Rs,
  output [3:0] S_MSB,
  output [3:0] S_LSB
);

  wire addec1_1_out_5;

  ADDEC1 addec1_1 (.in_1(Re), .in_2(X_LSB), .in_3(Y_LSB), .out_4(S_LSB), .out_5(addec1_1_out_5));
  ADDEC1 addec1_2 (.in_1(addec1_1_out_5), .in_2(X_MSB), .in_3(Y_MSB), .out_4(S_MSB), .out_5(Rs));

  // Notes on the sheet:
  //   ,
endmodule
