// Logisim project TP6.circ as structural Verilog: 1 circuit, main circuit main
module main (
  input  RAZ,
  input  in_2,
  input  in_3,
  input  in_4,
  input  in_5,
  input  in_6,
  input  in_7,
  input  in_8,
  input  in_9,
  input  in_10,
  input  in_11,
  output out_12,
  output out_13,
  output out_14,
  output out_15
);

  wire clock_1_out, clock_2_out, clock_3_out;

  Clock clock_1 (.out(clock_1_out));
  Clock clock_2 (.out(clock_2_out));
  Clock clock_3 (.out(clock_3_out));
  // FSM_Entity #(.content("fsm Machinejeton @[ 50 , 50 , 800 , 500 ] { in req [ 1 ] @[ 50 , 123 , 27 , 15 ]\n; in end [ 1 ] @[ 50 , 161 , 30 , 15 ] ; out Start [ 1 ] @[ 813 , 140 , 37 , 15\n] ; out Ack [ 1 ] @[ 822 , 174 , 28 , 15 ] ; codeWidth = 4 ; reset = A ; state\nA = \"1000\" @[ 234 , 135 , 30 , 30 ] { commands @[ 219 , 125 , 67 , 36 ] { Start\n= \"0\" ; Ack = \"0\" ; } transitions { A -> B when req @[ 437 , 112 , 27 , 21 ] ;\n} } state B = \"0100\" @[ 605 , 132 , 30 , 30 ] { commands @[ 645 , 111 , 67 , 36\n] { Start = \"1\" ; Ack = \"0\" ; } transitions { B -> C when / req @[ 692 , 262 ,\n41 , 21 ] ; } } state C = \"0010\" @[ 602 , 382 , 30 , 30 ] { commands @[ 645 ,\n425 , 67 , 36 ] { Start = \"0\" ; Ack = \"0\" ; } transitions { C -> D when end @[\n411 , 457 , 30 , 21 ] ; } } state D = \"0001\" @[ 243 , 381 , 30 , 30 ] {\ncommands @[ 210 , 435 , 67 , 36 ] { Start = \"0\" ; Ack = \"1\" ; } transitions { D\n-> A when / req @[ 210 , 277 , 41 , 21 ] ; } } }")) fsm_entity_1: pin names not known; wires that end beside it: clock_1_out, RAZ, in_2, in_3, out_12
  // FSM_Entity #(.content("fsm Codagedense @[ 50 , 50 , 800 , 500 ] { in req [ 1 ] @[ 50 , 137 , 27 , 15 ]\n; in end [ 1 ] @[ 50 , 174 , 30 , 15 ] ; out Start [ 1 ] @[ 813 , 140 , 37 , 15\n] ; out Ack [ 1 ] @[ 822 , 176 , 28 , 15 ] ; codeWidth = 2 ; reset = A ; state\nA = \"00\" @[ 258 , 137 , 30 , 30 ] { commands @[ 211 , 123 , 67 , 36 ] { Start =\n\"0\" ; Ack = \"0\" ; } transitions { A -> B when req @[ 393 , 118 , 27 , 21 ] ; }\n} state B = \"01\" @[ 498 , 145 , 30 , 30 ] { commands @[ 528 , 119 , 67 , 36 ] {\nStart = \"1\" ; Ack = \"0\" ; } transitions { B -> C when / req @[ 621 , 254 , 41 ,\n21 ] ; } } state C = \"10\" @[ 526 , 369 , 30 , 30 ] { commands @[ 571 , 384 , 67\n, 36 ] { Start = \"0\" ; Ack = \"0\" ; } transitions { C -> D when end @[ 381 , 433\n, 30 , 21 ] ; } } state D = \"11\" @[ 233 , 378 , 30 , 30 ] { commands @[ 212 ,\n430 , 67 , 36 ] { Start = \"0\" ; Ack = \"1\" ; } transitions { D -> A when / end\n@[ 158 , 269 , 44 , 21 ] ; } } }")) fsm_entity_2: pin names not known; wires that end beside it: in_4, clock_2_out, in_5, in_6, in_7, out_13, out_14
  // FSM_Entity #(.content("fsm Genclock @[ 50 , 50 , 800 , 500 ] { in attente [ 1 ] @[ 50 , 100 , 53 , 15 ]\n; codeWidth = 2 ; reset = t1 ; state t1 = \"01\" @[ 300 , 188 , 30 , 30 ] {\ncommands @[ 345 , 203 , 30 , 20 ] { } transitions { t1 -> t2 when / attente @[\n432 , 151 , 67 , 21 ] ; } } state t2 = \"10\" @[ 624 , 175 , 30 , 30 ] { commands\n@[ 669 , 190 , 30 , 20 ] { } transitions { t2 -> t3 when / attente @[ 606 , 341\n, 67 , 21 ] ; } } state t3 = \"00\" @[ 452 , 361 , 30 , 30 ] { commands @[ 497 ,\n376 , 30 , 20 ] { } transitions { t3 -> t1 when / attente @[ 326 , 349 , 67 ,\n21 ] ; } } }")) fsm_entity_3: pin names not known; wires that end beside it: in_8, clock_3_out, in_9, in_10, in_11, out_15

  // Notes on the sheet:
  //   Machine à jetons
endmodule
