// Logisim project TP6_Codagedense.circ as structural Verilog: 1 circuit, main circuit main
module main (
  input  reset,
  output Start,
  output X,
  output etatA,
  output Y,
  output etatB,
  output Ack,
  output etatC,
  output etatD
);

  wire and_1_out, and_3_out, and_4_out, and_5_out, and_6_out, and_8_out, clk, DX, DY, end1, n_end, n_req,
       n_reset, not_4_out, not_5_out, not_6_out, not_7_out, or_1_out, or_3_out, req;

  Clock #(.highDuration(4), .lowDuration(4)) u_req (.out(req));
  Clock #(.highDuration(4), .lowDuration(3)) end2 (.out(end1));
  Clock u_clk (.out(clk));
  Clock sysclk ();  // open: out
  not not_1 (n_req, req);
  not not_2 (n_end, end1);
  not not_3 (n_reset, reset);
  and and_1 (and_1_out, DX, n_reset);
  D_Flip_Flop A (.D(and_1_out), .clk(clk), .Q(X));  // open: Qn, preset, reset
  not not_4 (not_4_out, X);
  not not_5 (not_5_out, Y);
  and and_2 (etatA, not_4_out, not_5_out);
  and and_3 (and_3_out, etatA, req);
  and and_4 (and_4_out, etatC, end1);
  and and_5 (and_5_out, Ack, req);
  or or_1 (or_1_out, and_3_out, and_4_out);
  or or_2 (DX, or_1_out, and_5_out);
  and and_6 (and_6_out, DY, n_reset);
  not not_6 (not_6_out, Y);
  D_Flip_Flop B (.D(and_6_out), .clk(clk), .Q(Y));  // open: Qn, preset, reset
  and and_7 (etatB, X, not_6_out);
  or or_3 (or_3_out, etatB, etatC);
  and and_8 (and_8_out, Ack, req);
  not not_7 (not_7_out, X);
  or or_4 (DY, or_3_out, and_8_out);
  and and_9 (etatC, not_7_out, Y);
  and and_10 (Ack, X, Y);

  assign etatD = Ack;
  assign Start = etatB;

  // Other names for the same wires on the sheet: A = etatA; B = etatB; C = etatC; D = Ack; QX = X; QY = Y

  // Notes on the sheet:
  //   Codage dense
endmodule
