// Logisim project TP6_GENCLOCK.circ as structural Verilog: 1 circuit, main circuit main
module main (
  input  HE,
  input  attente,
  input  reset,
  output X,
  output E,
  output Y,
  output t1,
  output t2,
  output t3
);

  wire and_2_out, and_4_out, DX, DY, n_attente, n_reset, not_3_out, not_4_out, not_5_out, not_6_out,
       or_1_out, or_2_out;

  not not_1 (n_attente, attente);
  not not_2 (n_reset, reset);
  not not_3 (not_3_out, X);
  not not_4 (not_4_out, Y);
  and and_1 (E, not_3_out, not_4_out);
  or or_1 (or_1_out, E, t3);
  and and_2 (and_2_out, t2, n_attente);
  D_Flip_Flop A (.D(or_2_out), .clk(HE), .Q(X));  // open: Qn, preset, reset
  or or_2 (or_2_out, DX, reset);
  or or_3 (DX, or_1_out, and_2_out);
  not not_5 (not_5_out, Y);
  and and_3 (t1, X, not_5_out);
  and and_4 (and_4_out, DY, n_reset);
  or or_4 (DY, t1, t2);
  D_Flip_Flop B (.D(and_4_out), .clk(HE), .Q(Y));  // open: Qn, preset, reset
  not not_6 (not_6_out, X);
  and and_5 (t2, not_6_out, Y);
  and and_6 (t3, X, Y);

  // Other names for the same wires on the sheet: QX = X; QY = Y

  // Notes on the sheet:
  //   Genclock
endmodule
