// Logisim project TP6_Machinejeton.circ as structural Verilog: 1 circuit, main circuit main
module main (
  input  req,
  input  end1,
  input  reset,
  output etatA,
  output etatB,
  output Start,
  output etatC,
  output Ack,
  output etatD
);

  wire and_1_out, and_2_out, and_3_out, and_5_out, and_6_out, and_7_out, and_8_out, and_9_out, clk, DA, DB,
       DC, DD, n_end, n_req, n_reset, or_1_out;

  Clock u_clk (.out(clk));
  not not_1 (n_req, req);
  not not_2 (n_end, end1);
  not not_3 (n_reset, reset);
  D_Flip_Flop A (.D(or_1_out), .clk(clk), .Q(etatA));  // open: Qn, preset, reset
  or or_1 (or_1_out, DA, reset);
  and and_1 (and_1_out, etatA, n_req);
  and and_2 (and_2_out, Ack, n_req);
  or or_2 (DA, and_1_out, and_2_out);
  D_Flip_Flop B (.D(and_3_out), .clk(clk), .Q(etatB));  // open: Qn, preset, reset
  and and_3 (and_3_out, DB, n_reset);
  and and_4 (DB, req, etatA);
  and and_5 (and_5_out, DC, n_reset);
  D_Flip_Flop C (.D(and_5_out), .clk(clk), .Q(etatC));  // open: Qn, preset, reset
  and and_6 (and_6_out, n_end, etatC);
  or or_3 (DC, and_6_out, etatB);
  and and_7 (and_7_out, DD, n_reset);
  D_Flip_Flop D (.D(and_7_out), .clk(clk), .Q(Ack));  // open: Qn, preset, reset
  and and_8 (and_8_out, end1, etatC);
  and and_9 (and_9_out, req, Ack);
  or or_4 (DD, and_8_out, and_9_out);

  assign etatD = Ack;
  assign Start = etatB;

  // Other names for the same wires on the sheet: QA = etatA; QB = etatB; QC = etatC; QD = Ack

  // Notes on the sheet:
  //   Codage dense
  //   Machine à jetons
endmodule
