// Logisim project Keypad_Afficheur.circ as structural Verilog: 2 circuits, main circuit Traducteur
module Clavier (
  input  clk,
  input  Ligne0,
  input  Ligne1,
  input  Ligne2,
  input  Ligne3,
  output [3:0] Clavier,
  output Colonne0,
  output Colonne1,
  output Colonne2,
  output Colonne3
);

  wire and_1_out, and_2_out, and_3_out, and_4_out, and_5_out, and_6_out, and_7_out, and_8_out, and_9_out,
       and_10_out, and_11_out, and_12_out, and_13_out, and_14_out, machine0_p4, or_1_out, or_2_out, or_4_out,
       or_5_out, or_6_out, or_8_out, or_10_out, or_11_out, or_12_out;

  // FSM_Entity #(.content("fsm titi @[ 50 , 50 , 800 , 500 ] { in x [ 1 ] @[ 50 , 125 , 12 , 15 ] ; out C0\n[ 1 ] @[ 828 , 140 , 22 , 15 ] ; out C1 [ 1 ] @[ 828 , 170 , 22 , 15 ] ; out C2\n[ 1 ] @[ 828 , 202 , 22 , 15 ] ; out C3 [ 1 ] @[ 828 , 232 , 22 , 15 ] ;\ncodeWidth = 2 ; reset = A ; state A = \"00\" @[ 300 , 200 , 30 , 30 ] { commands\n@[ 260 , 156 , 52 , 66 ] { C0 = \"1\" ; C1 = \"0\" ; C2 = \"0\" ; C3 = \"0\" ; }\ntransitions { A -> B when x == \"1\" @[ 400 , 150 , 60 , 21 ] ; } } state B =\n\"01\" @[ 487 , 189 , 30 , 30 ] { commands @[ 534 , 161 , 52 , 66 ] { C0 = \"0\" ;\nC1 = \"1\" ; C2 = \"0\" ; C3 = \"0\" ; } transitions { B -> C when x == \"1\" @[ 579 ,\n281 , 60 , 21 ] ; } } state C = \"10\" @[ 509 , 352 , 30 , 30 ] { commands @[ 560\n, 376 , 52 , 66 ] { C0 = \"0\" ; C1 = \"0\" ; C2 = \"1\" ; C3 = \"0\" ; } transitions {\nC -> D when x == \"1\" @[ 424 , 419 , 60 , 21 ] ; } } state D = \"11\" @[ 300 , 365\n, 30 , 30 ] { commands @[ 269 , 393 , 52 , 66 ] { C0 = \"0\" ; C1 = \"0\" ; C2 =\n\"0\" ; C3 = \"1\" ; } transitions { D -> A when x == \"1\" @[ 249 , 292 , 60 , 21 ]\n; } } }")) machine0: pin names not known; wires that end beside it: clk, 1'b0, 1'b1, machine0_p4, Colonne1, Colonne0, Colonne1, Colonne2, Colonne3
  or or_1 (or_1_out, Colonne0, Colonne2, Colonne3);
  or or_2 (or_2_out, Ligne0, Ligne2);
  and and_1 (and_1_out, Colonne1, Ligne1);
  and and_2 (and_2_out, Colonne2, Ligne2);
  and and_3 (and_3_out, Colonne2, Ligne3);
  and and_4 (and_4_out, or_1_out, or_2_out);
  or or_3 (Clavier[0], and_4_out, and_1_out, and_2_out, and_3_out);
  and and_5 (and_5_out, Colonne0, Ligne2);
  and and_6 (and_6_out, Colonne0, Ligne3);
  and and_7 (and_7_out, Colonne2, Ligne3);
  or or_4 (or_4_out, Colonne1, Colonne2, Colonne3);
  or or_5 (or_5_out, Colonne2, Colonne3);
  and and_8 (and_8_out, or_4_out, Ligne0);
  and and_9 (and_9_out, Ligne1, or_5_out);
  or or_6 (or_6_out, Ligne0, Ligne1, Ligne2, Ligne3);
  or or_7 (Clavier[1], and_8_out, and_9_out, and_5_out, and_6_out, and_7_out);
  not not_1 (machine0_p4, or_6_out);
  or or_8 (or_8_out, Ligne0, Ligne1, Ligne2, Ligne3);
  and and_10 (and_10_out, Colonne0, Ligne2);
  and and_11 (and_11_out, or_8_out, Colonne3);
  or or_9 (Clavier[2], and_11_out, Ligne1, and_10_out);
  or or_10 (or_10_out, Ligne0, Ligne1, Ligne2, Ligne3);
  or or_11 (or_11_out, Colonne1, Colonne2);
  or or_12 (or_12_out, Colonne0, Colonne2);
  and and_12 (and_12_out, or_10_out, Colonne3);
  and and_13 (and_13_out, Ligne2, or_11_out);
  and and_14 (and_14_out, Ligne3, or_12_out);
  or or_13 (Clavier[3], and_12_out, and_13_out, and_14_out);

  // Other names for the same wires on the sheet: C0 = Colonne0; C1 = Colonne1; C2 = Colonne2; C3 = Colonne3;
  //   bit0 = Clavier[0]; bit1 = Clavier[1]; bit2 = Clavier[2]; bit3 = Clavier[3]; L0 = Ligne0; L1 = Ligne1;
  //   L2 = Ligne2; L3 = Ligne3
endmodule

module Traducteur (
);

  wire bcd_to_7_segment_decoder_1_p1, bcd_to_7_segment_decoder_1_p2, bcd_to_7_segment_decoder_1_p3,
       bcd_to_7_segment_decoder_1_p4, bcd_to_7_segment_decoder_1_p5, bcd_to_7_segment_decoder_1_p6,
       bcd_to_7_segment_decoder_1_p7, bcd_to_7_segment_decoder_1_p8, bcd_to_7_segment_decoder_2_p1,
       bcd_to_7_segment_decoder_2_p2, bcd_to_7_segment_decoder_2_p3, bcd_to_7_segment_decoder_2_p4,
       bcd_to_7_segment_decoder_2_p6, bcd_to_7_segment_decoder_2_p7, bcd_to_7_segment_decoder_2_p8,
       binairy_to_bcd_converter_1_p3, cl_p2, cl_p3, cl_p4, cl_p5, cl_p6, cl_p7, cl_p8, clav_colonne0,
       clav_colonne1, clav_colonne2, clav_colonne3, clock_1_out, not_1_out, not_2_out, not_3_out, not_4_out,
       not_5_out;
  wire [3:0] clav_clavier;

  Clock clock_1 (.out(clock_1_out));
  not not_1 (not_1_out, cl_p5);
  not not_2 (not_2_out, cl_p6);
  not not_3 (not_3_out, cl_p7);
  not not_4 (not_4_out, cl_p8);
  Clavier clav (
    .clk(clock_1_out), .Ligne0(not_1_out), .Ligne1(not_2_out), .Ligne2(not_3_out), .Ligne3(not_4_out),
    .Clavier(clav_clavier), .Colonne0(clav_colonne0), .Colonne1(clav_colonne1), .Colonne2(clav_colonne2),
    .Colonne3(clav_colonne3));
  not not_5 (not_5_out, clav_colonne0);
  // KeyPad cl: pin names not known; wires that end beside it: not_5_out, cl_p2, cl_p3, cl_p4, cl_p5, cl_p6, cl_p7, cl_p8
  // BCD_to_7_Segment_decoder bcd_to_7_segment_decoder_1: pin names not known; wires that end beside it: bcd_to_7_segment_decoder_1_p1, bcd_to_7_segment_decoder_1_p2, bcd_to_7_segment_decoder_1_p3, bcd_to_7_segment_decoder_1_p4, bcd_to_7_segment_decoder_1_p5, bcd_to_7_segment_decoder_1_p6, bcd_to_7_segment_decoder_1_p7, bcd_to_7_segment_decoder_1_p8
  not not_6 (cl_p3, clav_colonne2);
  not not_7 (cl_p2, clav_colonne1);
  _7_Segment_Display hex2 (
    .g(bcd_to_7_segment_decoder_1_p1), .f(bcd_to_7_segment_decoder_1_p3), .a(bcd_to_7_segment_decoder_1_p6),
    .b(bcd_to_7_segment_decoder_1_p8), .e(bcd_to_7_segment_decoder_1_p2), .d(bcd_to_7_segment_decoder_1_p4),
    .c(bcd_to_7_segment_decoder_1_p7), .dp(1'b0));
  // Binairy_to_BCD_converter #(.binvalue(4)) binairy_to_bcd_converter_1: pin names not known; wires that end beside it: clav_clavier, bcd_to_7_segment_decoder_1_p5, binairy_to_bcd_converter_1_p3
  not not_8 (cl_p4, clav_colonne3);
  // BCD_to_7_Segment_decoder bcd_to_7_segment_decoder_2: pin names not known; wires that end beside it: bcd_to_7_segment_decoder_2_p1, bcd_to_7_segment_decoder_2_p2, bcd_to_7_segment_decoder_2_p3, bcd_to_7_segment_decoder_2_p4, binairy_to_bcd_converter_1_p3, bcd_to_7_segment_decoder_2_p6, bcd_to_7_segment_decoder_2_p7, bcd_to_7_segment_decoder_2_p8
  _7_Segment_Display hex1 (
    .g(bcd_to_7_segment_decoder_2_p1), .f(bcd_to_7_segment_decoder_2_p3), .a(bcd_to_7_segment_decoder_2_p6),
    .b(bcd_to_7_segment_decoder_2_p8), .e(bcd_to_7_segment_decoder_2_p2), .d(bcd_to_7_segment_decoder_2_p4),
    .c(bcd_to_7_segment_decoder_2_p7), .dp(1'b0));
endmodule
