// Logisim project TP78_test1.circ as structural Verilog: 7 circuits, main circuit Calculatrice
module GestionCalcul (
  input  [3:0] clavier,
  input  clavieractif,
  input  clk,
  output [31:0] Resultat
);

  wire Affichage, and1_out, comparator_1_eq, comparator_3_gt, gest_affich;
  wire [1:0] OP, OP1;
  wire [4:0] R;
  wire [30:0] multiplier_1_out;
  wire [31:0] A, adder_1_out, B, Result, subtractor_1_out;

  Comparator #(.width(5), .mode("unsigned")) comparator_1 (.a(R), .b(5'b10000), .eq(comparator_1_eq));  // open: gt, lt
  Adder #(.width(32)) adder_1 (.a(A), .b(B), .out(adder_1_out), .cin(1'b0));  // open: cout
  Subtractor #(.width(32)) subtractor_1 (.a(B), .b(A), .out(subtractor_1_out), .bin(1'b0));  // open: bout
  Multiplier #(.width(31)) multiplier_1 (
    .a(A[30:0]), .b(B[30:0]), .out(multiplier_1_out), .cin({31{1'b0}}));  // open: cout
  GestionKeypad gest (
    .clavieractif(clavieractif), .c(clavier), .clear(comparator_1_eq), .clk(clk), .affichage(A), .OP(OP),
    .R(R), .Affich(gest_affich));  // open: overflow
  Comparator #(.width(5), .mode("unsigned")) comparator_2 (.a(R), .b({5{1'b0}}), .gt(Affichage));  // open: eq, lt
  and and1 (and1_out, Affichage, gest_affich);
  Comparator #(.width(5), .mode("unsigned")) comparator_3 (.a(R), .b({5{1'b0}}), .gt(comparator_3_gt));  // open: eq, lt
  Register #(.width(32)) reg25 (.D(Result), .en(and1_out), .clk(clk), .Q(B), .clr(comparator_1_eq));
  Register #(.width(2)) reg26 (.D(OP), .en(comparator_3_gt), .clk(clk), .Q(OP1), .clr(comparator_1_eq));
  Multiplexer #(.select(2), .width(32), .enable("false")) multiplexer_1 (
    .in0(adder_1_out), .in1(subtractor_1_out), .in2({1'b0, multiplier_1_out}), .in3(B), .out(Result),
    .sel(OP1));
  Multiplexer #(.width(32), .enable("false")) multiplexer_2 (.in0(A), .in1(B), .out(Resultat), .sel(Affichage));

  // Other names for the same wires on the sheet: clavier_t[31:0] = A
endmodule

module GestionKeypad (
  input  clavieractif,
  input  [3:0] c,
  input  clear,
  input  clk,
  output [31:0] affichage,
  output overflow,
  output [1:0] OP,
  output [4:0] R,
  output Affich
);

  wire and1_out, and2_out, comparator_6_lt, machine2_p2, machine2_p3, machine2_p10, or_1_out;
  wire [15:0] multiplier_1_cout, multiplier_1_out;
  wire [31:0] adder_1_out;

  Multiplier #(.width(16)) multiplier_1 (
    .a(affichage[15:0]), .b(16'ha), .out(multiplier_1_out), .cin({16{1'b0}}), .cout(multiplier_1_cout));
  Comparator #(.width(4)) comparator_1 (.a(c), .b(4'b1111), .eq(R[0]));  // open: gt, lt
  Comparator #(.width(4)) comparator_2 (.a(c), .b(4'b1110), .eq(R[1]));  // open: gt, lt
  Comparator #(.width(4)) comparator_3 (.a(c), .b(4'b1101), .eq(R[2]));  // open: gt, lt
  Comparator #(.width(4)) comparator_4 (.a(c), .b(4'b1100), .eq(R[3]));  // open: gt, lt
  Comparator #(.width(4)) comparator_5 (.a(c), .b(4'b1011), .eq(R[4]));  // open: gt, lt
  Adder #(.width(32)) adder_1 (
    .a({{28{1'b0}}, c}), .b({multiplier_1_cout, multiplier_1_out}), .out(adder_1_out), .cin(1'b0),
    .cout(overflow));
  Comparator #(.width(4), .mode("unsigned")) comparator_6 (.a(c), .b(4'b1010), .lt(comparator_6_lt));  // open: gt, eq
  Register #(.width(32)) reg2 (.D(adder_1_out), .en(and2_out), .clk(clk), .Q(affichage), .clr(or_1_out));
  or or_1 (or_1_out, clear, machine2_p10);
  Operation ope0 (.OP(R), .oper(OP));
  and and1 (and1_out, clavieractif, comparator_6_lt);
  and and2 (and2_out, and1_out, machine2_p2);
  // FSM_Entity #(.content("fsm mach1 @[ 50 , 50 , 800 , 500 ] { in c [ 1 ] @[ 50 , 100 , 13 , 15 ] ; in op\n[ 1 ] @[ 50 , 168 , 22 , 15 ] ; out X [ 1 ] @[ 837 , 140 , 13 , 15 ] ; out Z [\n1 ] @[ 835 , 194 , 15 , 15 ] ; out Y [ 1 ] @[ 837 , 166 , 13 , 15 ] ; codeWidth\n= 2 ; reset = S0 ; state S0 = \"01\" @[ 297 , 181 , 30 , 30 ] { commands @[ 235 ,\n173 , 45 , 51 ] { X = \"0\" ; Y = \"0\" ; Z = \"0\" ; } transitions { S0 -> S1 when c\n== \"1\" @[ 432 , 151 , 61 , 21 ] ; } } state S1 = \"10\" @[ 553 , 174 , 30 , 30 ]\n{ commands @[ 583 , 189 , 45 , 51 ] { X = \"1\" ; Y = \"0\" ; Z = \"1\" ; }\ntransitions { S1 -> S2 when default @[ 568 , 344 , 50 , 21 ] ; } } state S2 =\n\"11\" @[ 444 , 344 , 30 , 30 ] { commands @[ 488 , 391 , 45 , 51 ] { X = \"0\" ; Y\n= \"1\" ; Z = \"0\" ; } transitions { S2 -> S0 when c == \"0\" . op == \"1\" @[ 304 ,\n286 , 139 , 21 ] ; } } }")) machine1: pin names not known; wires that end beside it: clk, 1'b0, 1'b1, clavieractif, comparator_6_lt
  // FSM_Entity #(.content("fsm mach2 @[ 50 , 50 , 800 , 500 ] { in op [ 1 ] @[ 50 , 100 , 22 , 15 ] ; in c\n[ 1 ] @[ 50 , 140 , 13 , 15 ] ; in Y1 [ 1 ] @[ 50 , 187 , 21 , 15 ] ; out Y [ 1\n] @[ 837 , 140 , 13 , 15 ] ; codeWidth = 2 ; reset = S0 ; state S0 = \"01\" @[\n300 , 200 , 30 , 30 ] { commands @[ 339 , 180 , 43 , 21 ] { Y = \"0\" ; }\ntransitions { S0 -> S1 when Y1 == \"1\" @[ 483 , 144 , 69 , 21 ] ; } } state S1 =\n\"10\" @[ 647 , 192 , 30 , 30 ] { commands @[ 691 , 207 , 43 , 21 ] { Y = \"0\" ; }\ntransitions { S1 -> S2 when c == \"0\" . op == \"0\" . Y1 == \"1\" @[ 567 , 362 , 216\n, 21 ] ; } } state S2 = \"00\" @[ 448 , 351 , 30 , 30 ] { commands @[ 492 , 406 ,\n43 , 21 ] { Y = \"1\" ; } transitions { S2 -> S0 when c == \"0\" . op == \"1\" @[ 330\n, 375 , 139 , 21 ] ; } } }")) machine2: pin names not known; wires that end beside it: Affich, machine2_p2, machine2_p3, clk, 1'b0, 1'b1, comparator_6_lt, clavieractif, machine2_p3, machine2_p10

  // Other names for the same wires on the sheet: c4bits[3:0] = c; c_t[3:0] = c
endmodule

module Clear (
  output [31:0] A,
  output [31:0] B
);


  assign A = {32{1'b0}};
  assign B = {32{1'b0}};
endmodule

module Clavier (
  input  Ligne0,
  input  Ligne1,
  input  Ligne2,
  input  Ligne3,
  input  clk,
  output [3:0] Clavier,
  output Clavieractif,
  output Colonne0,
  output Colonne1,
  output Colonne2,
  output Colonne3
);

  wire and_2_out, bit0, bit1, bit2, bit3, comparator_1_gt, or_1_out, or_2_out, or_3_out, or_4_out, or_5_out,
       or_6_out, or_7_out, or_8_out, or_9_out, X;

  // FSM_Entity #(.content("fsm mach0 @[ 50 , 50 , 800 , 500 ] { in x [ 1 ] @[ 50 , 125 , 12 , 15 ] ; out C0\n[ 1 ] @[ 828 , 140 , 22 , 15 ] ; out C1 [ 1 ] @[ 828 , 170 , 22 , 15 ] ; out C2\n[ 1 ] @[ 828 , 202 , 22 , 15 ] ; out C3 [ 1 ] @[ 828 , 232 , 22 , 15 ] ;\ncodeWidth = 2 ; reset = A ; state A = \"00\" @[ 300 , 200 , 30 , 30 ] { commands\n@[ 260 , 156 , 52 , 66 ] { C0 = \"1\" ; C1 = \"0\" ; C2 = \"0\" ; C3 = \"0\" ; }\ntransitions { A -> B when x == \"1\" @[ 400 , 150 , 60 , 21 ] ; } } state B =\n\"01\" @[ 487 , 189 , 30 , 30 ] { commands @[ 534 , 161 , 52 , 66 ] { C0 = \"0\" ;\nC1 = \"1\" ; C2 = \"0\" ; C3 = \"0\" ; } transitions { B -> C when x == \"1\" @[ 579 ,\n281 , 60 , 21 ] ; } } state C = \"10\" @[ 509 , 352 , 30 , 30 ] { commands @[ 560\n, 376 , 52 , 66 ] { C0 = \"0\" ; C1 = \"0\" ; C2 = \"1\" ; C3 = \"0\" ; } transitions {\nC -> D when x == \"1\" @[ 424 , 419 , 60 , 21 ] ; } } state D = \"11\" @[ 300 , 365\n, 30 , 30 ] { commands @[ 269 , 393 , 52 , 66 ] { C0 = \"0\" ; C1 = \"0\" ; C2 =\n\"0\" ; C3 = \"1\" ; } transitions { D -> A when x == \"1\" @[ 249 , 292 , 60 , 21 ]\n; } } }")) machine0: pin names not known; wires that end beside it: clk, 1'b0, 1'b1, X, Colonne1, Colonne0, Colonne1, Colonne2, Colonne3
  or or_1 (or_1_out, Colonne0, Colonne1, Colonne2, Colonne3);
  or or_2 (or_2_out, Ligne1, Ligne3);
  and and_1 (bit0, or_1_out, or_2_out);
  or or_3 (or_3_out, Colonne0, Colonne1, Colonne2, Colonne3);
  or or_4 (or_4_out, Ligne2, Ligne3);
  and and_2 (and_2_out, Colonne0, Ligne0);
  and and_3 (bit1, or_3_out, or_4_out);
  Comparator #(.width(4), .mode("unsigned")) comparator_1 (
    .a({bit3, bit2, bit1, bit0}), .b(4'b0000), .gt(comparator_1_gt));  // open: eq, lt
  or or_5 (or_5_out, comparator_1_gt, and_2_out);
  not not_1 (X, or_5_out);
  // FSM_Entity #(.content("fsm mach3 @[ 50 , 50 , 800 , 500 ] { in X [ 1 ] @[ 50 , 100 , 13 , 15 ] ; out\nClavieractif [ 1 ] @[ 776 , 148 , 74 , 15 ] ; codeWidth = 2 ; reset = S0 ;\nstate S0 = \"00\" @[ 300 , 200 , 30 , 30 ] { commands @[ 216 , 202 , 104 , 21 ] {\nClavieractif = \"0\" ; } transitions { S0 -> S3 when X == \"0\" @[ 371 , 142 , 61 ,\n21 ] ; } } state S1 = \"01\" @[ 576 , 207 , 30 , 30 ] { commands @[ 621 , 222 ,\n104 , 21 ] { Clavieractif = \"1\" ; } transitions { S1 -> S2 when X == \"1\" @[ 638\n, 392 , 61 , 21 ] ; } } state S2 = \"10\" @[ 416 , 412 , 30 , 30 ] { commands @[\n461 , 427 , 104 , 21 ] { Clavieractif = \"0\" ; } transitions { S2 -> S0 when X\n== \"1\" @[ 314 , 344 , 61 , 21 ] ; } } state S3 = \"11\" @[ 449 , 106 , 30 , 30 ]\n{ commands @[ 494 , 121 , 104 , 21 ] { Clavieractif = \"0\" ; } transitions { S3\n-> S1 when X == \"0\" @[ 570 , 160 , 61 , 21 ] ; } } }")) machine3: pin names not known; wires that end beside it: clk, 1'b0, 1'b1, X, Clavieractif
  or or_6 (or_6_out, Colonne1, Colonne3);
  or or_7 (or_7_out, Ligne0, Ligne1, Ligne2, Ligne3);
  Register #(.width(4)) regui (.D({bit3, bit2, bit1, bit0}), .en(or_5_out), .clk(clk), .Q(Clavier));  // open: clr
  and and_4 (bit2, or_6_out, or_7_out);
  or or_8 (or_8_out, Colonne2, Colonne3);
  or or_9 (or_9_out, Ligne0, Ligne1, Ligne2, Ligne3);
  and and_5 (bit3, or_8_out, or_9_out);

  // Other names for the same wires on the sheet: C0 = Colonne0; C1 = Colonne1; C2 = Colonne2; C3 = Colonne3;
  //   L0 = Ligne0; L1 = Ligne1; L2 = Ligne2; L3 = Ligne3
endmodule

module Operation (
  input  [4:0] OP,
  output [1:0] oper
);

  wire [3:0] comparator_1_eq;

  Comparator #(.width(5), .mode("unsigned")) comparator_1 (
    .a(OP), .b(5'b00001), .eq(comparator_1_eq[0]));  // open: gt, lt
  Comparator #(.width(5), .mode("unsigned")) comparator_2 (
    .a(OP), .b(5'b00010), .eq(comparator_1_eq[1]));  // open: gt, lt
  Comparator #(.width(5), .mode("unsigned")) comparator_3 (
    .a(OP), .b(5'b00100), .eq(comparator_1_eq[2]));  // open: gt, lt
  Comparator #(.width(5), .mode("unsigned")) comparator_4 (
    .a(OP), .b(5'b01000), .eq(comparator_1_eq[3]));  // open: gt, lt
  Multiplexer #(.select(4), .width(2), .enable("false")) multiplexer_1 (
    .in0(2'b00), .in1(2'b00), .in2(2'b01), .in3(2'b00), .in4(2'b10), .in5(2'b00), .in6(2'b00), .in7(2'b00),
    .in8(2'b11), .in9(2'b00), .in10(2'b00), .in11(2'b00), .in12(2'b00), .in13(2'b00), .in14(2'b00),
    .in15(2'b00), .out(oper), .sel(comparator_1_eq));
endmodule

module Calculatrice (
  output [31:0] out_1
);

  wire bcd_to_7_segment_decoder_1_p1, bcd_to_7_segment_decoder_1_p2, bcd_to_7_segment_decoder_1_p3,
       bcd_to_7_segment_decoder_1_p4, bcd_to_7_segment_decoder_1_p6, bcd_to_7_segment_decoder_1_p7,
       bcd_to_7_segment_decoder_1_p8, bcd_to_7_segment_decoder_2_p1, bcd_to_7_segment_decoder_2_p2,
       bcd_to_7_segment_decoder_2_p3, bcd_to_7_segment_decoder_2_p4, bcd_to_7_segment_decoder_2_p6,
       bcd_to_7_segment_decoder_2_p7, bcd_to_7_segment_decoder_2_p8, bcd_to_7_segment_decoder_3_p1,
       bcd_to_7_segment_decoder_3_p2, bcd_to_7_segment_decoder_3_p3, bcd_to_7_segment_decoder_3_p4,
       bcd_to_7_segment_decoder_3_p6, bcd_to_7_segment_decoder_3_p7, bcd_to_7_segment_decoder_3_p8,
       bcd_to_7_segment_decoder_4_p1, bcd_to_7_segment_decoder_4_p2, bcd_to_7_segment_decoder_4_p3,
       bcd_to_7_segment_decoder_4_p4, bcd_to_7_segment_decoder_4_p6, bcd_to_7_segment_decoder_4_p7,
       bcd_to_7_segment_decoder_4_p8, bcd_to_7_segment_decoder_5_p1, bcd_to_7_segment_decoder_5_p2,
       bcd_to_7_segment_decoder_5_p3, bcd_to_7_segment_decoder_5_p4, bcd_to_7_segment_decoder_5_p6,
       bcd_to_7_segment_decoder_5_p7, bcd_to_7_segment_decoder_5_p8, bcd_to_7_segment_decoder_6_p1,
       bcd_to_7_segment_decoder_6_p2, bcd_to_7_segment_decoder_6_p3, bcd_to_7_segment_decoder_6_p4,
       bcd_to_7_segment_decoder_6_p5, bcd_to_7_segment_decoder_6_p7, bcd_to_7_segment_decoder_6_p8,
       bcd_to_7_segment_decoder_6_p9, binairy_to_bcd_converter_1_p2, binairy_to_bcd_converter_2_p2,
       binairy_to_bcd_converter_3_p2, binairy_to_bcd_converter_4_p3, binairy_to_bcd_converter_5_p2,
       clavi_clavieractif, clk_out, keypad_1_p1, keypad_1_p2, keypad_1_p3, keypad_1_p4, keypad_1_p5,
       keypad_1_p6, keypad_1_p7, keypad_1_p8;
  wire [3:0] cl_hex1, cl_hex2, cl_hex3, cl_hex4, clavi_clavier;

  Traducteur cl (.Resultat(out_1), .Hex4(cl_hex4), .Hex3(cl_hex3), .Hex2(cl_hex2), .Hex1(cl_hex1));
  // KeyPad keypad_1: pin names not known; wires that end beside it: keypad_1_p1, keypad_1_p2, keypad_1_p3, keypad_1_p4, keypad_1_p5, keypad_1_p6, keypad_1_p7, keypad_1_p8
  // Binairy_to_BCD_converter #(.binvalue(4)) binairy_to_bcd_converter_1: pin names not known; wires that end beside it: cl_hex4, binairy_to_bcd_converter_1_p2
  // BCD_to_7_Segment_decoder bcd_to_7_segment_decoder_1: pin names not known; wires that end beside it: bcd_to_7_segment_decoder_1_p1, bcd_to_7_segment_decoder_1_p2, bcd_to_7_segment_decoder_1_p3, bcd_to_7_segment_decoder_1_p4, binairy_to_bcd_converter_1_p2, bcd_to_7_segment_decoder_1_p6, bcd_to_7_segment_decoder_1_p7, bcd_to_7_segment_decoder_1_p8
  _7_Segment_Display Hex4 (
    .g(bcd_to_7_segment_decoder_1_p1), .f(bcd_to_7_segment_decoder_1_p3), .a(bcd_to_7_segment_decoder_1_p6),
    .b(bcd_to_7_segment_decoder_1_p8), .e(bcd_to_7_segment_decoder_1_p2), .d(bcd_to_7_segment_decoder_1_p4),
    .c(bcd_to_7_segment_decoder_1_p7));  // open: dp
  // Binairy_to_BCD_converter #(.binvalue(4)) binairy_to_bcd_converter_2: pin names not known; wires that end beside it: cl_hex3, binairy_to_bcd_converter_2_p2
  Clock #(.highDuration(2), .lowDuration(2)) clk (.out(clk_out));
  // BCD_to_7_Segment_decoder bcd_to_7_segment_decoder_2: pin names not known; wires that end beside it: bcd_to_7_segment_decoder_2_p1, bcd_to_7_segment_decoder_2_p2, bcd_to_7_segment_decoder_2_p3, bcd_to_7_segment_decoder_2_p4, binairy_to_bcd_converter_2_p2, bcd_to_7_segment_decoder_2_p6, bcd_to_7_segment_decoder_2_p7, bcd_to_7_segment_decoder_2_p8
  _7_Segment_Display Hex3 (
    .g(bcd_to_7_segment_decoder_2_p1), .f(bcd_to_7_segment_decoder_2_p3), .a(bcd_to_7_segment_decoder_2_p6),
    .b(bcd_to_7_segment_decoder_2_p8), .e(bcd_to_7_segment_decoder_2_p2), .d(bcd_to_7_segment_decoder_2_p4),
    .c(bcd_to_7_segment_decoder_2_p7));  // open: dp
  Clavier clavi (
    .Ligne0(keypad_1_p5), .Ligne1(keypad_1_p6), .Ligne2(keypad_1_p7), .Ligne3(keypad_1_p8), .clk(clk_out),
    .Clavier(clavi_clavier), .Clavieractif(clavi_clavieractif), .Colonne0(keypad_1_p1),
    .Colonne1(keypad_1_p2), .Colonne2(keypad_1_p3), .Colonne3(keypad_1_p4));
  // Binairy_to_BCD_converter #(.binvalue(4)) binairy_to_bcd_converter_3: pin names not known; wires that end beside it: cl_hex2, binairy_to_bcd_converter_3_p2
  // BCD_to_7_Segment_decoder bcd_to_7_segment_decoder_3: pin names not known; wires that end beside it: bcd_to_7_segment_decoder_3_p1, bcd_to_7_segment_decoder_3_p2, bcd_to_7_segment_decoder_3_p3, bcd_to_7_segment_decoder_3_p4, binairy_to_bcd_converter_3_p2, bcd_to_7_segment_decoder_3_p6, bcd_to_7_segment_decoder_3_p7, bcd_to_7_segment_decoder_3_p8
  // Binairy_to_BCD_converter #(.binvalue(4)) binairy_to_bcd_converter_4: pin names not known; wires that end beside it: clavi_clavieractif, clavi_clavier, binairy_to_bcd_converter_4_p3
  _7_Segment_Display Hex2 (
    .g(bcd_to_7_segment_decoder_3_p1), .f(bcd_to_7_segment_decoder_3_p3), .a(bcd_to_7_segment_decoder_3_p6),
    .b(bcd_to_7_segment_decoder_3_p8), .e(bcd_to_7_segment_decoder_3_p2), .d(bcd_to_7_segment_decoder_3_p4),
    .c(bcd_to_7_segment_decoder_3_p7));  // open: dp
  // Binairy_to_BCD_converter #(.binvalue(4)) binairy_to_bcd_converter_5: pin names not known; wires that end beside it: cl_hex1, binairy_to_bcd_converter_5_p2
  GestionCalcul calc (.clavier(clavi_clavier), .clavieractif(clavi_clavieractif), .clk(clk_out), .Resultat(out_1));
  _7_Segment_Display Hex6 (
    .g(bcd_to_7_segment_decoder_4_p1), .f(bcd_to_7_segment_decoder_4_p3), .a(bcd_to_7_segment_decoder_4_p6),
    .b(bcd_to_7_segment_decoder_4_p8), .e(bcd_to_7_segment_decoder_4_p2), .d(bcd_to_7_segment_decoder_4_p4),
    .c(bcd_to_7_segment_decoder_4_p7));  // open: dp
  // BCD_to_7_Segment_decoder bcd_to_7_segment_decoder_4: pin names not known; wires that end beside it: bcd_to_7_segment_decoder_4_p1, bcd_to_7_segment_decoder_4_p2, bcd_to_7_segment_decoder_4_p3, bcd_to_7_segment_decoder_4_p4, binairy_to_bcd_converter_4_p3, bcd_to_7_segment_decoder_4_p6, bcd_to_7_segment_decoder_4_p7, bcd_to_7_segment_decoder_4_p8
  // BCD_to_7_Segment_decoder bcd_to_7_segment_decoder_5: pin names not known; wires that end beside it: bcd_to_7_segment_decoder_5_p1, bcd_to_7_segment_decoder_5_p2, bcd_to_7_segment_decoder_5_p3, bcd_to_7_segment_decoder_5_p4, binairy_to_bcd_converter_5_p2, bcd_to_7_segment_decoder_5_p6, bcd_to_7_segment_decoder_5_p7, bcd_to_7_segment_decoder_5_p8
  // Binairy_to_BCD_converter #(.binvalue(13)) binairy_to_bcd_converter_6: pin names not known; wires that end beside it: out_1[12:0]
  _7_Segment_Display Hex1 (
    .g(bcd_to_7_segment_decoder_5_p1), .f(bcd_to_7_segment_decoder_5_p3), .a(bcd_to_7_segment_decoder_5_p6),
    .b(bcd_to_7_segment_decoder_5_p8), .e(bcd_to_7_segment_decoder_5_p2), .d(bcd_to_7_segment_decoder_5_p4),
    .c(bcd_to_7_segment_decoder_5_p7));  // open: dp
  // BCD_to_7_Segment_decoder bcd_to_7_segment_decoder_6: pin names not known; wires that end beside it: bcd_to_7_segment_decoder_6_p1, bcd_to_7_segment_decoder_6_p2, bcd_to_7_segment_decoder_6_p3, bcd_to_7_segment_decoder_6_p4, bcd_to_7_segment_decoder_6_p5, bcd_to_7_segment_decoder_6_p1, bcd_to_7_segment_decoder_6_p7, bcd_to_7_segment_decoder_6_p8, bcd_to_7_segment_decoder_6_p9
  _7_Segment_Display u_7_segment_display_1 (
    .g(bcd_to_7_segment_decoder_6_p2), .f(bcd_to_7_segment_decoder_6_p4), .a(bcd_to_7_segment_decoder_6_p7),
    .b(bcd_to_7_segment_decoder_6_p9), .e(bcd_to_7_segment_decoder_6_p3), .d(bcd_to_7_segment_decoder_6_p5),
    .c(bcd_to_7_segment_decoder_6_p8));  // open: dp
endmodule

module Traducteur (
  input  [31:0] Resultat,
  output [3:0] Hex4,
  output [3:0] Hex3,
  output [3:0] Hex2,
  output [3:0] Hex1
);

  // Binairy_to_BCD_converter #(.binvalue(13)) binairy_to_bcd_converter_1: pin names not known; wires that end beside it: Resultat[12:0], Hex4, Hex3, Hex2, Hex1
endmodule
