// Logisim project TP78_test3.circ as structural Verilog: 6 circuits, main circuit Calculatrice
module GestionCalcul (
  input  [3:0] clavier,
  input  clavieractif,
  input  clk,
  input  clear,
  output [31:0] Resultat,
  output clearall
);

  wire aB, AFFICH, and_1_out, and_2_out, clk_t, comparator_1_gt, comparator_2_eq, comparator_3_eq,
       comparator_4_gt, comparator_6_eq, comparator_7_eq, mach_affich_p11, mach_affich_p13, or_2_out, RA,
       WEA, WEB;
  wire [1:0] OP, OP1;
  wire [4:0] R;
  wire [30:0] multiplier_1_out;
  wire [31:0] A, adder_1_out, B, clavier_t, multiplexer_1_out, multiplexer_4_out, result, subtractor_1_out,
       subtractor_2_out;

  Clock clock_1 (.out(clk_t));
  Comparator #(.width(5), .mode("unsigned")) comparator_1 (.a(R), .b({5{1'b0}}), .gt(comparator_1_gt));  // open: eq, lt
  Comparator #(.width(5), .mode("unsigned")) comparator_2 (.a(R), .b(5'b01000), .eq(comparator_2_eq));  // open: gt, lt
  // FSM_Entity #(.content("fsm example @[ 50 , 50 , 800 , 500 ] { in OP [ 1 ] @[ 50 , 100 , 23 , 15 ] ; in\nCA [ 1 ] @[ 50 , 129 , 22 , 15 ] ; in RA [ 1 ] @[ 50 , 159 , 22 , 15 ] ; in EQ\n[ 1 ] @[ 50 , 186 , 23 , 15 ] ; out WEA [ 1 ] @[ 817 , 94 , 33 , 15 ] ; out WEB\n[ 1 ] @[ 817 , 122 , 33 , 15 ] ; out DECA [ 1 ] @[ 811 , 151 , 39 , 15 ] ; out\nAFFICH [ 1 ] @[ 802 , 182 , 48 , 15 ] ; out CLEAR [ 1 ] @[ 806 , 212 , 44 , 15\n] ; codeWidth = 4 ; reset = S0 ; state S0 = \"0000\" @[ 187 , 122 , 30 , 30 ] {\ncommands @[ 223 , 156 , 78 , 81 ] { WEA = \"0\" ; WEB = \"0\" ; DECA = \"0\" ; AFFICH\n= \"0\" ; CLEAR = \"0\" ; } transitions { S0 -> S1 when OP == \"1\" . CA == \"1\" . RA\n== \"0\" . EQ == \"0\" @[ 177 , 85 , 306 , 21 ] ; S0 -> S4 when OP == \"1\" . CA ==\n\"1\" . RA == \"1\" @[ 459 , 306 , 227 , 21 ] ; } } state S1 = \"0001\" @[ 464 , 99 ,\n30 , 30 ] { commands @[ 509 , 114 , 69 , 51 ] { WEA = \"1\" ; WEB = \"0\" ; DECA =\n\"1\" ; } transitions { S1 -> S2 when default @[ 626 , 94 , 50 , 21 ] ; } } state\nS2 = \"0010\" @[ 679 , 116 , 30 , 30 ] { commands @[ 724 , 131 , 69 , 51 ] { WEA\n= \"0\" ; WEB = \"0\" ; DECA = \"0\" ; } transitions { S2 -> S3 when OP == \"0\" . CA\n== \"1\" @[ 708 , 262 , 149 , 21 ] ; } } state S3 = \"0011\" @[ 741 , 305 , 30 , 30\n] { commands @[ 786 , 320 , 63 , 36 ] { WEA = \"0\" ; WEB = \"0\" ; } transitions {\nS3 -> S4 when OP == \"1\" . CA == \"1\" @[ 768 , 404 , 149 , 21 ] ; } } state S4 =\n\"0100\" @[ 709 , 465 , 30 , 30 ] { commands @[ 754 , 480 , 69 , 51 ] { WEA = \"0\"\n; WEB = \"1\" ; DECA = \"1\" ; } transitions { S4 -> S5 when default @[ 656 , 517 ,\n50 , 21 ] ; } } state S5 = \"0101\" @[ 531 , 480 , 30 , 30 ] { commands @[ 576 ,\n495 , 69 , 51 ] { WEA = \"1\" ; WEB = \"0\" ; DECA = \"0\" ; } transitions { S5 -> S6\nwhen default @[ 425 , 515 , 50 , 21 ] ; } } state S6 = \"0110\" @[ 316 , 446 , 30\n, 30 ] { commands @[ 361 , 461 , 78 , 51 ] { WEA = \"0\" ; WEB = \"0\" ; AFFICH =\n\"1\" ; } transitions { S6 -> S0 when OP == \"0\" . EQ == \"0\" . CA == \"0\" @[ 391 ,\n372 , 228 , 21 ] ; S6 -> S7 when OP == \"1\" . EQ == \"1\" . CA == \"1\" @[ 106 , 512\n, 228 , 21 ] ; } } state S7 = \"0111\" @[ 75 , 384 , 30 , 30 ] { commands @[ 119\n, 399 , 78 , 21 ] { AFFICH = \"1\" ; } transitions { S7 -> S8 when OP == \"0\" . EQ\n== \"0\" . CA == \"1\" @[ 85 , 274 , 228 , 21 ] ; S7 -> S0 when OP == \"1\" . EQ ==\n\"0\" . CA == \"1\" @[ 208 , 327 , 228 , 21 ] ; } } state S8 = \"1000\" @[ 93 , 195 ,\n30 , 30 ] { commands @[ 145 , 220 , 74 , 21 ] { CLEAR = \"1\" ; } transitions {\nS8 -> S0 when default @[ 102 , 141 , 50 , 21 ] ; } } }")) mach_affich: pin names not known; wires that end beside it: clk, clk_t, clearall, 1'b1, comparator_1_gt, clavieractif, RA, comparator_2_eq, WEA, WEB, mach_affich_p11, AFFICH, mach_affich_p13
  Adder #(.width(32)) adder_1 (.a(A), .b(B), .out(adder_1_out), .cin(1'b0));  // open: cout
  Subtractor #(.width(32)) subtractor_1 (.a(A), .b(B), .out(subtractor_1_out), .bin(1'b0));  // open: bout
  Multiplier #(.width(31)) multiplier_1 (
    .a(A[30:0]), .b(B[30:0]), .out(multiplier_1_out), .cin({31{1'b0}}));  // open: cout
  Comparator #(.width(5), .mode("unsigned")) comparator_3 (.a(R), .b(5'b10000), .eq(comparator_3_eq));  // open: gt, lt
  GestionKeypad gest (
    .clavieractif(clavieractif), .c(clavier), .clear(clearall), .clk(clk_t), .affichage(clavier_t), .OP(OP),
    .R(R));  // open: overflow
  or or_1 (clearall, comparator_3_eq, clear, mach_affich_p13);
  Multiplexer #(.select(2), .width(32), .enable("false")) multiplexer_1 (
    .in0(adder_1_out), .in1(subtractor_1_out), .in2({1'b0, multiplier_1_out}), .in3(A),
    .out(multiplexer_1_out), .sel(OP1));
  Comparator #(.width(5), .mode("unsigned")) comparator_4 (.a(R), .b({5{1'b0}}), .gt(comparator_4_gt));  // open: eq, lt
  and and_1 (and_1_out, comparator_4_gt, mach_affich_p11);
  Subtractor #(.width(32)) subtractor_2 (
    .a(32'h2000), .b(multiplexer_1_out), .out(subtractor_2_out), .bin(1'b0));  // open: bout
  Comparator #(.width(32), .mode("unsigned")) comparator_5 (.a(A), .b(B), .lt(aB));  // open: gt, eq
  Comparator #(.width(2), .mode("unsigned")) comparator_6 (.a(OP1), .b(2'b01), .eq(comparator_6_eq));  // open: gt, lt
  Comparator #(.width(2), .mode("unsigned")) comparator_7 (.a(OP1), .b(2'b11), .eq(comparator_7_eq));  // open: gt, lt
  // Shift_Register #(.width(2), .length(2)) deca: pin names not known; wires that end beside it: clearall, 1'b0, and_1_out, clk_t, OP, 2'b00, 2'b00, OP1
  Multiplexer #(.width(32), .enable("false")) multiplexer_2 (
    .in0(multiplexer_1_out), .in1(subtractor_2_out), .out(result), .sel(and_2_out));
  and and_2 (and_2_out, aB, or_2_out);
  _7_Segment_Display Hex5 (.g(aB), .f(1'b0), .a(1'b0), .b(1'b0), .e(1'b0), .d(1'b0), .c(1'b0), .dp(1'b0));
  or or_2 (or_2_out, comparator_6_eq, comparator_7_eq);
  Multiplexer #(.width(32), .enable("false")) multiplexer_3 (.in0(clavier_t), .in1(A), .out(Resultat), .sel(AFFICH));
  Multiplexer #(.width(32), .enable("false")) multiplexer_4 (
    .in0(clavier_t), .in1(result), .out(multiplexer_4_out), .sel(RA));
  Register #(.width(32)) u_A (.D(multiplexer_4_out), .en(WEA), .clk(clk_t), .Q(A), .clr(clearall));
  Register #(.width(32)) u_B (.D(clavier_t), .en(WEB), .clk(clk_t), .Q(B), .clr(clearall));
  Comparator #(.width(32), .mode("unsigned")) comparator_8 (.a(A), .b({32{1'b0}}), .gt(RA));  // open: eq, lt

  // Other names for the same wires on the sheet: ca = clavieractif; clear_t = clearall
endmodule

module GestionKeypad (
  input  clavieractif,
  input  [3:0] c,
  input  clear,
  input  clk,
  output [31:0] affichage,
  output overflow,
  output [1:0] OP,
  output [4:0] R
);

  wire and1_out, and2_out, comparator_6_lt, machine1_p6, machine1_p7, or_1_out;
  wire [15:0] multiplier_1_cout, multiplier_1_out;
  wire [31:0] adder_1_out;

  Multiplier #(.width(16)) multiplier_1 (
    .a(affichage[15:0]), .b(16'ha), .out(multiplier_1_out), .cin({16{1'b0}}), .cout(multiplier_1_cout));
  Comparator #(.width(4)) comparator_1 (.a(c), .b(4'b1111), .eq(R[0]));  // open: gt, lt
  Comparator #(.width(4)) comparator_2 (.a(c), .b(4'b1110), .eq(R[1]));  // open: gt, lt
  Comparator #(.width(4)) comparator_3 (.a(c), .b(4'b1101), .eq(R[2]));  // open: gt, lt
  Comparator #(.width(4)) comparator_4 (.a(c), .b(4'b1100), .eq(R[3]));  // open: gt, lt
  Comparator #(.width(4)) comparator_5 (.a(c), .b(4'b1011), .eq(R[4]));  // open: gt, lt
  Adder #(.width(32)) adder_1 (
    .a({{28{1'b0}}, c}), .b({multiplier_1_cout, multiplier_1_out}), .out(adder_1_out), .cin(1'b0),
    .cout(overflow));
  Comparator #(.width(4), .mode("unsigned")) comparator_6 (.a(c), .b(4'b1010), .lt(comparator_6_lt));  // open: gt, eq
  Register #(.width(32)) reg2 (.D(adder_1_out), .en(and2_out), .clk(clk), .Q(affichage), .clr(or_1_out));
  or or_1 (or_1_out, clear, machine1_p7);
  Operation ope0 (.OP(R), .oper(OP));
  and and1 (and1_out, clavieractif, comparator_6_lt);
  and and2 (and2_out, and1_out, machine1_p6);
  // FSM_Entity #(.content("fsm mach1 @[ 50 , 50 , 800 , 500 ] { in c [ 1 ] @[ 50 , 100 , 12 , 15 ] ; in op\n[ 1 ] @[ 50 , 168 , 21 , 15 ] ; out Z [ 1 ] @[ 835 , 194 , 15 , 15 ] ; out Y [\n1 ] @[ 837 , 166 , 13 , 15 ] ; codeWidth = 2 ; reset = S0 ; state S0 = \"01\" @[\n297 , 181 , 30 , 30 ] { commands @[ 250 , 173 , 45 , 36 ] { Y = \"0\" ; Z = \"0\" ;\n} transitions { S0 -> S1 when c == \"1\" @[ 432 , 151 , 58 , 21 ] ; } } state S1\n= \"10\" @[ 610 , 165 , 30 , 30 ] { commands @[ 670 , 180 , 45 , 36 ] { Y = \"0\" ;\nZ = \"1\" ; } transitions { S1 -> S2 when default @[ 698 , 281 , 47 , 21 ] ; } }\nstate S2 = \"11\" @[ 620 , 369 , 30 , 30 ] { commands @[ 680 , 384 , 45 , 36 ] {\nY = \"0\" ; Z = \"0\" ; } transitions { S2 -> S0 when c == \"0\" . op == \"1\" @[ 432 ,\n346 , 130 , 21 ] ; S2 -> S3 when c == \"0\" . op == \"0\" @[ 473 , 482 , 130 , 21 ]\n; } } state S3 = \"00\" @[ 320 , 411 , 30 , 30 ] { commands @[ 365 , 426 , 45 ,\n36 ] { Y = \"1\" ; Z = \"0\" ; } transitions { S3 -> S0 when c == \"0\" . op == \"1\"\n@[ 270 , 343 , 130 , 21 ] ; } } }")) machine1: pin names not known; wires that end beside it: clk, 1'b0, 1'b1, clavieractif, comparator_6_lt, machine1_p6, machine1_p7

  // Other names for the same wires on the sheet: c4bits[3:0] = c; c_t[3:0] = c
endmodule

module Clavier (
  input  Ligne0,
  input  Ligne1,
  input  Ligne2,
  input  Ligne3,
  input  clk,
  input  clearall,
  output [3:0] Clavier,
  output Clavieractif,
  output Colonne0,
  output Colonne1,
  output Colonne2,
  output Colonne3
);

  wire and_1_out, and_2_out, and_3_out, and_4_out, and_5_out, and_6_out, and_7_out, and_8_out, and_9_out,
       and_10_out, and_11_out, and_12_out, and_13_out, and_14_out, and_15_out, bit0, bit1, bit2, bit3,
       comparator_1_gt, or_1_out, or_2_out, or_4_out, or_5_out, or_7_out, or_8_out, or_10_out, or_11_out,
       or_12_out, X;

  // FSM_Entity #(.content("fsm mach0 @[ 50 , 50 , 800 , 500 ] { in x [ 1 ] @[ 50 , 125 , 12 , 15 ] ; out C0\n[ 1 ] @[ 828 , 140 , 22 , 15 ] ; out C1 [ 1 ] @[ 828 , 170 , 22 , 15 ] ; out C2\n[ 1 ] @[ 828 , 202 , 22 , 15 ] ; out C3 [ 1 ] @[ 828 , 232 , 22 , 15 ] ;\ncodeWidth = 2 ; reset = A ; state A = \"00\" @[ 300 , 200 , 30 , 30 ] { commands\n@[ 260 , 156 , 52 , 66 ] { C0 = \"1\" ; C1 = \"0\" ; C2 = \"0\" ; C3 = \"0\" ; }\ntransitions { A -> B when x == \"1\" @[ 400 , 150 , 60 , 21 ] ; } } state B =\n\"01\" @[ 487 , 189 , 30 , 30 ] { commands @[ 534 , 161 , 52 , 66 ] { C0 = \"0\" ;\nC1 = \"1\" ; C2 = \"0\" ; C3 = \"0\" ; } transitions { B -> C when x == \"1\" @[ 579 ,\n281 , 60 , 21 ] ; } } state C = \"10\" @[ 509 , 352 , 30 , 30 ] { commands @[ 560\n, 376 , 52 , 66 ] { C0 = \"0\" ; C1 = \"0\" ; C2 = \"1\" ; C3 = \"0\" ; } transitions {\nC -> D when x == \"1\" @[ 424 , 419 , 60 , 21 ] ; } } state D = \"11\" @[ 300 , 365\n, 30 , 30 ] { commands @[ 269 , 393 , 52 , 66 ] { C0 = \"0\" ; C1 = \"0\" ; C2 =\n\"0\" ; C3 = \"1\" ; } transitions { D -> A when x == \"1\" @[ 249 , 292 , 60 , 21 ]\n; } } }")) machine0: pin names not known; wires that end beside it: clk, clearall, 1'b1, X, Colonne1, Colonne0, Colonne1, Colonne2, Colonne3
  or or_1 (or_1_out, Colonne0, Colonne2, Colonne3);
  or or_2 (or_2_out, Ligne0, Ligne2);
  and and_1 (and_1_out, Colonne1, Ligne1);
  and and_2 (and_2_out, Colonne2, Ligne2);
  and and_3 (and_3_out, Colonne2, Ligne3);
  and and_4 (and_4_out, or_1_out, or_2_out);
  or or_3 (bit0, and_4_out, and_1_out, and_2_out, and_3_out);
  and and_5 (and_5_out, Colonne0, Ligne2);
  and and_6 (and_6_out, Colonne0, Ligne3);
  and and_7 (and_7_out, Colonne2, Ligne3);
  or or_4 (or_4_out, Colonne1, Colonne2, Colonne3);
  or or_5 (or_5_out, Colonne2, Colonne3);
  and and_8 (and_8_out, or_4_out, Ligne0);
  and and_9 (and_9_out, Ligne1, or_5_out);
  and and_10 (and_10_out, Colonne1, Ligne3);
  or or_6 (bit1, and_8_out, and_9_out, and_5_out, and_6_out, and_7_out);
  Comparator #(.width(4), .mode("unsigned")) comparator_1 (
    .a({bit3, bit2, bit1, bit0}), .b(4'b0000), .gt(comparator_1_gt));  // open: eq, lt
  or or_7 (or_7_out, comparator_1_gt, and_10_out);
  not not_1 (X, or_7_out);
  // FSM_Entity #(.content("fsm mach3 @[ 50 , 50 , 800 , 500 ] { in X [ 1 ] @[ 50 , 100 , 13 , 15 ] ; out\nClavieractif [ 1 ] @[ 776 , 148 , 74 , 15 ] ; codeWidth = 2 ; reset = S0 ;\nstate S0 = \"00\" @[ 300 , 200 , 30 , 30 ] { commands @[ 216 , 202 , 104 , 21 ] {\nClavieractif = \"0\" ; } transitions { S0 -> S3 when X == \"0\" @[ 371 , 142 , 61 ,\n21 ] ; } } state S1 = \"01\" @[ 576 , 207 , 30 , 30 ] { commands @[ 621 , 222 ,\n104 , 21 ] { Clavieractif = \"1\" ; } transitions { S1 -> S2 when X == \"1\" @[ 638\n, 392 , 61 , 21 ] ; } } state S2 = \"10\" @[ 416 , 412 , 30 , 30 ] { commands @[\n461 , 427 , 104 , 21 ] { Clavieractif = \"0\" ; } transitions { S2 -> S0 when X\n== \"1\" @[ 314 , 344 , 61 , 21 ] ; } } state S3 = \"11\" @[ 449 , 106 , 30 , 30 ]\n{ commands @[ 494 , 121 , 104 , 21 ] { Clavieractif = \"0\" ; } transitions { S3\n-> S1 when X == \"0\" @[ 570 , 160 , 61 , 21 ] ; } } }")) machine3: pin names not known; wires that end beside it: clk, clearall, 1'b1, X, Clavieractif
  or or_8 (or_8_out, Ligne0, Ligne1, Ligne2, Ligne3);
  and and_11 (and_11_out, Colonne0, Ligne2);
  Register #(.width(4)) regui (.D({bit3, bit2, bit1, bit0}), .en(or_7_out), .clk(clk), .Q(Clavier), .clr(clearall));
  and and_12 (and_12_out, or_8_out, Colonne3);
  or or_9 (bit2, and_12_out, Ligne1, and_11_out);
  or or_10 (or_10_out, Ligne0, Ligne1, Ligne2, Ligne3);
  or or_11 (or_11_out, Colonne1, Colonne2);
  or or_12 (or_12_out, Colonne0, Colonne2);
  and and_13 (and_13_out, or_10_out, Colonne3);
  and and_14 (and_14_out, Ligne2, or_11_out);
  and and_15 (and_15_out, Ligne3, or_12_out);
  or or_13 (bit3, and_13_out, and_14_out, and_15_out);

  // Other names for the same wires on the sheet: C0 = Colonne0; C1 = Colonne1; C2 = Colonne2; C3 = Colonne3;
  //   clear = clearall; L0 = Ligne0; L1 = Ligne1; L2 = Ligne2; L3 = Ligne3
endmodule

module Operation (
  input  [4:0] OP,
  output [1:0] oper
);

  wire [3:0] comparator_1_eq;

  Comparator #(.width(5), .mode("unsigned")) comparator_1 (
    .a(OP), .b(5'b00001), .eq(comparator_1_eq[0]));  // open: gt, lt
  Comparator #(.width(5), .mode("unsigned")) comparator_2 (
    .a(OP), .b(5'b00010), .eq(comparator_1_eq[1]));  // open: gt, lt
  Comparator #(.width(5), .mode("unsigned")) comparator_3 (
    .a(OP), .b(5'b00100), .eq(comparator_1_eq[2]));  // open: gt, lt
  Comparator #(.width(5), .mode("unsigned")) comparator_4 (
    .a(OP), .b(5'b01000), .eq(comparator_1_eq[3]));  // open: gt, lt
  Multiplexer #(.select(4), .width(2), .enable("false")) multiplexer_1 (
    .in0(2'b00), .in1(2'b00), .in2(2'b01), .in3(2'b00), .in4(2'b10), .in5(2'b00), .in6(2'b00), .in7(2'b00),
    .in8(2'b11), .in9(2'b00), .in10(2'b00), .in11(2'b00), .in12(2'b00), .in13(2'b00), .in14(2'b00),
    .in15(2'b00), .out(oper), .sel(comparator_1_eq));
endmodule

module Calculatrice (
);

  wire binairy_to_bcd_converter_1_p2, binairy_to_bcd_converter_2_p2, binairy_to_bcd_converter_3_p2,
       binairy_to_bcd_converter_4_p2, calc_clearall, clav_p3, clav_p4, clav_p5, clav_p6, clav_p7, clav_p8,
       clavi_colonne0, clavi_colonne1, clavi_colonne2, clavi_colonne3, clavierac, clear, clk_out,
       comparator_1_gt, not_1_out, not_2_out, not_3_out, not_6_out, not_7_out, not_8_out, not_9_out;
  wire [3:0] cl_hex1, cl_hex2, cl_hex3, cl_hex4, clavi_clavier;
  wire [31:0] calc_resultat;

  Comparator #(.width(32), .mode("unsigned")) comparator_1 (
    .a(calc_resultat), .b(32'h1fff), .gt(comparator_1_gt));  // open: eq, lt
  not not_1 (not_1_out, clavierac);
  and and_1 (clear, not_1_out, comparator_1_gt);
  Traducteur cl (.Resultat(calc_resultat), .Hex4(cl_hex4), .Hex3(cl_hex3), .Hex2(cl_hex2), .Hex1(cl_hex1));
  // Binairy_to_BCD_converter #(.binvalue(4)) binairy_to_bcd_converter_1: pin names not known; wires that end beside it: cl_hex4, binairy_to_bcd_converter_1_p2
  not not_2 (not_2_out, clavi_colonne0);
  not not_3 (not_3_out, clavi_colonne1);
  // KeyPad clav: pin names not known; wires that end beside it: not_2_out, not_3_out, clav_p3, clav_p4, clav_p5, clav_p6, clav_p7, clav_p8
  // BCD_to_7_Segment_decoder bcd_to_7_segment_decoder_1: pin names not known; wires that end beside it: binairy_to_bcd_converter_1_p2
  _7_Segment_Display Hex4 ();  // open: g, f, a, b, e, d, c, dp
  not not_4 (clav_p3, clavi_colonne2);
  not not_5 (clav_p4, clavi_colonne3);
  not not_6 (not_6_out, clav_p5);
  not not_7 (not_7_out, clav_p6);
  not not_8 (not_8_out, clav_p7);
  not not_9 (not_9_out, clav_p8);
  // Binairy_to_BCD_converter #(.binvalue(4)) binairy_to_bcd_converter_2: pin names not known; wires that end beside it: cl_hex3, binairy_to_bcd_converter_2_p2
  Clock #(.highDuration(2), .lowDuration(2)) clk (.out(clk_out));
  _7_Segment_Display Hex3 ();  // open: g, f, a, b, e, d, c, dp
  // BCD_to_7_Segment_decoder bcd_to_7_segment_decoder_2: pin names not known; wires that end beside it: binairy_to_bcd_converter_2_p2
  Clavier clavi (
    .Ligne0(not_6_out), .Ligne1(not_7_out), .Ligne2(not_8_out), .Ligne3(not_9_out), .clk(clk_out),
    .clearall(calc_clearall), .Clavier(clavi_clavier), .Clavieractif(clavierac), .Colonne0(clavi_colonne0),
    .Colonne1(clavi_colonne1), .Colonne2(clavi_colonne2), .Colonne3(clavi_colonne3));
  // Binairy_to_BCD_converter #(.binvalue(4)) binairy_to_bcd_converter_3: pin names not known; wires that end beside it: cl_hex2, binairy_to_bcd_converter_3_p2
  // BCD_to_7_Segment_decoder bcd_to_7_segment_decoder_3: pin names not known; wires that end beside it: binairy_to_bcd_converter_3_p2
  _7_Segment_Display Hex2 ();  // open: g, f, a, b, e, d, c, dp
  // Binairy_to_BCD_converter #(.binvalue(4)) binairy_to_bcd_converter_4: pin names not known; wires that end beside it: cl_hex1, binairy_to_bcd_converter_4_p2
  GestionCalcul calc (
    .clavier(clavi_clavier), .clavieractif(clavierac), .clk(clk_out), .clear(clear),
    .Resultat(calc_resultat), .clearall(calc_clearall));
  // BCD_to_7_Segment_decoder bcd_to_7_segment_decoder_4: pin names not known; wires that end beside it: binairy_to_bcd_converter_4_p2
  _7_Segment_Display Hex1 ();  // open: g, f, a, b, e, d, c, dp
endmodule

module Traducteur (
  input  [31:0] Resultat,
  output [3:0] Hex4,
  output [3:0] Hex3,
  output [3:0] Hex2,
  output [3:0] Hex1
);

  // Binairy_to_BCD_converter #(.binvalue(13)) binairy_to_bcd_converter_1: pin names not known; wires that end beside it: Resultat[12:0], Hex4, Hex3, Hex2, Hex1
endmodule
