// Logisim project TP78_test4.circ as structural Verilog: 7 circuits, main circuit Calculatrice
module GestionCalcul (
  input  [3:0] clavier,
  input  clavieractif,
  input  clk,
  input  clear,
  output [31:0] Resultat,
  output clearall
);

  wire Affichage, Algo_Calcul_p9, and_1_out, and_2_out, clearA, clk_t, comparator_1_eq, comparator_2_eq,
       comparator_2_gt, or_1_out, WEA, WEB, WEOP;
  wire [1:0] OP, OP1, OPERATEUR;
  wire [4:0] R;
  wire [31:0] A, B, clavier_t, result;

  Clock clock_1 (.out(clk_t));
  Comparator #(.width(5), .mode("unsigned")) comparator_1 (.a(R), .b(5'b10000), .eq(comparator_1_eq));  // open: gt, lt
  Comparator #(.width(5), .mode("unsigned")) comparator_2 (
    .a(R), .b({5{1'b0}}), .gt(comparator_2_gt), .eq(comparator_2_eq));  // open: lt
  and and_1 (and_1_out, comparator_2_gt, clavieractif);
  and and_2 (and_2_out, comparator_2_eq, clavieractif);
  Register #(.width(32)) u_A (.D(clavier_t), .en(WEA), .clk(clk_t), .Q(A), .clr(or_1_out));
  or or_1 (or_1_out, clearall, clearA);
  // FSM_Entity #(.content("fsm example @[ 50 , 50 , 800 , 500 ] { in OPERATEUR [ 2 ] @[ 50 , 249 , 109 , 15\n] ; in cl [ 1 ] @[ 50 , 202 , 16 , 15 ] ; in notoperande [ 1 ] @[ 50 , 307 , 88\n, 15 ] ; in operande [ 1 ] @[ 50 , 372 , 67 , 15 ] ; out Clear [ 1 ] @[ 812 ,\n102 , 38 , 15 ] ; out OP [ 2 ] @[ 797 , 131 , 53 , 15 ] ; out ClearA [ 1 ] @[\n804 , 161 , 46 , 15 ] ; out WEOP [ 1 ] @[ 808 , 190 , 42 , 15 ] ; out WEA [ 1 ]\n@[ 817 , 221 , 33 , 15 ] ; out WEB [ 1 ] @[ 817 , 248 , 33 , 15 ] ; out\nAffichage [ 1 ] @[ 786 , 275 , 64 , 15 ] ; codeWidth = 4 ; reset = S0 ; state\nS0 = \"0000\" @[ 128 , 129 , 30 , 30 ] { commands @[ 57 , 78 , 94 , 81 ] { Clear\n= \"0\" ; ClearA = \"0\" ; WEOP = \"0\" ; WEA = \"1\" ; Affichage = \"0\" ; } transitions\n{ S0 -> S1 when cl == \"1\" . notoperande == \"1\" @[ 231 , 102 , 208 , 21 ] ; S0\n-> S2 when cl == \"0\" . notoperande == \"1\" @[ 196 , 195 , 208 , 21 ] ; } } state\nS1 = \"0001\" @[ 500 , 85 , 30 , 30 ] { commands @[ 549 , 80 , 76 , 81 ] { Clear\n= \"1\" ; ClearA = \"0\" ; OP = \"00\" ; WEOP = \"0\" ; WEA = \"0\" ; } transitions { S1\n-> S10 when default @[ 773 , 83 , 50 , 21 ] ; } } state S2 = \"0010\" @[ 237 ,\n233 , 30 , 30 ] { commands @[ 245 , 174 , 76 , 66 ] { Clear = \"0\" ; ClearA =\n\"0\" ; WEOP = \"0\" ; WEA = \"0\" ; } transitions { S2 -> S3 when OPERATEUR == \"00\"\n@[ 317 , 221 , 135 , 21 ] ; S2 -> S5 when OPERATEUR == \"01\" @[ 277 , 276 , 135\n, 21 ] ; S2 -> S7 when OPERATEUR == \"10\" @[ 306 , 320 , 135 , 21 ] ; S2 -> S9\nwhen OPERATEUR == \"11\" @[ 191 , 334 , 135 , 21 ] ; } } state S3 = \"0011\" @[ 426\n, 166 , 30 , 30 ] { commands @[ 471 , 181 , 63 , 36 ] { OP = \"00\" ; WEB = \"1\" ;\n} transitions { S3 -> S4 when default @[ 546 , 219 , 50 , 21 ] ; } } state S4 =\n\"0100\" @[ 577 , 346 , 30 , 30 ] { commands @[ 616 , 327 , 94 , 51 ] { ClearA =\n\"1\" ; WEB = \"0\" ; Affichage = \"1\" ; } transitions { S4 -> S10 when default @[\n623 , 409 , 50 , 21 ] ; } } state S5 = \"0101\" @[ 398 , 246 , 30 , 30 ] {\ncommands @[ 443 , 261 , 63 , 36 ] { OP = \"01\" ; WEB = \"1\" ; } transitions { S5\n-> S4 when default @[ 517 , 297 , 50 , 21 ] ; } } state S7 = \"0111\" @[ 368 ,\n341 , 30 , 30 ] { commands @[ 413 , 356 , 63 , 36 ] { OP = \"10\" ; WEB = \"1\" ; }\ntransitions { S7 -> S4 when default @[ 507 , 347 , 50 , 21 ] ; } } state S9 =\n\"1001\" @[ 293 , 419 , 30 , 30 ] { commands @[ 338 , 434 , 76 , 51 ] { OP = \"11\"\n; ClearA = \"1\" ; WEB = \"0\" ; } transitions { S9 -> S10 when default @[ 544 ,\n444 , 50 , 21 ] ; } } state S10 = \"1010\" @[ 707 , 466 , 30 , 30 ] { commands @[\n752 , 481 , 94 , 66 ] { Clear = \"0\" ; ClearA = \"0\" ; WEOP = \"1\" ; Affichage =\n\"1\" ; } transitions { S10 -> S11 when notoperande == \"0\" @[ 440 , 517 , 136 ,\n21 ] ; } } state S11 = \"1011\" @[ 150 , 447 , 30 , 30 ] { commands @[ 195 , 462\n, 94 , 66 ] { Clear = \"0\" ; ClearA = \"0\" ; WEOP = \"0\" ; Affichage = \"1\" ; }\ntransitions { S11 -> S0 when operande == \"1\" . cl == \"0\" . notoperande == \"0\"\n@[ 47 , 281 , 331 , 21 ] ; S11 -> S1 when operande == \"0\" . cl == \"1\" .\nnotoperande == \"1\" @[ 156 , 392 , 331 , 21 ] ; } } }")) Algo_Calcul: pin names not known; wires that end beside it: clk, clk_t, clearall, 1'b1, OPERATEUR, comparator_1_eq, and_1_out, and_2_out, Algo_Calcul_p9, OP, clearA, WEOP, WEA, WEB, Affichage
  UAL Calcul (.A(A), .B(B), .OP(OP), .Resultat(result));
  Register #(.width(32)) u_B (.D(result), .en(WEB), .clk(clk_t), .Q(B), .clr(clearall));
  GestionKeypad gest (
    .clavieractif(clavieractif), .c(clavier), .clear(clearall), .clk(clk_t), .affichage(clavier_t), .OP(OP1),
    .R(R));  // open: overflow
  or or_2 (clearall, clear, Algo_Calcul_p9);
  Register #(.width(2)) register_1 (.D(OP1), .en(WEOP), .clk(clk_t), .Q(OPERATEUR), .clr(clearall));
  Multiplexer #(.width(32), .enable("false")) multiplexer_1 (.in0(A), .in1(B), .out(Resultat), .sel(Affichage));

  // Other names for the same wires on the sheet: ca = clavieractif; clear_t = clearall
endmodule

module GestionKeypad (
  input  clavieractif,
  input  [3:0] c,
  input  clear,
  input  clk,
  output [31:0] affichage,
  output overflow,
  output [1:0] OP,
  output [4:0] R
);

  wire and1_out, and2_out, comparator_6_lt, machine1_p6, machine1_p7, or_1_out;
  wire [15:0] multiplier_1_cout, multiplier_1_out;
  wire [31:0] adder_1_out;

  Multiplier #(.width(16)) multiplier_1 (
    .a(affichage[15:0]), .b(16'ha), .out(multiplier_1_out), .cin({16{1'b0}}), .cout(multiplier_1_cout));
  Comparator #(.width(4)) comparator_1 (.a(c), .b(4'b1111), .eq(R[0]));  // open: gt, lt
  Comparator #(.width(4)) comparator_2 (.a(c), .b(4'b1110), .eq(R[1]));  // open: gt, lt
  Comparator #(.width(4)) comparator_3 (.a(c), .b(4'b1101), .eq(R[2]));  // open: gt, lt
  Comparator #(.width(4)) comparator_4 (.a(c), .b(4'b1100), .eq(R[3]));  // open: gt, lt
  Comparator #(.width(4)) comparator_5 (.a(c), .b(4'b1011), .eq(R[4]));  // open: gt, lt
  Adder #(.width(32)) adder_1 (
    .a({{28{1'b0}}, c}), .b({multiplier_1_cout, multiplier_1_out}), .out(adder_1_out), .cin(1'b0),
    .cout(overflow));
  Comparator #(.width(4), .mode("unsigned")) comparator_6 (.a(c), .b(4'b1010), .lt(comparator_6_lt));  // open: gt, eq
  Register #(.width(32)) reg2 (.D(adder_1_out), .en(and2_out), .clk(clk), .Q(affichage), .clr(or_1_out));
  or or_1 (or_1_out, clear, machine1_p7);
  Operation ope0 (.OP(R), .oper(OP));
  and and1 (and1_out, clavieractif, comparator_6_lt);
  and and2 (and2_out, and1_out, machine1_p6);
  // FSM_Entity #(.content("fsm mach1 @[ 50 , 50 , 800 , 500 ] { in c [ 1 ] @[ 50 , 100 , 13 , 15 ] ; in op\n[ 1 ] @[ 50 , 168 , 22 , 15 ] ; out Z [ 1 ] @[ 835 , 194 , 15 , 15 ] ; out Y [\n1 ] @[ 837 , 166 , 13 , 15 ] ; codeWidth = 2 ; reset = S0 ; state S0 = \"01\" @[\n297 , 181 , 30 , 30 ] { commands @[ 250 , 173 , 45 , 36 ] { Y = \"0\" ; Z = \"0\" ;\n} transitions { S0 -> S1 when c == \"1\" @[ 432 , 151 , 61 , 21 ] ; } } state S1\n= \"10\" @[ 610 , 165 , 30 , 30 ] { commands @[ 670 , 180 , 45 , 36 ] { Y = \"0\" ;\nZ = \"1\" ; } transitions { S1 -> S2 when default @[ 698 , 281 , 50 , 21 ] ; } }\nstate S2 = \"11\" @[ 620 , 369 , 30 , 30 ] { commands @[ 680 , 384 , 45 , 36 ] {\nY = \"0\" ; Z = \"0\" ; } transitions { S2 -> S0 when c == \"0\" . op == \"1\" @[ 432 ,\n346 , 139 , 21 ] ; S2 -> S3 when c == \"0\" . op == \"0\" @[ 473 , 482 , 139 , 21 ]\n; } } state S3 = \"00\" @[ 320 , 411 , 30 , 30 ] { commands @[ 365 , 426 , 45 ,\n36 ] { Y = \"1\" ; Z = \"0\" ; } transitions { S3 -> S0 when c == \"0\" . op == \"1\"\n@[ 270 , 343 , 139 , 21 ] ; } } }")) machine1: pin names not known; wires that end beside it: clk, 1'b0, 1'b1, clavieractif, comparator_6_lt, machine1_p6, machine1_p7

  // Other names for the same wires on the sheet: c4bits[3:0] = c; c_t[3:0] = c
endmodule

module Clavier (
  input  Ligne0,
  input  Ligne1,
  input  Ligne2,
  input  Ligne3,
  input  clk,
  input  clearall,
  output [3:0] Clavier,
  output Clavieractif,
  output Colonne0,
  output Colonne1,
  output Colonne2,
  output Colonne3
);

  wire and_1_out, and_2_out, and_3_out, and_4_out, and_5_out, and_6_out, and_7_out, and_8_out, and_9_out,
       and_10_out, and_11_out, and_12_out, and_13_out, and_14_out, and_15_out, bit0, bit1, bit2, bit3,
       comparator_1_gt, or_1_out, or_2_out, or_4_out, or_5_out, or_7_out, or_8_out, or_10_out, or_11_out,
       or_12_out, X;

  // FSM_Entity #(.content("fsm mach0 @[ 50 , 50 , 800 , 500 ] { in x [ 1 ] @[ 50 , 125 , 12 , 15 ] ; out C0\n[ 1 ] @[ 828 , 140 , 22 , 15 ] ; out C1 [ 1 ] @[ 828 , 170 , 22 , 15 ] ; out C2\n[ 1 ] @[ 828 , 202 , 22 , 15 ] ; out C3 [ 1 ] @[ 828 , 232 , 22 , 15 ] ;\ncodeWidth = 2 ; reset = A ; state A = \"00\" @[ 300 , 200 , 30 , 30 ] { commands\n@[ 260 , 156 , 52 , 66 ] { C0 = \"1\" ; C1 = \"0\" ; C2 = \"0\" ; C3 = \"0\" ; }\ntransitions { A -> B when x == \"1\" @[ 400 , 150 , 60 , 21 ] ; } } state B =\n\"01\" @[ 487 , 189 , 30 , 30 ] { commands @[ 534 , 161 , 52 , 66 ] { C0 = \"0\" ;\nC1 = \"1\" ; C2 = \"0\" ; C3 = \"0\" ; } transitions { B -> C when x == \"1\" @[ 579 ,\n281 , 60 , 21 ] ; } } state C = \"10\" @[ 509 , 352 , 30 , 30 ] { commands @[ 560\n, 376 , 52 , 66 ] { C0 = \"0\" ; C1 = \"0\" ; C2 = \"1\" ; C3 = \"0\" ; } transitions {\nC -> D when x == \"1\" @[ 424 , 419 , 60 , 21 ] ; } } state D = \"11\" @[ 300 , 365\n, 30 , 30 ] { commands @[ 269 , 393 , 52 , 66 ] { C0 = \"0\" ; C1 = \"0\" ; C2 =\n\"0\" ; C3 = \"1\" ; } transitions { D -> A when x == \"1\" @[ 249 , 292 , 60 , 21 ]\n; } } }")) machine0: pin names not known; wires that end beside it: clk, clearall, 1'b1, X, Colonne1, Colonne0, Colonne1, Colonne2, Colonne3
  or or_1 (or_1_out, Colonne0, Colonne2, Colonne3);
  or or_2 (or_2_out, Ligne0, Ligne2);
  and and_1 (and_1_out, Colonne1, Ligne1);
  and and_2 (and_2_out, Colonne2, Ligne2);
  and and_3 (and_3_out, Colonne2, Ligne3);
  and and_4 (and_4_out, or_1_out, or_2_out);
  or or_3 (bit0, and_4_out, and_1_out, and_2_out, and_3_out);
  and and_5 (and_5_out, Colonne0, Ligne2);
  and and_6 (and_6_out, Colonne0, Ligne3);
  and and_7 (and_7_out, Colonne2, Ligne3);
  or or_4 (or_4_out, Colonne1, Colonne2, Colonne3);
  or or_5 (or_5_out, Colonne2, Colonne3);
  and and_8 (and_8_out, or_4_out, Ligne0);
  and and_9 (and_9_out, Ligne1, or_5_out);
  and and_10 (and_10_out, Colonne1, Ligne3);
  or or_6 (bit1, and_8_out, and_9_out, and_5_out, and_6_out, and_7_out);
  Comparator #(.width(4), .mode("unsigned")) comparator_1 (
    .a({bit3, bit2, bit1, bit0}), .b(4'b0000), .gt(comparator_1_gt));  // open: eq, lt
  or or_7 (or_7_out, comparator_1_gt, and_10_out);
  not not_1 (X, or_7_out);
  // FSM_Entity #(.content("fsm mach3 @[ 50 , 50 , 800 , 500 ] { in X [ 1 ] @[ 50 , 100 , 13 , 15 ] ; out\nClavieractif [ 1 ] @[ 776 , 148 , 74 , 15 ] ; codeWidth = 2 ; reset = S0 ;\nstate S0 = \"00\" @[ 300 , 200 , 30 , 30 ] { commands @[ 216 , 202 , 104 , 21 ] {\nClavieractif = \"0\" ; } transitions { S0 -> S3 when X == \"0\" @[ 371 , 142 , 61 ,\n21 ] ; } } state S1 = \"01\" @[ 576 , 207 , 30 , 30 ] { commands @[ 621 , 222 ,\n104 , 21 ] { Clavieractif = \"1\" ; } transitions { S1 -> S2 when X == \"1\" @[ 638\n, 392 , 61 , 21 ] ; } } state S2 = \"10\" @[ 416 , 412 , 30 , 30 ] { commands @[\n461 , 427 , 104 , 21 ] { Clavieractif = \"0\" ; } transitions { S2 -> S0 when X\n== \"1\" @[ 314 , 344 , 61 , 21 ] ; } } state S3 = \"11\" @[ 449 , 106 , 30 , 30 ]\n{ commands @[ 494 , 121 , 104 , 21 ] { Clavieractif = \"0\" ; } transitions { S3\n-> S1 when X == \"0\" @[ 570 , 160 , 61 , 21 ] ; } } }")) machine3: pin names not known; wires that end beside it: clk, clearall, 1'b1, X, Clavieractif
  or or_8 (or_8_out, Ligne0, Ligne1, Ligne2, Ligne3);
  and and_11 (and_11_out, Colonne0, Ligne2);
  Register #(.width(4)) regui (.D({bit3, bit2, bit1, bit0}), .en(or_7_out), .clk(clk), .Q(Clavier), .clr(clearall));
  and and_12 (and_12_out, or_8_out, Colonne3);
  or or_9 (bit2, and_12_out, Ligne1, and_11_out);
  or or_10 (or_10_out, Ligne0, Ligne1, Ligne2, Ligne3);
  or or_11 (or_11_out, Colonne1, Colonne2);
  or or_12 (or_12_out, Colonne0, Colonne2);
  and and_13 (and_13_out, or_10_out, Colonne3);
  and and_14 (and_14_out, Ligne2, or_11_out);
  and and_15 (and_15_out, Ligne3, or_12_out);
  or or_13 (bit3, and_13_out, and_14_out, and_15_out);

  // Other names for the same wires on the sheet: C0 = Colonne0; C1 = Colonne1; C2 = Colonne2; C3 = Colonne3;
  //   clear = clearall; L0 = Ligne0; L1 = Ligne1; L2 = Ligne2; L3 = Ligne3
endmodule

module Operation (
  input  [4:0] OP,
  output [1:0] oper
);

  wire [3:0] comparator_1_eq;

  Comparator #(.width(5), .mode("unsigned")) comparator_1 (
    .a(OP), .b(5'b00001), .eq(comparator_1_eq[0]));  // open: gt, lt
  Comparator #(.width(5), .mode("unsigned")) comparator_2 (
    .a(OP), .b(5'b00010), .eq(comparator_1_eq[1]));  // open: gt, lt
  Comparator #(.width(5), .mode("unsigned")) comparator_3 (
    .a(OP), .b(5'b00100), .eq(comparator_1_eq[2]));  // open: gt, lt
  Comparator #(.width(5), .mode("unsigned")) comparator_4 (
    .a(OP), .b(5'b01000), .eq(comparator_1_eq[3]));  // open: gt, lt
  Multiplexer #(.select(4), .width(2), .enable("false")) multiplexer_1 (
    .in0(2'b00), .in1(2'b00), .in2(2'b01), .in3(2'b00), .in4(2'b10), .in5(2'b00), .in6(2'b00), .in7(2'b00),
    .in8(2'b11), .in9(2'b00), .in10(2'b00), .in11(2'b00), .in12(2'b00), .in13(2'b00), .in14(2'b00),
    .in15(2'b00), .out(oper), .sel(comparator_1_eq));
endmodule

module Calculatrice (
);

  wire binairy_to_bcd_converter_1_p2, binairy_to_bcd_converter_2_p2, binairy_to_bcd_converter_3_p2,
       binairy_to_bcd_converter_4_p2, calc_clearall, clav_p3, clav_p4, clav_p5, clav_p6, clav_p7, clav_p8,
       clavi_colonne0, clavi_colonne1, clavi_colonne2, clavi_colonne3, clavierac, clear, clk_out,
       comparator_1_gt, not_1_out, not_2_out, not_3_out, not_6_out, not_7_out, not_8_out, not_9_out;
  wire [3:0] cl_hex1, cl_hex2, cl_hex3, cl_hex4, clavi_clavier;
  wire [31:0] calc_resultat;

  Comparator #(.width(32), .mode("unsigned")) comparator_1 (
    .a(calc_resultat), .b(32'h1fff), .gt(comparator_1_gt));  // open: eq, lt
  not not_1 (not_1_out, clavierac);
  and and_1 (clear, not_1_out, comparator_1_gt);
  Traducteur cl (.Resultat(calc_resultat), .Hex4(cl_hex4), .Hex3(cl_hex3), .Hex2(cl_hex2), .Hex1(cl_hex1));
  // Binairy_to_BCD_converter #(.binvalue(4)) binairy_to_bcd_converter_1: pin names not known; wires that end beside it: cl_hex4, binairy_to_bcd_converter_1_p2
  not not_2 (not_2_out, clavi_colonne0);
  not not_3 (not_3_out, clavi_colonne1);
  // KeyPad clav: pin names not known; wires that end beside it: not_2_out, not_3_out, clav_p3, clav_p4, clav_p5, clav_p6, clav_p7, clav_p8
  // BCD_to_7_Segment_decoder bcd_to_7_segment_decoder_1: pin names not known; wires that end beside it: binairy_to_bcd_converter_1_p2
  _7_Segment_Display Hex4 ();  // open: g, f, a, b, e, d, c, dp
  not not_4 (clav_p3, clavi_colonne2);
  not not_5 (clav_p4, clavi_colonne3);
  not not_6 (not_6_out, clav_p5);
  not not_7 (not_7_out, clav_p6);
  not not_8 (not_8_out, clav_p7);
  not not_9 (not_9_out, clav_p8);
  // Binairy_to_BCD_converter #(.binvalue(4)) binairy_to_bcd_converter_2: pin names not known; wires that end beside it: cl_hex3, binairy_to_bcd_converter_2_p2
  Clock #(.highDuration(2), .lowDuration(2)) clk (.out(clk_out));
  _7_Segment_Display Hex3 ();  // open: g, f, a, b, e, d, c, dp
  // BCD_to_7_Segment_decoder bcd_to_7_segment_decoder_2: pin names not known; wires that end beside it: binairy_to_bcd_converter_2_p2
  Clavier clavi (
    .Ligne0(not_6_out), .Ligne1(not_7_out), .Ligne2(not_8_out), .Ligne3(not_9_out), .clk(clk_out),
    .clearall(calc_clearall), .Clavier(clavi_clavier), .Clavieractif(clavierac), .Colonne0(clavi_colonne0),
    .Colonne1(clavi_colonne1), .Colonne2(clavi_colonne2), .Colonne3(clavi_colonne3));
  // Binairy_to_BCD_converter #(.binvalue(4)) binairy_to_bcd_converter_3: pin names not known; wires that end beside it: cl_hex2, binairy_to_bcd_converter_3_p2
  // BCD_to_7_Segment_decoder bcd_to_7_segment_decoder_3: pin names not known; wires that end beside it: binairy_to_bcd_converter_3_p2
  _7_Segment_Display Hex2 ();  // open: g, f, a, b, e, d, c, dp
  // Binairy_to_BCD_converter #(.binvalue(4)) binairy_to_bcd_converter_4: pin names not known; wires that end beside it: cl_hex1, binairy_to_bcd_converter_4_p2
  GestionCalcul calc (
    .clavier(clavi_clavier), .clavieractif(clavierac), .clk(clk_out), .clear(clear),
    .Resultat(calc_resultat), .clearall(calc_clearall));
  // BCD_to_7_Segment_decoder bcd_to_7_segment_decoder_4: pin names not known; wires that end beside it: binairy_to_bcd_converter_4_p2
  _7_Segment_Display Hex1 ();  // open: g, f, a, b, e, d, c, dp
endmodule

module Traducteur (
  input  [31:0] Resultat,
  output [3:0] Hex4,
  output [3:0] Hex3,
  output [3:0] Hex2,
  output [3:0] Hex1
);

  // Binairy_to_BCD_converter #(.binvalue(13)) binairy_to_bcd_converter_1: pin names not known; wires that end beside it: Resultat[12:0], Hex4, Hex3, Hex2, Hex1
endmodule

module UAL (
  input  [31:0] A,
  input  [31:0] B,
  input  [1:0] OP,
  output [31:0] Resultat
);

  wire [30:0] multiplier_1_out;
  wire [31:0] adder_1_out, subtractor_1_out;
  wire [31:31] undriven;

  Adder #(.width(32)) adder_1 (.a(A), .b(B), .out(adder_1_out), .cin(1'b0));  // open: cout
  Subtractor #(.width(32)) subtractor_1 (.a(B), .b(A), .out(subtractor_1_out), .bin(1'b0));  // open: bout
  Multiplier #(.width(31)) multiplier_1 (
    .a(A[30:0]), .b(B[30:0]), .out(multiplier_1_out), .cin({31{1'b0}}));  // open: cout
  Multiplexer #(.select(2), .width(32), .enable("false")) multiplexer_1 (
    .in0(adder_1_out), .in1(subtractor_1_out), .in2({undriven[31], multiplier_1_out}), .in3(A),
    .out(Resultat), .sel(OP));
endmodule
