// Logisim project TP78_test5.circ as structural Verilog: 9 circuits, main circuit SYSTEME
module UC (
  input  clk,
  input  clearall,
  input  Req,
  input  [3:0] C,
  input  [1:0] OP,
  output WEA,
  output WEB,
  output WEC,
  output WEOP,
  output [1:0] OPERATEUR,
  output affich,
  output clear,
  output clearA,
  output clearC,
  output Ack
);

  wire comparator_1_eq, comparator_1_gt, comparator_1_lt, comparator_2_gt, Unite_Commande_p17;

  Comparator #(.width(4), .mode("unsigned")) comparator_1 (
    .a(C), .b(4'b1010), .gt(comparator_1_gt), .eq(comparator_1_eq), .lt(comparator_1_lt));
  Comparator #(.width(4), .mode("unsigned")) comparator_2 (.a(C), .b(4'b1100), .gt(comparator_2_gt));  // open: eq, lt
  // FSM_Entity #(.content("fsm UnitC @[ 50 , 50 , 800 , 500 ] { in Req [ 1 ] @[ 50 , 100 , 30 , 15 ] ; in C\n[ 4 ] @[ 50 , 132 , 44 , 15 ] ; in sup10 [ 1 ] @[ 50 , 184 , 45 , 15 ] ; in\ninf10 [ 1 ] @[ 50 , 247 , 37 , 15 ] ; in sup12 [ 1 ] @[ 50 , 273 , 45 , 15 ] ;\nin equ10 [ 1 ] @[ 50 , 214 , 46 , 15 ] ; in OP [ 2 ] @[ 50 , 310 , 53 , 15 ] ;\nout WEA [ 1 ] @[ 817 , 117 , 33 , 15 ] ; out WEB [ 1 ] @[ 817 , 165 , 33 , 15 ]\n; out WEC [ 1 ] @[ 817 , 140 , 33 , 15 ] ; out WEOP [ 1 ] @[ 808 , 189 , 42 ,\n15 ] ; out OPERATEUR [ 2 ] @[ 741 , 215 , 109 , 15 ] ; out affich [ 1 ] @[ 810\n, 241 , 40 , 15 ] ; out clear [ 1 ] @[ 813 , 267 , 37 , 15 ] ; out clearA [ 1 ]\n@[ 805 , 294 , 45 , 15 ] ; out Ack [ 1 ] @[ 822 , 88 , 28 , 15 ] ; out clearC [\n1 ] @[ 805 , 321 , 45 , 15 ] ; codeWidth = 4 ; reset = S0 ; state S0 = \"0000\"\n@[ 106 , 90 , 30 , 30 ] { commands @[ 138 , 138 , 75 , 141 ] { Ack = \"0\" ; WEA\n= \"0\" ; WEB = \"0\" ; WEC = \"0\" ; WEOP = \"0\" ; affich = \"0\" ; clear = \"0\" ;\nclearA = \"0\" ; clearC = \"0\" ; } transitions { S0 -> S1 when Req == \"1\" @[ 197 ,\n120 , 78 , 21 ] ; } } state S1 = \"0001\" @[ 277 , 89 , 30 , 30 ] { commands @[\n292 , 83 , 63 , 21 ] { WEC = \"1\" ; } transitions { S1 -> S2 when default @[ 345\n, 117 , 50 , 21 ] ; } } state S2 = \"0010\" @[ 394 , 84 , 30 , 30 ] { commands @[\n439 , 99 , 63 , 36 ] { Ack = \"1\" ; WEC = \"0\" ; } transitions { S2 -> S3 when\nReq == \"0\" @[ 510 , 116 , 78 , 21 ] ; } } state S3 = \"0011\" @[ 604 , 88 , 30 ,\n30 ] { commands @[ 649 , 103 , 58 , 21 ] { Ack = \"0\" ; } transitions { S3 -> S0\nwhen equ10 == \"1\" . inf10 == \"0\" . sup10 == \"0\" @[ 350 , 176 , 288 , 21 ] ; S3\n-> S4 when equ10 == \"0\" . inf10 == \"1\" . sup10 == \"0\" @[ 512 , 202 , 288 , 21 ]\n; S3 -> S5 when equ10 == \"0\" . inf10 == \"0\" . sup10 == \"1\" @[ 648 , 153 , 288 ,\n21 ] ; } } state S4 = \"0100\" @[ 423 , 226 , 30 , 30 ] { commands @[ 468 , 241 ,\n63 , 21 ] { WEA = \"1\" ; } transitions { S4 -> S0 when default @[ 319 , 197 , 50\n, 21 ] ; } } state S5 = \"0101\" @[ 651 , 220 , 30 , 30 ] { commands @[ 696 , 235\n, 30 , 20 ] { } transitions { S5 -> S6 when C == \"1011\" @[ 574 , 285 , 86 , 21\n] ; S5 -> S7 when C /= \"1011\" @[ 680 , 298 , 80 , 21 ] ; } } state S6 = \"0110\"\n@[ 417 , 307 , 30 , 30 ] { commands @[ 462 , 322 , 67 , 21 ] { clear = \"1\" ; }\ntransitions { S6 -> S0 when default @[ 256 , 226 , 50 , 21 ] ; } } state S7 =\n\"0111\" @[ 656 , 346 , 30 , 30 ] { commands @[ 701 , 361 , 63 , 21 ] { WEB = \"1\"\n; } transitions { S7 -> S8 when default @[ 685 , 428 , 50 , 21 ] ; } } state S8\n= \"1000\" @[ 657 , 473 , 30 , 30 ] { commands @[ 712 , 484 , 75 , 36 ] { WEB =\n\"0\" ; clearA = \"1\" ; } transitions { S8 -> S13 when C == \"1100\" @[ 317 , 517 ,\n86 , 21 ] ; S8 -> S9 when C /= \"1100\" @[ 455 , 444 , 80 , 21 ] ; } } state S9 =\n\"1001\" @[ 316 , 413 , 30 , 30 ] { commands @[ 284 , 381 , 108 , 36 ] {\nOPERATEUR = OP ; WEOP = \"1\" ; } transitions { S9 -> S13 when default @[ 201 ,\n456 , 50 , 21 ] ; } } state S13 = \"1101\" @[ 92 , 442 , 30 , 30 ] { commands @[\n85 , 476 , 75 , 66 ] { WEOP = \"0\" ; affich = \"1\" ; clearA = \"0\" ; clearC = \"1\"\n; } transitions { S13 -> S0 when Req == \"1\" @[ 132 , 300 , 78 , 21 ] ; } } }")) Unite_Commande: pin names not known; wires that end beside it: clk, clearall, 1'b1, Req, C, comparator_1_gt, comparator_1_lt, comparator_2_gt, comparator_1_eq, OP, WEA, WEB, WEC, WEOP, OPERATEUR, affich, Unite_Commande_p17, clearA, Ack, clearC
  or or_1 (clear, Unite_Commande_p17, clearall);
endmodule

module UT (
  input  clk,
  input  [3:0] Keypad,
  input  WEA,
  input  WEB,
  input  WEC,
  input  WEOP,
  input  [1:0] OPERATEUR,
  input  affich,
  input  clear,
  input  clearA,
  input  clearC,
  output [31:0] Affichage,
  output [3:0] Creg,
  output [1:0] OP
);

  wire or_1_out, or_2_out;
  wire [1:0] register_1_q;
  wire [15:0] A_q, multiplier_1_cout, multiplier_1_out;
  wire [31:0] adder_1_out, B_q, Calcul_resultat;
  wire [31:16] A_q_2;

  Register #(.width(4)) C (.D(Keypad), .en(WEC), .clk(clk), .Q(Creg), .clr(or_1_out));
  or or_1 (or_1_out, clear, clearC);
  Multiplexer #(.select(2), .width(2), .enable("false")) multiplexer_1 (
    .in0(2'b11), .in1(2'b10), .in2(2'b01), .in3(2'b00), .out(OP), .sel(Creg[1:0]));
  Multiplier #(.width(16)) multiplier_1 (
    .a(A_q), .b(16'ha), .out(multiplier_1_out), .cin({16{1'b0}}), .cout(multiplier_1_cout));
  Adder #(.width(32)) adder_1 (
    .a({{28{1'b0}}, Creg}), .b({multiplier_1_cout, multiplier_1_out}), .out(adder_1_out), .cin(1'b0));  // open: cout
  Register #(.width(32)) A (.D(adder_1_out), .en(WEA), .clk(clk), .Q({A_q_2, A_q}), .clr(or_2_out));
  or or_2 (or_2_out, clear, clearA);
  Register #(.width(2)) register_1 (.D(OPERATEUR), .en(WEOP), .clk(clk), .Q(register_1_q), .clr(clear));
  Multiplexer #(.width(32), .enable("false")) multiplexer_2 (
    .in0({A_q_2, A_q}), .in1(B_q), .out(Affichage), .sel(affich));
  UAL Calcul (.A({A_q_2, A_q}), .B(B_q), .OP(register_1_q), .Resultat(Calcul_resultat));
  Register #(.width(32)) B (.D(Calcul_resultat), .en(WEB), .clk(clk), .Q(B_q), .clr(clear));
endmodule

module Clavier (
  input  Ligne0,
  input  Ligne1,
  input  Ligne2,
  input  Ligne3,
  input  clk,
  input  clearall,
  input  Ack,
  output [3:0] Keyval,
  output Colonne0,
  output Colonne1,
  output Colonne2,
  output Colonne3,
  output Req
);

  wire and_1_out, and_2_out, and_3_out, and_4_out, and_5_out, and_6_out, and_7_out, and_8_out, and_9_out,
       and_10_out, and_11_out, and_12_out, and_13_out, and_14_out, or_1_out, or_2_out, or_4_out, or_5_out,
       or_7_out, or_8_out, or_10_out, or_11_out, or_12_out, X;

  // FSM_Entity #(.content("fsm mach0 @[ 50 , 50 , 800 , 500 ] { in x [ 1 ] @[ 50 , 125 , 12 , 15 ] ; out C0\n[ 1 ] @[ 828 , 140 , 22 , 15 ] ; out C1 [ 1 ] @[ 828 , 170 , 22 , 15 ] ; out C2\n[ 1 ] @[ 828 , 202 , 22 , 15 ] ; out C3 [ 1 ] @[ 828 , 232 , 22 , 15 ] ;\ncodeWidth = 2 ; reset = A ; state A = \"00\" @[ 300 , 200 , 30 , 30 ] { commands\n@[ 260 , 156 , 52 , 66 ] { C0 = \"1\" ; C1 = \"0\" ; C2 = \"0\" ; C3 = \"0\" ; }\ntransitions { A -> B when x == \"1\" @[ 400 , 150 , 60 , 21 ] ; } } state B =\n\"01\" @[ 487 , 189 , 30 , 30 ] { commands @[ 534 , 161 , 52 , 66 ] { C0 = \"0\" ;\nC1 = \"1\" ; C2 = \"0\" ; C3 = \"0\" ; } transitions { B -> C when x == \"1\" @[ 579 ,\n281 , 60 , 21 ] ; } } state C = \"10\" @[ 509 , 352 , 30 , 30 ] { commands @[ 560\n, 376 , 52 , 66 ] { C0 = \"0\" ; C1 = \"0\" ; C2 = \"1\" ; C3 = \"0\" ; } transitions {\nC -> D when x == \"1\" @[ 424 , 419 , 60 , 21 ] ; } } state D = \"11\" @[ 300 , 365\n, 30 , 30 ] { commands @[ 269 , 393 , 52 , 66 ] { C0 = \"0\" ; C1 = \"0\" ; C2 =\n\"0\" ; C3 = \"1\" ; } transitions { D -> A when x == \"1\" @[ 249 , 292 , 60 , 21 ]\n; } } }")) machine0: pin names not known; wires that end beside it: clk, clearall, 1'b1, X, Colonne0, Colonne1, Colonne2, Colonne3
  or or_1 (or_1_out, Colonne0, Colonne2, Colonne3);
  or or_2 (or_2_out, Ligne0, Ligne2);
  and and_1 (and_1_out, Colonne1, Ligne1);
  and and_2 (and_2_out, Colonne2, Ligne2);
  and and_3 (and_3_out, Colonne2, Ligne3);
  and and_4 (and_4_out, or_1_out, or_2_out);
  or or_3 (Keyval[0], and_4_out, and_1_out, and_2_out, and_3_out);
  and and_5 (and_5_out, Colonne0, Ligne2);
  and and_6 (and_6_out, Colonne0, Ligne3);
  and and_7 (and_7_out, Colonne2, Ligne3);
  or or_4 (or_4_out, Colonne1, Colonne2, Colonne3);
  or or_5 (or_5_out, Colonne2, Colonne3);
  and and_8 (and_8_out, or_4_out, Ligne0);
  and and_9 (and_9_out, Ligne1, or_5_out);
  or or_6 (Keyval[1], and_8_out, and_9_out, and_5_out, and_6_out, and_7_out);
  or or_7 (or_7_out, Ligne0, Ligne1, Ligne2, Ligne3);
  or or_8 (or_8_out, Ligne0, Ligne1, Ligne2, Ligne3);
  not not_1 (X, or_7_out);
  and and_10 (and_10_out, Colonne0, Ligne2);
  and and_11 (and_11_out, or_8_out, Colonne3);
  or or_9 (Keyval[2], and_11_out, Ligne1, and_10_out);
  HandShake HS (.clk(clk), .clear(clearall), .Ack(Ack), .clavieractif(or_7_out), .Req(Req));
  or or_10 (or_10_out, Ligne0, Ligne1, Ligne2, Ligne3);
  or or_11 (or_11_out, Colonne1, Colonne2);
  or or_12 (or_12_out, Colonne0, Colonne2);
  and and_12 (and_12_out, or_10_out, Colonne3);
  and and_13 (and_13_out, Ligne2, or_11_out);
  and and_14 (and_14_out, Ligne3, or_12_out);
  or or_13 (Keyval[3], and_12_out, and_13_out, and_14_out);

  // Other names for the same wires on the sheet: C0 = Colonne0; C1 = Colonne1; C2 = Colonne2; C3 = Colonne3;
  //   clear = clearall; bit0 = Keyval[0]; bit1 = Keyval[1]; bit2 = Keyval[2]; bit3 = Keyval[3]; L0 = Ligne0;
  //   L1 = Ligne1; L2 = Ligne2; L3 = Ligne3
endmodule

module Operation (
  input  [4:0] OP,
  output [1:0] oper
);

  wire [3:0] comparator_1_eq;

  Comparator #(.width(5), .mode("unsigned")) comparator_1 (
    .a(OP), .b(5'b00001), .eq(comparator_1_eq[0]));  // open: gt, lt
  Comparator #(.width(5), .mode("unsigned")) comparator_2 (
    .a(OP), .b(5'b00010), .eq(comparator_1_eq[1]));  // open: gt, lt
  Comparator #(.width(5), .mode("unsigned")) comparator_3 (
    .a(OP), .b(5'b00100), .eq(comparator_1_eq[2]));  // open: gt, lt
  Comparator #(.width(5), .mode("unsigned")) comparator_4 (
    .a(OP), .b(5'b01000), .eq(comparator_1_eq[3]));  // open: gt, lt
  Multiplexer #(.select(4), .width(2), .enable("false")) multiplexer_1 (
    .in0(2'b00), .in1(2'b00), .in2(2'b01), .in3(2'b00), .in4(2'b10), .in5(2'b00), .in6(2'b00), .in7(2'b00),
    .in8(2'b11), .in9(2'b00), .in10(2'b00), .in11(2'b00), .in12(2'b00), .in13(2'b00), .in14(2'b00),
    .in15(2'b00), .out(oper), .sel(comparator_1_eq));
endmodule

module SYSTEME (
  input  cl
);

  wire binairy_to_bcd_converter_1_p2, binairy_to_bcd_converter_2_p1, binairy_to_bcd_converter_3_p1,
       binairy_to_bcd_converter_4_p1, Calto_ack, clav_p1, clav_p2, clav_p3, clav_p4, clav_p5, clav_p6,
       clav_p7, clav_p8, clk, comparator_1_gt, not_1_out, Req;
  wire [3:0] Clavi_keyval, Decod_hex1, Decod_hex2, Decod_hex3, Decod_hex4;
  wire [31:0] Calto_affichage;

  // KeyPad clav: pin names not known; wires that end beside it: clav_p1, clav_p2, clav_p3, clav_p4, clav_p5, clav_p6, clav_p7, clav_p8
  Clock #(.highDuration(2), .lowDuration(2)) u_clk (.out(clk));
  Comparator #(.width(32), .mode("unsigned")) comparator_1 (
    .a(Calto_affichage), .b(32'h1fff), .gt(comparator_1_gt));  // open: eq, lt
  not not_1 (not_1_out, Req);
  // AND_Gate and_1 has open pins: in0=not_1_out, in1=comparator_1_gt, out=open
  Decodeur Decod (
    .Resultat(Calto_affichage), .Hex4(Decod_hex4), .Hex3(Decod_hex3), .Hex2(Decod_hex2), .Hex1(Decod_hex1));
  Clavier Clavi (
    .Ligne0(clav_p5), .Ligne1(clav_p6), .Ligne2(clav_p7), .Ligne3(clav_p8), .clk(clk), .clearall(cl),
    .Ack(Calto_ack), .Keyval(Clavi_keyval), .Colonne0(clav_p1), .Colonne1(clav_p2), .Colonne2(clav_p3),
    .Colonne3(clav_p4), .Req(Req));
  // Binairy_to_BCD_converter #(.binvalue(4)) binairy_to_bcd_converter_1: pin names not known; wires that end beside it: Decod_hex4, binairy_to_bcd_converter_1_p2
  // _7_Segment_Display Hex4: pin names not known; wires that end beside it: binairy_to_bcd_converter_1_p2, Decod_hex3
  // BCD_to_7_Segment_decoder bcd_to_7_segment_decoder_1: pin names not known
  // Binairy_to_BCD_converter #(.binvalue(4)) binairy_to_bcd_converter_2: pin names not known; wires that end beside it: binairy_to_bcd_converter_2_p1
  // _7_Segment_Display Hex3: pin names not known; wires that end beside it: binairy_to_bcd_converter_2_p1, Decod_hex2
  // BCD_to_7_Segment_decoder bcd_to_7_segment_decoder_2: pin names not known
  Calculatrice Calto (
    .clk(clk), .Keypad(Clavi_keyval), .Req(Req), .clearall(cl), .Affichage(Calto_affichage), .Ack(Calto_ack));
  // Binairy_to_BCD_converter #(.binvalue(4)) binairy_to_bcd_converter_3: pin names not known; wires that end beside it: binairy_to_bcd_converter_3_p1
  // _7_Segment_Display Hex2: pin names not known; wires that end beside it: binairy_to_bcd_converter_3_p1, Decod_hex1
  // BCD_to_7_Segment_decoder bcd_to_7_segment_decoder_3: pin names not known
  // Binairy_to_BCD_converter #(.binvalue(4)) binairy_to_bcd_converter_4: pin names not known; wires that end beside it: binairy_to_bcd_converter_4_p1
  // BCD_to_7_Segment_decoder bcd_to_7_segment_decoder_4: pin names not known; wires that end beside it: binairy_to_bcd_converter_4_p1
  _7_Segment_Display Hex1 ();  // open: g, f, a, b, e, d, c, dp

  // Other names for the same wires on the sheet: clear = cl
endmodule

module Decodeur (
  input  [31:0] Resultat,
  output [3:0] Hex4,
  output [3:0] Hex3,
  output [3:0] Hex2,
  output [3:0] Hex1
);

  // Binairy_to_BCD_converter #(.binvalue(13)) binairy_to_bcd_converter_1: pin names not known; wires that end beside it: Resultat[12:0], Hex4, Hex3, Hex2, Hex1
endmodule

module UAL (
  input  [31:0] A,
  input  [31:0] B,
  input  [1:0] OP,
  output [31:0] Resultat
);

  wire [30:0] multiplier_1_out;
  wire [31:0] adder_1_out, nand_1_out, subtractor_1_out;

  Adder #(.width(32)) adder_1 (.a(A), .b(B), .out(adder_1_out), .cin(1'b0));  // open: cout
  Subtractor #(.width(32)) subtractor_1 (.a(B), .b(A), .out(subtractor_1_out), .bin(1'b0));  // open: bout
  Multiplier #(.width(31)) multiplier_1 (
    .a(A[30:0]), .b(B[30:0]), .out(multiplier_1_out), .cin({31{1'b0}}));  // open: cout
  assign nand_1_out = ~(A & B);  // NAND_Gate nand_1, 32 bits wide
  Multiplexer #(.select(2), .width(32), .enable("false")) multiplexer_1 (
    .in0(adder_1_out), .in1(subtractor_1_out), .in2({1'b0, multiplier_1_out}), .in3(nand_1_out),
    .out(Resultat), .sel(OP));
endmodule

module Calculatrice (
  input  clk,
  input  [3:0] Keypad,
  input  Req,
  input  clearall,
  output [31:0] Affichage,
  output Ack
);

  wire Commande_affich, Commande_clear, Commande_cleara, Commande_clearc, Commande_wea, Commande_web,
       Commande_wec, Commande_weop;
  wire [1:0] Commande_operateur, Traitement_op;
  wire [3:0] Traitement_creg;

  UC Commande (
    .clk(clk), .clearall(clearall), .Req(Req), .C(Traitement_creg), .OP(Traitement_op), .WEA(Commande_wea),
    .WEB(Commande_web), .WEC(Commande_wec), .WEOP(Commande_weop), .OPERATEUR(Commande_operateur),
    .affich(Commande_affich), .clear(Commande_clear), .clearA(Commande_cleara), .clearC(Commande_clearc),
    .Ack(Ack));
  UT Traitement (
    .clk(clk), .Keypad(Keypad), .WEA(Commande_wea), .WEB(Commande_web), .WEC(Commande_wec),
    .WEOP(Commande_weop), .OPERATEUR(Commande_operateur), .affich(Commande_affich), .clear(Commande_clear),
    .clearA(Commande_cleara), .clearC(Commande_clearc), .Affichage(Affichage), .Creg(Traitement_creg),
    .OP(Traitement_op));
endmodule

module HandShake (
  input  clk,
  input  clear,
  input  Ack,
  input  clavieractif,
  output Req
);

  // FSM_Entity #(.content("fsm HS @[ 50 , 50 , 800 , 500 ] { in Ack [ 1 ] @[ 50 , 100 , 28 , 15 ] ; in\nclavierac [ 1 ] @[ 50 , 163 , 61 , 15 ] ; out Req [ 1 ] @[ 820 , 140 , 30 , 15\n] ; codeWidth = 2 ; reset = S0 ; state S0 = \"00\" @[ 224 , 181 , 30 , 30 ] {\ncommands @[ 269 , 196 , 60 , 21 ] { Req = \"0\" ; } transitions { S0 -> S1 when\nclavierac == \"1\" @[ 329 , 210 , 109 , 21 ] ; } } state S1 = \"01\" @[ 465 , 180 ,\n30 , 30 ] { commands @[ 510 , 195 , 60 , 21 ] { Req = \"1\" ; } transitions { S1\n-> S2 when Ack == \"1\" @[ 496 , 308 , 76 , 21 ] ; } } state S2 = \"10\" @[ 465 ,\n405 , 30 , 30 ] { commands @[ 510 , 420 , 60 , 21 ] { Req = \"0\" ; } transitions\n{ S2 -> S3 when Ack == \"0\" @[ 336 , 435 , 76 , 21 ] ; } } state S3 = \"11\" @[\n224 , 404 , 30 , 30 ] { commands @[ 198 , 443 , 60 , 21 ] { Req = \"0\" ; }\ntransitions { S3 -> S0 when clavierac == \"0\" @[ 254 , 306 , 109 , 21 ] ; } } }")) Handshake: pin names not known; wires that end beside it: clk, clear, 1'b1, Ack, clavieractif, Req
endmodule
