// Logisim project bugs_out.circ as structural Verilog: 1 circuit, main circuit main
module main (
  input  in_1,
  input  in_2,
  input  in_3
);

  wire clock_1_out, fsm_entity_1_p4;

  Clock clock_1 (.out(clock_1_out));
  // FSM_Entity #(.content("fsm example @[ 50 , 50 , 800 , 500 ] { out Y [ 1 ] @[ 836 , 242 , 14 , 15 ] ;\ncodeWidth = 2 ; reset = S0 ; state S0 = \"01\" @[ 297 , 181 , 30 , 30 ] {\ncommands @[ 266 , 173 , 30 , 20 ] { } transitions { S0 -> S1 when default @[\n397 , 143 , 50 , 22 ] ; } } state S1 = \"10\" @[ 470 , 186 , 30 , 30 ] { commands\n@[ 512 , 191 , 44 , 22 ] { Y = \"1\" ; } transitions { S1 -> S0 when default @[\n385 , 249 , 50 , 22 ] ; } } }")) fsm_entity_1: pin names not known; wires that end beside it: clock_1_out, in_1, in_2, fsm_entity_1_p4, fsm_entity_1_p4, in_3
endmodule
