// Logisim project calc.circ as structural Verilog: 3 circuits, main circuit main
module main (
  input  [3:0] in_1,
  input  in_2,
  input  in_3
);

  wire clk_out, fsm_entity_1_p6, fsm_entity_1_p8, fsm_entity_1_p9;
  wire [1:0] fsm_entity_1_p7;
  wire [30:0] multiplier_1_out;
  wire [31:0] adder_1_out, adder_2_out, and_1_out, bit_extender_1_out, bit_extender_2_out, multiplexer_1_out,
       multiplexer_2_out, or_1_out, register_1_q, register_2_q, subtractor_1_out;

  Clock clk (.out(clk_out));
  // FSM_Entity #(.content("fsm example @[ 50 , 50 , 800 , 500 ] { in keypad [ 4 ] @[ 50 , 164 , 79 , 15 ] ;\nin A [ 1 ] @[ 50 , 212 , 15 , 15 ] ; out doDisplay [ 1 ] @[ 781 , 140 , 69 , 15\n] ; out selectOp [ 2 ] @[ 761 , 290 , 89 , 15 ] ; out wea [ 1 ] @[ 820 , 217 ,\n30 , 15 ] ; out web [ 1 ] @[ 819 , 197 , 31 , 15 ] ; codeWidth = 2 ; reset = S0\n; state S0 = \"01\" @[ 244 , 173 , 30 , 30 ] { commands @[ 272 , 188 , 99 , 38 ]\n{ doDisplay = \"1\" ; wea = \"0\" ; } transitions { S0 -> S1 when A . keypad /=\n\"0010\" @[ 287 , 105 , 139 , 22 ] ; } } state S1 = \"00\" @[ 478 , 179 , 30 , 30 ]\n{ commands @[ 521 , 194 , 60 , 22 ] { wea = \"1\" ; } transitions { S1 -> S0 when\ndefault @[ 358 , 255 , 50 , 22 ] ; } } }")) fsm_entity_1: pin names not known; wires that end beside it: clk_out, in_3, 1'b1, in_1, in_2, fsm_entity_1_p6, fsm_entity_1_p7, fsm_entity_1_p8, fsm_entity_1_p9
  Multiplier #(.width(31)) multiplier_1 (.a(register_1_q[30:0]), .b(31'ha), .out(multiplier_1_out));  // open: cin, cout
  assign bit_extender_1_out = {{28{1'b0}}, in_1};  // Bit_Extender bit_extender_1
  assign bit_extender_2_out = {{1{multiplier_1_out[30]}}, multiplier_1_out};  // Bit_Extender bit_extender_2
  Register #(.width(32)) register_1 (
    .D(adder_1_out), .en(fsm_entity_1_p8), .clk(clk_out), .Q(register_1_q), .clr(in_3));
  Adder #(.width(32)) adder_1 (.a(bit_extender_2_out), .b(bit_extender_1_out), .out(adder_1_out));  // open: cin, cout
  Register #(.width(32)) register_2 (
    .D(multiplexer_2_out), .en(fsm_entity_1_p9), .clk(clk_out), .Q(register_2_q));  // open: clr
  Multiplexer #(.width(32), .enable("false")) multiplexer_1 (
    .in0(register_2_q), .in1(register_1_q), .out(multiplexer_1_out), .sel(fsm_entity_1_p6));
  Hex_Digit_Display hex_digit_display_1 (.value(multiplexer_1_out[27:24]));  // open: dp
  Hex_Digit_Display hex_digit_display_2 (.value(multiplexer_1_out[31:28]));  // open: dp
  Adder #(.width(32)) adder_2 (.a(register_1_q), .b(register_2_q), .out(adder_2_out));  // open: cin, cout
  Subtractor #(.width(32)) subtractor_1 (
    .a(register_1_q), .b(register_2_q), .out(subtractor_1_out));  // open: bin, bout
  assign and_1_out = register_1_q & register_2_q;  // AND_Gate and_1, 32 bits wide
  assign or_1_out = register_1_q | register_2_q;  // OR_Gate or_1, 32 bits wide
  Hex_Digit_Display hex_digit_display_3 (.value(multiplexer_1_out[23:20]));  // open: dp
  Hex_Digit_Display hex_digit_display_4 (.value(multiplexer_1_out[19:16]));  // open: dp
  Hex_Digit_Display hex_digit_display_5 (.value(multiplexer_1_out[15:12]));  // open: dp
  Hex_Digit_Display hex_digit_display_6 (.value(multiplexer_1_out[11:8]));  // open: dp
  Hex_Digit_Display hex_digit_display_7 (.value(multiplexer_1_out[7:4]));  // open: dp
  Multiplexer #(.select(2), .width(32), .enable("false")) multiplexer_2 (
    .in0(adder_2_out), .in1(subtractor_1_out), .in2(and_1_out), .in3(or_1_out), .out(multiplexer_2_out),
    .sel(fsm_entity_1_p7));
  Hex_Digit_Display hex_digit_display_8 (.value(multiplexer_1_out[3:0]));  // open: dp
endmodule

module DECODE (
  input  L1,
  input  L2,
  input  L3,
  input  L4,
  output Hit,
  output [1:0] RowId
);

  wire not_1_out, not_2_out, not_3_out, not_4_out;

  not not_1 (not_1_out, L1);
  not not_2 (not_2_out, L2);
  not not_3 (not_3_out, L3);
  not not_4 (not_4_out, L4);
  or or_1 (Hit, L4, L3, L2, L1);
  or or_2 (RowId[1], L4, L3);
  or or_3 (RowId[0], L4, L2);
endmodule

module sdfg (
  input  in_1,
  output out_2
);

  buf buffer_1 (out_2, in_1);
endmodule
