// Logisim project calc2auto.circ as structural Verilog: 3 circuits, main circuit main
module main (
  input  in_1
);

  wire decode_1_hit, decoder_1_out0, decoder_1_out1, decoder_1_out2, decoder_1_out3, fsm_entity_1_p2,
       keypad_1_p5, keypad_1_p6, keypad_1_p7, keypad_1_p8, UC_p6, UC_p8, UC_p9;
  wire [1:0] decode_1_rowid, fsm_entity_1_p7, UC_p7;
  wire [30:0] multiplier_1_out, register_1_q;
  wire [31:0] adder_1_out, adder_2_out, and_1_out, bit_extender_1_out, bit_extender_2_out, multiplexer_1_out,
       multiplexer_2_out, or_1_out, register_2_q, subtractor_1_out;
  wire [31:31] register_1_q_2;

  Decoder #(.select(2), .enable("false")) decoder_1 (
    .out0(decoder_1_out0), .out1(decoder_1_out1), .out2(decoder_1_out2), .out3(decoder_1_out3),
    .sel(fsm_entity_1_p7));
  // KeyPad keypad_1: pin names not known; wires that end beside it: decoder_1_out0, decoder_1_out1, decoder_1_out2, decoder_1_out3, keypad_1_p5, keypad_1_p6, keypad_1_p7, keypad_1_p8
  DECODE decode_1 (
    .Hit(decode_1_hit), .L4(keypad_1_p8), .L3(keypad_1_p7), .L2(keypad_1_p6), .L1(keypad_1_p5),
    .RowId(decode_1_rowid));
  // FSM_Entity #(.content("fsm KeyPadCTRL @[ 50 , 50 , 800 , 500 ] { in rowId [ 2 ] @[ 50 , 126 , 69 , 15 ]\n; in active [ 1 ] @[ 50 , 171 , 43 , 15 ] ; out C [ 2 ] @[ 807 , 140 , 43 , 15\n] ; out Hit [ 1 ] @[ 825 , 241 , 25 , 15 ] ; out key [ 4 ] @[ 794 , 447 , 56 ,\n15 ] ; codeWidth = 4 ; reset = S0_key ; state S0_key = \"0001\" @[ 500 , 183 , 30\n, 30 ] { commands @[ 547 , 197 , 74 , 38 ] { C = \"00\" ; Hit = active ; }\ntransitions { S0_key -> S2_key when / active @[ 567 , 271 , 58 , 22 ] ; } }\nstate S1_key = \"1000\" @[ 273 , 179 , 30 , 30 ] { commands @[ 320 , 194 , 74 ,\n38 ] { C = \"11\" ; Hit = active ; } transitions { S1_key -> S0_key when / active\n@[ 407 , 136 , 58 , 22 ] ; } } state S2_key = \"0010\" @[ 524 , 353 , 30 , 30 ] {\ncommands @[ 571 , 367 , 74 , 38 ] { C = \"01\" ; Hit = active ; } transitions {\nS2_key -> S3_key when / active @[ 415 , 322 , 58 , 22 ] ; } } state S3_key =\n\"0100\" @[ 269 , 354 , 30 , 30 ] { commands @[ 316 , 368 , 74 , 38 ] { C = \"10\"\n; Hit = active ; } transitions { S3_key -> S1_key when / active @[ 284 , 263 ,\n58 , 22 ] ; } } }")) fsm_entity_1: pin names not known; wires that end beside it: decode_1_rowid, fsm_entity_1_p2, in_1, 1'b1, decode_1_rowid, decode_1_hit, fsm_entity_1_p7, fsm_entity_1_p7
  // Probe on {fsm_entity_1_p7, decode_1_rowid}
  Clock clk (.out(fsm_entity_1_p2));
  // FSM_Entity #(.content("fsm UC_Calc @[ 50 , 50 , 800 , 500 ] { in keypad [ 4 ] @[ 50 , 164 , 79 , 15 ] ;\nin A [ 1 ] @[ 50 , 212 , 15 , 15 ] ; out doDisplay [ 1 ] @[ 781 , 140 , 69 , 15\n] ; out selectOp [ 2 ] @[ 761 , 290 , 89 , 15 ] ; out wea [ 1 ] @[ 820 , 217 ,\n30 , 15 ] ; out web [ 1 ] @[ 819 , 197 , 31 , 15 ] ; out clear [ 1 ] @[ 814 ,\n383 , 36 , 15 ] ; codeWidth = 2 ; reset = S0 ; state S0 = \"01\" @[ 425 , 303 ,\n30 , 30 ] { commands @[ 468 , 318 , 61 , 38 ] { wea = \"0\" ; web = \"0\" ; }\ntransitions { S0 -> S1 when A . keypad /= \"1100\" . keypad /= \"1010\" @[ 471 ,\n242 , 263 , 22 ] ; S0 -> S2 when A . keypad == \"1100\" @[ 455 , 435 , 142 , 22 ]\n; S0 -> S3 when A . keypad == \"1010\" @[ 334 , 281 , 142 , 22 ] ; } } state S1 =\n\"00\" @[ 655 , 318 , 30 , 30 ] { commands @[ 683 , 333 , 99 , 38 ] { doDisplay =\n\"1\" ; wea = \"1\" ; } transitions { S1 -> S0 when default @[ 542 , 392 , 50 , 22\n] ; } } state S2 = \"10\" @[ 340 , 452 , 30 , 30 ] { commands @[ 383 , 467 , 66 ,\n22 ] { clear = \"1\" ; } transitions { S2 -> S0 when default @[ 353 , 388 , 50 ,\n22 ] ; } } state S3 = \"11\" @[ 225 , 289 , 30 , 30 ] { commands @[ 252 , 304 ,\n99 , 38 ] { doDisplay = \"0\" ; web = \"0\" ; } transitions { S3 -> S0 when default\n@[ 308 , 350 , 50 , 22 ] ; } } }")) UC: pin names not known; wires that end beside it: fsm_entity_1_p2, in_1, 1'b1, {fsm_entity_1_p7, decode_1_rowid}, decode_1_hit, UC_p6, UC_p7, UC_p8, UC_p9
  Multiplier #(.width(31)) multiplier_1 (.a(register_1_q), .b(31'ha), .out(multiplier_1_out));  // open: cin, cout
  assign bit_extender_1_out = {{1{multiplier_1_out[30]}}, multiplier_1_out};  // Bit_Extender bit_extender_1
  assign bit_extender_2_out = {{28{1'b0}}, {fsm_entity_1_p7, decode_1_rowid}};  // Bit_Extender bit_extender_2
  Adder #(.width(32)) adder_1 (.a(bit_extender_1_out), .b(bit_extender_2_out), .out(adder_1_out));  // open: cin, cout
  Register #(.width(32)) register_1 (
    .D(adder_1_out), .en(UC_p8), .clk(fsm_entity_1_p2), .Q({register_1_q_2[31], register_1_q}), .clr(in_1));
  Register #(.width(32)) register_2 (
    .D(multiplexer_2_out), .en(UC_p9), .clk(fsm_entity_1_p2), .Q(register_2_q));  // open: clr
  Multiplexer #(.width(32), .enable("false")) multiplexer_1 (
    .in0(register_2_q), .in1({register_1_q_2[31], register_1_q}), .out(multiplexer_1_out), .sel(UC_p6));
  Hex_Digit_Display hex_digit_display_1 (.value(multiplexer_1_out[31:28]));  // open: dp
  Hex_Digit_Display hex_digit_display_2 (.value(multiplexer_1_out[27:24]));  // open: dp
  Hex_Digit_Display hex_digit_display_3 (.value(multiplexer_1_out[23:20]));  // open: dp
  Adder #(.width(32)) adder_2 (
    .a({register_1_q_2[31], register_1_q}), .b(register_2_q), .out(adder_2_out));  // open: cin, cout
  Subtractor #(.width(32)) subtractor_1 (
    .a({register_1_q_2[31], register_1_q}), .b(register_2_q), .out(subtractor_1_out));  // open: bin, bout
  assign and_1_out = {register_1_q_2[31], register_1_q} & register_2_q;  // AND_Gate and_1, 32 bits wide
  assign or_1_out = {register_1_q_2[31], register_1_q} | register_2_q;  // OR_Gate or_1, 32 bits wide
  Hex_Digit_Display hex_digit_display_4 (.value(multiplexer_1_out[19:16]));  // open: dp
  Hex_Digit_Display hex_digit_display_5 (.value(multiplexer_1_out[15:12]));  // open: dp
  Hex_Digit_Display hex_digit_display_6 (.value(multiplexer_1_out[11:8]));  // open: dp
  Hex_Digit_Display hex_digit_display_7 (.value(multiplexer_1_out[7:4]));  // open: dp
  Multiplexer #(.select(2), .width(32), .enable("false")) multiplexer_2 (
    .in0(adder_2_out), .in1(subtractor_1_out), .in2(and_1_out), .in3(or_1_out), .out(multiplexer_2_out),
    .sel(UC_p7));
  Hex_Digit_Display hex_digit_display_8 (.value(multiplexer_1_out[3:0]));  // open: dp
endmodule

module DECODE (
  input  L1,
  input  L2,
  input  L3,
  input  L4,
  output Hit,
  output [1:0] RowId
);

  wire not_1_out, not_2_out, not_3_out, not_4_out;

  not not_1 (not_1_out, L1);
  not not_2 (not_2_out, L2);
  not not_3 (not_3_out, L3);
  not not_4 (not_4_out, L4);
  or or_1 (Hit, L4, L3, L2, L1);
  or or_2 (RowId[1], L4, L3);
  or or_3 (RowId[0], L4, L2);
endmodule

module sdfg (
  input  in_1,
  output out_2
);

  buf buffer_1 (out_2, in_1);
endmodule
