// Logisim project test_fsm.circ as structural Verilog: 1 circuit, main circuit main
module main (
  input  in_1,
  input  in_2,
  input  [2:0] in_3,
  input  in_4,
  input  in_5,
  output [3:0] out_6
);

  wire clock_1_out;

  Clock clock_1 (.out(clock_1_out));
  // FSM_Entity #(.content("fsm example @[ 50 , 50 , 800 , 500 ] { in A [ 3 ] @[ 50 , 100 , 43 , 15 ] ; in B\n[ 1 ] @[ 50 , 183 , 13 , 15 ] ; in C [ 1 ] @[ 50 , 269 , 15 , 15 ] ; out X [ 4\n] @[ 808 , 140 , 42 , 15 ] ; codeWidth = 2 ; reset = S0 ; state S0 = \"01\" @[\n297 , 181 , 30 , 30 ] { commands @[ 264 , 173 , 68 , 22 ] { X = \"0001\" ; }\ntransitions { S0 -> S1 when B . A == \"000\" @[ 394 , 150 , 96 , 22 ] ; S0 -> S3\nwhen A [ 0 ] @[ 346 , 302 , 31 , 22 ] ; } } state S1 = \"10\" @[ 470 , 186 , 30 ,\n30 ] { commands @[ 540 , 190 , 68 , 22 ] { X = \"0010\" ; } transitions { S1 ->\nS2 when / B . C @[ 556 , 256 , 49 , 22 ] ; } } state S2 = \"00\" @[ 477 , 312 ,\n30 , 30 ] { commands @[ 522 , 327 , 30 , 20 ] { } transitions { S2 -> S0 when A\n[ 0 ] @[ 402 , 202 , 31 , 22 ] ; S2 -> S3 when default @[ 432 , 412 , 50 , 22 ]\n; } } state S3 = \"11\" @[ 303 , 398 , 30 , 30 ] { commands @[ 348 , 413 , 30 ,\n20 ] { } transitions { S3 -> S0 when B + / C @[ 213 , 311 , 55 , 22 ] ; } } }")) fsm_entity_1: pin names not known; wires that end beside it: clock_1_out, in_1, in_2, in_3, in_4, in_5, out_6
endmodule
