// Logisim project two_fsms.circ as structural Verilog: 1 circuit, main circuit main
module main (
  input  in_1,
  output out_2,
  output out_3
);

  wire clock_1_out;

  Clock clock_1 (.out(clock_1_out));
  // FSM_Entity #(.content("fsm Ex2 @[ 50 , 50 , 800 , 500 ] { in X [ 1 ] @[ 50 , 100 , 14 , 15 ] ; out Y [\n1 ] @[ 836 , 140 , 14 , 15 ] ; codeWidth = 2 ; reset = FSM1_0 ; state FSM1_0 =\n\"00\" @[ 297 , 181 , 30 , 30 ] { commands @[ 264 , 173 , 44 , 22 ] { Y = \"0\" ; }\ntransitions { FSM1_0 -> FSM1_1 when X @[ 401 , 146 , 14 , 22 ] ; } } state\nFSM1_1 = \"01\" @[ 470 , 186 , 30 , 30 ] { commands @[ 540 , 190 , 44 , 22 ] { Y\n= \"1\" ; } transitions { FSM1_1 -> FSM1_0 when / X @[ 399 , 251 , 29 , 22 ] ; }\n} }")) fsm_entity_1: pin names not known; wires that end beside it: clock_1_out, 1'b0, 1'b1
  // FSM_Entity #(.content("fsm Ex1 @[ 50 , 50 , 800 , 500 ] { in X [ 1 ] @[ 50 , 100 , 14 , 15 ] ; out Y [\n1 ] @[ 836 , 140 , 14 , 15 ] ; codeWidth = 2 ; reset = S0 ; state S0 = \"00\" @[\n262 , 192 , 30 , 30 ] { commands @[ 307 , 207 , 44 , 22 ] { Y = \"0\" ; }\ntransitions { S0 -> S1 when X @[ 456 , 152 , 14 , 22 ] ; } } state S1 = \"10\" @[\n633 , 185 , 30 , 30 ] { commands @[ 678 , 200 , 44 , 22 ] { Y = \"0\" ; }\ntransitions { S1 -> S2 when X @[ 662 , 325 , 14 , 22 ] ; S1 -> S0 when default\n@[ 455 , 287 , 50 , 22 ] ; } } state S2 = \"11\" @[ 463 , 413 , 30 , 30 ] {\ncommands @[ 508 , 428 , 44 , 22 ] { Y = \"1\" ; } transitions { S2 -> S0 when / X\n@[ 338 , 352 , 29 , 22 ] ; } } }")) fsm_entity_2: pin names not known; wires that end beside it: in_1, clock_1_out, 1'b0, 1'b1, in_1, out_2, out_3
endmodule
